// Logisim project 32RV.circ as structural Verilog
module main (
  input  [31:0] in_1,
  input  in_2
);

  wire clock_1_out, idecode_1_ar_i, idecode_1_ar_r, idecode_1_auipc, idecode_1_br, idecode_1_ebc,
       idecode_1_jal, idecode_1_jalr, idecode_1_ld, idecode_1_lui, idecode_1_st, not_1_out;
  wire [2:0] idecode_1_funct3;
  wire [4:0] idecode_1_rd, idecode_1_rs1, idecode_1_rs2;
  wire [6:0] idecode_1_funct7;
  wire [31:0] idecode_1_imm, IF_ID_q, IM_dout, multiplexer_1_out, programcounter_1_outpc,
       programcounter_1_outpcplus4;

  Multiplexer #(.width(32)) multiplexer_1 (
    .in0(in_1), .in1(programcounter_1_outpcplus4), .out(multiplexer_1_out), .sel(not_1_out));
  Clock clock_1 (.out(clock_1_out));
  not not_1 (not_1_out, in_2);
  ProgramCounter programcounter_1 (
    .inPC(multiplexer_1_out), .CLK(clock_1_out), .outPCPlus4(programcounter_1_outpcplus4),
    .outPC(programcounter_1_outpc));
  RAM #(.addrWidth(15), .dataWidth(32)) IM (
    .addr(programcounter_1_outpc[14:0]), .clk(clock_1_out), .dout(IM_dout));  // open: we, oe, din
  Register #(.width(32)) IF_ID (.D(IM_dout), .en(1'b1), .clk(clock_1_out), .Q(IF_ID_q));  // open: clr
  IDecode idecode_1 (
    .instr(IF_ID_q), .rd(idecode_1_rd), .funct3(idecode_1_funct3), .rs1(idecode_1_rs1), .rs2(idecode_1_rs2),
    .funct7(idecode_1_funct7), .imm(idecode_1_imm), .ar_r(idecode_1_ar_r), .ar_i(idecode_1_ar_i),
    .ld(idecode_1_ld), .st(idecode_1_st), .br(idecode_1_br), .jal(idecode_1_jal), .jalr(idecode_1_jalr),
    .lui(idecode_1_lui), .auipc(idecode_1_auipc), .ebc(idecode_1_ebc));

  // Other names for the same wires on the sheet: branch = in_2; jmp_ins_idx[31:0] = in_1
endmodule

module ProgramCounter (
  input  [31:0] inPC,
  input  CLK,
  output [31:0] outPCPlus4,
  output [31:0] outPC
);

  Register #(.width(32)) register_1 (.D(inPC), .en(1'b1), .clk(CLK), .Q(outPC));  // open: clr
  Adder #(.width(32)) adder_1 (.a(outPC), .b(32'h1), .out(outPCPlus4));  // open: cin, cout

  // Other names for the same wires on the sheet: CLK_t = CLK; inPC_t[31:0] = inPC; outPC_t[31:0] = outPC;
  //   outPCPlus4_t[31:0] = outPCPlus4
endmodule

module RegisterFile (
  input  [4:0] rsi1,
  input  [4:0] rsi2,
  input  [4:0] rdi,
  input  [31:0] rd,
  input  we,
  input  CLK,
  output [31:0] rs1,
  output [31:0] rs2
);

  wire x0we_t, x1we_t, x2we_t, x3we_t, x4we_t, x5we_t, x6we_t, x7we_t, x8we_t, x9we_t, x10we_t, x11we_t,
       x12we_t, x13we_t, x14we_t, x15we_t, x16we_t, x17we_t, x18we_t, x19we_t, x20we_t, x21we_t, x22we_t,
       x23we_t, x24we_t, x25we_t, x26we_t, x27we_t, x28we_t, x29we_t, x30we_t, x31we_t;
  wire [31:0] x1q_t, x2q_t, x3q_t, x4q_t, x5q_t, x6q_t, x7q_t, x8q_t, x9q_t, x10q_t, x11q_t, x12q_t, x13q_t,
       x14q_t, x15q_t, x16q_t, x17q_t, x18q_t, x19q_t, x20q_t, x21q_t, x22q_t, x23q_t, x24q_t, x25q_t,
       x26q_t, x27q_t, x28q_t, x29q_t, x30q_t, x31q_t;

  Demultiplexer #(.select(5)) demultiplexer_1 (
    .out0(x0we_t), .out1(x1we_t), .out2(x2we_t), .out3(x3we_t), .out4(x4we_t), .out5(x5we_t), .out6(x6we_t),
    .out7(x7we_t), .out8(x8we_t), .out9(x9we_t), .out10(x10we_t), .out11(x11we_t), .out12(x12we_t),
    .out13(x13we_t), .out14(x14we_t), .out15(x15we_t), .out16(x16we_t), .out17(x17we_t), .out18(x18we_t),
    .out19(x19we_t), .out20(x20we_t), .out21(x21we_t), .out22(x22we_t), .out23(x23we_t), .out24(x24we_t),
    .out25(x25we_t), .out26(x26we_t), .out27(x27we_t), .out28(x28we_t), .out29(x29we_t), .out30(x30we_t),
    .out31(x31we_t), .in(we), .sel(rdi));
  Register #(.width(32)) x4 (.D(rd), .en(x4we_t), .clk(CLK), .Q(x4q_t));  // open: clr
  Register #(.width(32)) x8 (.D(rd), .en(x8we_t), .clk(CLK), .Q(x8q_t));  // open: clr
  Register #(.width(32)) x12 (.D(rd), .en(x12we_t), .clk(CLK), .Q(x12q_t));  // open: clr
  Register #(.width(32)) x16 (.D(rd), .en(x16we_t), .clk(CLK), .Q(x16q_t));  // open: clr
  Register #(.width(32)) x20 (.D(rd), .en(x20we_t), .clk(CLK), .Q(x20q_t));  // open: clr
  Register #(.width(32)) x24 (.D(rd), .en(x24we_t), .clk(CLK), .Q(x24q_t));  // open: clr
  Register #(.width(32)) x28 (.D(rd), .en(x28we_t), .clk(CLK), .Q(x28q_t));  // open: clr
  Register #(.width(32)) x1 (.D(rd), .en(x1we_t), .clk(CLK), .Q(x1q_t));  // open: clr
  Register #(.width(32)) x5 (.D(rd), .en(x5we_t), .clk(CLK), .Q(x5q_t));  // open: clr
  Register #(.width(32)) x9 (.D(rd), .en(x9we_t), .clk(CLK), .Q(x9q_t));  // open: clr
  Register #(.width(32)) x13 (.D(rd), .en(x13we_t), .clk(CLK), .Q(x13q_t));  // open: clr
  Register #(.width(32)) x17 (.D(rd), .en(x17we_t), .clk(CLK), .Q(x17q_t));  // open: clr
  Register #(.width(32)) x21 (.D(rd), .en(x21we_t), .clk(CLK), .Q(x21q_t));  // open: clr
  Register #(.width(32)) x25 (.D(rd), .en(x25we_t), .clk(CLK), .Q(x25q_t));  // open: clr
  Register #(.width(32)) x29 (.D(rd), .en(x29we_t), .clk(CLK), .Q(x29q_t));  // open: clr
  Register #(.width(32)) x2 (.D(rd), .en(x2we_t), .clk(CLK), .Q(x2q_t));  // open: clr
  Register #(.width(32)) x6 (.D(rd), .en(x6we_t), .clk(CLK), .Q(x6q_t));  // open: clr
  Register #(.width(32)) x10 (.D(rd), .en(x10we_t), .clk(CLK), .Q(x10q_t));  // open: clr
  Register #(.width(32)) x14 (.D(rd), .en(x14we_t), .clk(CLK), .Q(x14q_t));  // open: clr
  Register #(.width(32)) x18 (.D(rd), .en(x18we_t), .clk(CLK), .Q(x18q_t));  // open: clr
  Register #(.width(32)) x22 (.D(rd), .en(x22we_t), .clk(CLK), .Q(x22q_t));  // open: clr
  Register #(.width(32)) x26 (.D(rd), .en(x26we_t), .clk(CLK), .Q(x26q_t));  // open: clr
  Register #(.width(32)) x30 (.D(rd), .en(x30we_t), .clk(CLK), .Q(x30q_t));  // open: clr
  Register #(.width(32)) x3 (.D(rd), .en(x3we_t), .clk(CLK), .Q(x3q_t));  // open: clr
  Register #(.width(32)) x7 (.D(rd), .en(x7we_t), .clk(CLK), .Q(x7q_t));  // open: clr
  Register #(.width(32)) x11 (.D(rd), .en(x11we_t), .clk(CLK), .Q(x11q_t));  // open: clr
  Register #(.width(32)) x15 (.D(rd), .en(x15we_t), .clk(CLK), .Q(x15q_t));  // open: clr
  Register #(.width(32)) x19 (.D(rd), .en(x19we_t), .clk(CLK), .Q(x19q_t));  // open: clr
  Register #(.width(32)) x23 (.D(rd), .en(x23we_t), .clk(CLK), .Q(x23q_t));  // open: clr
  Register #(.width(32)) x27 (.D(rd), .en(x27we_t), .clk(CLK), .Q(x27q_t));  // open: clr
  Register #(.width(32)) x31 (.D(rd), .en(x31we_t), .clk(CLK), .Q(x31q_t));  // open: clr
  Multiplexer #(.select(5), .width(32)) multiplexer_1 (
    .in0({32{1'b0}}), .in1(x1q_t), .in2(x2q_t), .in3(x3q_t), .in4(x4q_t), .in5(x5q_t), .in6(x6q_t),
    .in7(x7q_t), .in8(x8q_t), .in9(x9q_t), .in10(x10q_t), .in11(x11q_t), .in12(x12q_t), .in13(x13q_t),
    .in14(x14q_t), .in15(x15q_t), .in16(x16q_t), .in17(x17q_t), .in18(x18q_t), .in19(x19q_t), .in20(x20q_t),
    .in21(x21q_t), .in22(x22q_t), .in23(x23q_t), .in24(x24q_t), .in25(x25q_t), .in26(x26q_t), .in27(x27q_t),
    .in28(x28q_t), .in29(x29q_t), .in30(x30q_t), .in31(x31q_t), .out(rs2), .sel(rsi2));
  Multiplexer #(.select(5), .width(32)) multiplexer_2 (
    .in0({32{1'b0}}), .in1(x1q_t), .in2(x2q_t), .in3(x3q_t), .in4(x4q_t), .in5(x5q_t), .in6(x6q_t),
    .in7(x7q_t), .in8(x8q_t), .in9(x9q_t), .in10(x10q_t), .in11(x11q_t), .in12(x12q_t), .in13(x13q_t),
    .in14(x14q_t), .in15(x15q_t), .in16(x16q_t), .in17(x17q_t), .in18(x18q_t), .in19(x19q_t), .in20(x20q_t),
    .in21(x21q_t), .in22(x22q_t), .in23(x23q_t), .in24(x24q_t), .in25(x25q_t), .in26(x26q_t), .in27(x27q_t),
    .in28(x28q_t), .in29(x29q_t), .in30(x30q_t), .in31(x31q_t), .out(rs1), .sel(rsi1));

  // Other names for the same wires on the sheet: CLK_t = CLK; rd_t[31:0] = rd; rdi_t[4:0] = rdi; rs1_t[31:0] = rs1;
  //   rs2_t[31:0] = rs2; rsi1_t[4:0] = rsi1; rsi2_t[4:0] = rsi2; we_t = we

  // Notes on the sheet:
  //   Register Destination Index
  //   Register Destination Value
  //   Write Enable
  //   Clock
  //   Register Source Index
  //   si x0we enciende, es falta
  //   x0 siempre es 0
  //   Output Register Values
endmodule

module rv32i_regbank (
  input  [3:0] rs1_16,
  input  is_upper,
  input  wen,
  input  [3:0] rd_16,
  input  [31:0] din,
  input  clk,
  input  rst_n,
  input  [3:0] rs2_16,
  output [31:0] rs1_d,
  output [31:0] rs2_d
);

  wire demultiplexer_1_out0, demultiplexer_1_out1, demultiplexer_1_out2, demultiplexer_1_out3,
       demultiplexer_1_out4, demultiplexer_1_out5, demultiplexer_1_out6, demultiplexer_1_out7,
       demultiplexer_2_out0, demultiplexer_2_out1, demultiplexer_2_out2, demultiplexer_2_out3,
       demultiplexer_2_out4, demultiplexer_2_out5, demultiplexer_2_out6, demultiplexer_2_out7, wen0, wen1;
  wire [31:0] multiplexer_1_out, multiplexer_2_out, multiplexer_3_out, multiplexer_4_out, multiplexer_5_out,
       x0_q, x1_q, x2_q, x3_q, x4_q, x5_q, x6_q, x7_q, x8_q, x9_q, x10_q, x11_q, x12_q, x13_q, x14_q, x15_q;

  and and_1 (wen1, wen, rd_16[3]);
  // Probe on din
  and and_2 (wen0, ~rd_16[3], wen);  // AND_Gate
  Demultiplexer #(.select(3)) demultiplexer_1 (
    .out0(demultiplexer_1_out0), .out1(demultiplexer_1_out1), .out2(demultiplexer_1_out2),
    .out3(demultiplexer_1_out3), .out4(demultiplexer_1_out4), .out5(demultiplexer_1_out5),
    .out6(demultiplexer_1_out6), .out7(demultiplexer_1_out7), .in(wen0), .sel(rd_16[2:0]));
  Register #(.width(32)) x0 (.D(din), .en(demultiplexer_1_out0), .Q(x0_q), .clk(clk), .clr(rst_n));
  Register #(.width(32)) x1 (.D(din), .en(demultiplexer_1_out1), .Q(x1_q), .clk(clk), .clr(rst_n));
  Register #(.width(32)) x2 (.D(din), .en(demultiplexer_1_out2), .Q(x2_q), .clk(clk), .clr(rst_n));
  Register #(.width(32)) x3 (.D(din), .en(demultiplexer_1_out3), .Q(x3_q), .clk(clk), .clr(rst_n));
  Register #(.width(32)) x4 (.D(din), .en(demultiplexer_1_out4), .Q(x4_q), .clk(clk), .clr(rst_n));
  Register #(.width(32)) x5 (.D(din), .en(demultiplexer_1_out5), .Q(x5_q), .clk(clk), .clr(rst_n));
  Register #(.width(32)) x6 (.D(din), .en(demultiplexer_1_out6), .Q(x6_q), .clk(clk), .clr(rst_n));
  Register #(.width(32)) x7 (.D(din), .en(demultiplexer_1_out7), .Q(x7_q), .clk(clk), .clr(rst_n));
  Multiplexer #(.width(32)) multiplexer_1 (.in0({32{1'b0}}), .in1(x0_q), .out(multiplexer_1_out), .sel(is_upper));
  Multiplexer #(.select(3), .width(32)) multiplexer_2 (
    .in0(multiplexer_1_out), .in1(x1_q), .in2(x2_q), .in3(x3_q), .in4(x4_q), .in5(x5_q), .in6(x6_q),
    .in7(x7_q), .out(multiplexer_2_out), .sel(rs1_16[2:0]));
  Multiplexer #(.select(3), .width(32)) multiplexer_3 (
    .in0(multiplexer_1_out), .in1(x1_q), .in2(x2_q), .in3(x3_q), .in4(x4_q), .in5(x5_q), .in6(x6_q),
    .in7(x7_q), .out(multiplexer_3_out), .sel(rs2_16[2:0]));
  Demultiplexer #(.select(3)) demultiplexer_2 (
    .out0(demultiplexer_2_out0), .out1(demultiplexer_2_out1), .out2(demultiplexer_2_out2),
    .out3(demultiplexer_2_out3), .out4(demultiplexer_2_out4), .out5(demultiplexer_2_out5),
    .out6(demultiplexer_2_out6), .out7(demultiplexer_2_out7), .in(wen1), .sel(rd_16[2:0]));
  Register #(.width(32)) x8 (.D(din), .en(demultiplexer_2_out0), .Q(x8_q), .clk(clk), .clr(rst_n));
  Register #(.width(32)) x9 (.D(din), .en(demultiplexer_2_out1), .Q(x9_q), .clk(clk), .clr(rst_n));
  Register #(.width(32)) x10 (.D(din), .en(demultiplexer_2_out2), .Q(x10_q), .clk(clk), .clr(rst_n));
  Register #(.width(32)) x11 (.D(din), .en(demultiplexer_2_out3), .Q(x11_q), .clk(clk), .clr(rst_n));
  Register #(.width(32)) x12 (.D(din), .en(demultiplexer_2_out4), .Q(x12_q), .clk(clk), .clr(rst_n));
  Register #(.width(32)) x13 (.D(din), .en(demultiplexer_2_out5), .Q(x13_q), .clk(clk), .clr(rst_n));
  Register #(.width(32)) x14 (.D(din), .en(demultiplexer_2_out6), .Q(x14_q), .clk(clk), .clr(rst_n));
  Register #(.width(32)) x15 (.D(din), .en(demultiplexer_2_out7), .Q(x15_q), .clk(clk), .clr(rst_n));
  Multiplexer #(.select(3), .width(32)) multiplexer_4 (
    .in0(x8_q), .in1(x9_q), .in2(x10_q), .in3(x11_q), .in4(x12_q), .in5(x13_q), .in6(x14_q), .in7(x15_q),
    .out(multiplexer_4_out), .sel(rs1_16[2:0]));
  Multiplexer #(.select(3), .width(32)) multiplexer_5 (
    .in0(x8_q), .in1(x9_q), .in2(x10_q), .in3(x11_q), .in4(x12_q), .in5(x13_q), .in6(x14_q), .in7(x15_q),
    .out(multiplexer_5_out), .sel(rs2_16[2:0]));
  Multiplexer #(.width(32)) multiplexer_6 (
    .in0(multiplexer_2_out), .in1(multiplexer_4_out), .out(rs1_d), .sel(rs1_16[3]));
  Multiplexer #(.width(32)) multiplexer_7 (
    .in0(multiplexer_3_out), .in1(multiplexer_5_out), .out(rs2_d), .sel(rs2_16[3]));

  // Other names for the same wires on the sheet: rd_8[2:0] = rd_16[2:0]
endmodule

module rv32i_regfile (
  input  [4:0] rs1,
  input  [31:0] din,
  input  [4:0] rd,
  input  wen,
  input  [4:0] rs2,
  input  clk,
  input  rst_n,
  output [31:0] rsa,
  output [31:0] rsb
);

  wire wen0, wen1;
  wire [31:0] i_reg0_rs1_d, i_reg0_rs2_d, i_reg1_rs1_d, i_reg1_rs2_d;

  and and_1 (wen1, wen, rd[4]);
  and and_2 (wen0, wen, ~rd[4]);  // AND_Gate
  rv32i_regbank i_reg0 (
    .clk(clk), .rst_n(rst_n), .rs2_16(rs2[3:0]), .wen(wen0), .rd_16(rd[3:0]), .is_upper(1'b0),
    .rs1_16(rs1[3:0]), .din(din), .rs1_d(i_reg0_rs1_d), .rs2_d(i_reg0_rs2_d));
  rv32i_regbank i_reg1 (
    .clk(clk), .rst_n(rst_n), .rs2_16(rs2[3:0]), .wen(wen1), .rd_16(rd[3:0]), .is_upper(1'b1),
    .rs1_16(rs1[3:0]), .din(din), .rs1_d(i_reg1_rs1_d), .rs2_d(i_reg1_rs2_d));
  Multiplexer #(.width(32)) multiplexer_1 (.in0(i_reg0_rs1_d), .in1(i_reg1_rs1_d), .out(rsa), .sel(rs1[4]));
  Multiplexer #(.width(32)) multiplexer_2 (.in0(i_reg0_rs2_d), .in1(i_reg1_rs2_d), .out(rsb), .sel(rs2[4]));
endmodule

module rv32i_alu (
  input  [31:0] rsa,
  input  [31:0] rsb_imm,
  input  op_add,
  input  op_ge,
  input  op_eq,
  input  op_ne,
  input  op_lt,
  input  op_geu,
  input  op_ltu,
  input  op_sub,
  input  op_and,
  input  op_or,
  input  op_xor,
  input  op_sll,
  input  op_srl,
  input  op_sra,
  input  op_rs2_imm,
  output [31:0] dout
);

  wire comparator_1_eq, comparator_1_gt, comparator_1_lt, comparator_2_eq, comparator_2_gt, comparator_2_lt,
       multiplexer_1_out, multiplexer_2_out, multiplexer_3_out, multiplexer_4_out, multiplexer_5_out,
       not_1_out, or_2_out, or_3_out, or_4_out;
  wire [31:0] adder_1_out, and_1_out, bit_extender_1_out, multiplexer_6_out, multiplexer_7_out,
       multiplexer_8_out, multiplexer_9_out, multiplexer_10_out, multiplexer_11_out, multiplexer_12_out,
       multiplexer_13_out, or_1_out, shifter_1_out, shifter_2_out, shifter_3_out, subtractor_1_out, xor_1_out;

  // Probe on op_add
  Adder #(.width(32)) adder_1 (.a(rsa), .b(rsb_imm), .out(adder_1_out));  // open: cin, cout
  Subtractor #(.width(32)) subtractor_1 (.a(rsa), .b(rsb_imm), .out(subtractor_1_out));  // open: bin, bout
  assign and_1_out = rsa & rsb_imm;  // AND_Gate and_1, 32 bits wide
  assign or_1_out = rsa | rsb_imm;  // OR_Gate or_1, 32 bits wide
  assign xor_1_out = rsa ^ rsb_imm;  // XOR_Gate xor_1, 32 bits wide
  Shifter #(.width(32)) shifter_1 (.in(rsa), .\dist (rsb_imm[4:0]), .out(shifter_1_out));
  Shifter #(.shift("lr"), .width(32)) shifter_2 (.in(rsa), .\dist (rsb_imm[4:0]), .out(shifter_2_out));
  Shifter #(.shift("ar"), .width(32)) shifter_3 (.in(rsa), .\dist (rsb_imm[4:0]), .out(shifter_3_out));
  Comparator #(.width(32)) comparator_1 (
    .a(rsa), .b(rsb_imm), .gt(comparator_1_gt), .eq(comparator_1_eq), .lt(comparator_1_lt));
  Comparator #(.mode("unsigned"), .width(32)) comparator_2 (
    .a(rsa), .b(rsb_imm), .gt(comparator_2_gt), .eq(comparator_2_eq), .lt(comparator_2_lt));
  or or_2 (or_2_out, comparator_1_gt, comparator_1_eq);
  Multiplexer multiplexer_1 (.in0(or_2_out), .in1(comparator_1_eq), .out(multiplexer_1_out), .sel(op_eq));
  or or_3 (or_3_out, comparator_2_gt, comparator_2_eq);
  Multiplexer multiplexer_2 (.in0(multiplexer_1_out), .in1(not_1_out), .out(multiplexer_2_out), .sel(op_ne));
  not not_1 (not_1_out, comparator_1_eq);
  Multiplexer multiplexer_3 (.in0(multiplexer_2_out), .in1(comparator_1_lt), .out(multiplexer_3_out), .sel(op_lt));
  Multiplexer multiplexer_4 (.in0(multiplexer_3_out), .in1(or_3_out), .out(multiplexer_4_out), .sel(op_geu));
  assign bit_extender_1_out = {{31{1'b0}}, multiplexer_5_out};  // Bit_Extender bit_extender_1
  Multiplexer multiplexer_5 (.in0(multiplexer_4_out), .in1(comparator_2_lt), .out(multiplexer_5_out), .sel(op_ltu));
  or or_4 (or_4_out, op_ge, op_eq, op_ne, op_lt, op_geu, op_ltu);
  Multiplexer #(.width(32)) multiplexer_6 (
    .in0(adder_1_out), .in1(subtractor_1_out), .out(multiplexer_6_out), .sel(op_sub));
  Multiplexer #(.width(32)) multiplexer_7 (
    .in0(multiplexer_6_out), .in1(and_1_out), .out(multiplexer_7_out), .sel(op_and));
  Multiplexer #(.width(32)) multiplexer_8 (
    .in0(multiplexer_7_out), .in1(or_1_out), .out(multiplexer_8_out), .sel(op_or));
  Multiplexer #(.width(32)) multiplexer_9 (
    .in0(multiplexer_8_out), .in1(xor_1_out), .out(multiplexer_9_out), .sel(op_xor));
  Multiplexer #(.width(32)) multiplexer_10 (
    .in0(multiplexer_9_out), .in1(shifter_1_out), .out(multiplexer_10_out), .sel(op_sll));
  Multiplexer #(.width(32)) multiplexer_11 (
    .in0(multiplexer_10_out), .in1(shifter_2_out), .out(multiplexer_11_out), .sel(op_srl));
  Multiplexer #(.width(32)) multiplexer_12 (
    .in0(multiplexer_11_out), .in1(shifter_3_out), .out(multiplexer_12_out), .sel(op_sra));
  Multiplexer #(.width(32)) multiplexer_13 (
    .in0(multiplexer_12_out), .in1(bit_extender_1_out), .out(multiplexer_13_out), .sel(or_4_out));
  Multiplexer #(.width(32)) multiplexer_14 (.in0(multiplexer_13_out), .in1(rsb_imm), .out(dout), .sel(op_rs2_imm));

  // Notes on the sheet:
  //   unsigned
endmodule

module rv32i_indec (
  input  [31:0] instr,
  output [4:0] rd,
  output [2:0] funct3,
  output [4:0] rs1,
  output [4:0] rs2,
  output [6:0] funct7,
  output [31:0] imm,
  output ar_r,
  output ar_i,
  output ld,
  output st,
  output br,
  output jal,
  output jalr,
  output lui,
  output auipc,
  output ebc
);

  wire or_1_out;
  wire [31:0] multiplexer_1_out, multiplexer_2_out, multiplexer_3_out, rv32i_imm_1_b_imm, rv32i_imm_1_i_imm,
       rv32i_imm_1_j_imm, rv32i_imm_1_s_imm, rv32i_imm_1_u_imm;

  rv32i_imm rv32i_imm_1 (
    .instr(instr), .I_imm(rv32i_imm_1_i_imm), .S_imm(rv32i_imm_1_s_imm), .B_imm(rv32i_imm_1_b_imm),
    .U_imm(rv32i_imm_1_u_imm), .J_imm(rv32i_imm_1_j_imm));
  Comparator #(.width(7)) comparator_1 (.a(instr[6:0]), .b(7'b0110011), .eq(ar_r));  // open: gt, lt
  Comparator #(.width(7)) comparator_2 (.a(instr[6:0]), .b(7'b0010011), .eq(ar_i));  // open: gt, lt
  Comparator #(.width(7)) comparator_3 (.a(instr[6:0]), .b(7'b0000011), .eq(ld));  // open: gt, lt
  Comparator #(.width(7)) comparator_4 (.a(instr[6:0]), .b(7'b0100011), .eq(st));  // open: gt, lt
  Comparator #(.width(7)) comparator_5 (.a(instr[6:0]), .b(7'b1100011), .eq(br));  // open: gt, lt
  Comparator #(.width(7)) comparator_6 (.a(instr[6:0]), .b(7'b1101111), .eq(jal));  // open: gt, lt
  Comparator #(.width(7)) comparator_7 (.a(instr[6:0]), .b(7'b1100111), .eq(jalr));  // open: gt, lt
  Comparator #(.width(7)) comparator_8 (.a(instr[6:0]), .b(7'b0110111), .eq(lui));  // open: gt, lt
  Comparator #(.width(7)) comparator_9 (.a(instr[6:0]), .b(7'b0010111), .eq(auipc));  // open: gt, lt
  Comparator #(.width(7)) comparator_10 (.a(instr[6:0]), .b(7'b1110011), .eq(ebc));  // open: gt, lt
  Multiplexer #(.width(32)) multiplexer_1 (
    .in0(rv32i_imm_1_i_imm), .in1(rv32i_imm_1_s_imm), .out(multiplexer_1_out), .sel(st));
  Multiplexer #(.width(32)) multiplexer_2 (
    .in0(multiplexer_1_out), .in1(rv32i_imm_1_b_imm), .out(multiplexer_2_out), .sel(br));
  Multiplexer #(.width(32)) multiplexer_3 (
    .in0(multiplexer_2_out), .in1(rv32i_imm_1_u_imm), .out(multiplexer_3_out), .sel(or_1_out));
  or or_1 (or_1_out, auipc, lui);
  Multiplexer #(.width(32)) multiplexer_4 (.in0(multiplexer_3_out), .in1(rv32i_imm_1_j_imm), .out(imm), .sel(jal));

  assign funct3 = instr[14:12];
  assign funct7 = instr[31:25];
  assign rd = instr[11:7];
  assign rs1 = instr[19:15];
  assign rs2 = instr[24:20];
endmodule

module rv32i_imm (
  input  [31:0] instr,
  output [31:0] I_imm,
  output [31:0] S_imm,
  output [31:0] B_imm,
  output [31:0] U_imm,
  output [31:0] J_imm
);

  // NoConnect on instr[6:0]
  assign {I_imm[31], B_imm[31:12]} = {{20{instr[31]}}, instr[31]};  // Bit_Extender bit_extender_1
  // NoConnect on I_imm[31]
  // NoConnect on {I_imm[31], B_imm[31:13]}
  // NoConnect on {I_imm[31], B_imm[31:24]}

  assign B_imm[11:0] = {instr[7], instr[30:25], instr[11:8], 1'b0};
  assign I_imm[30:0] = {B_imm[31:12], instr[30:20]};
  assign J_imm = {B_imm[23:12], instr[19:12], instr[20], instr[30:21], 1'b0};
  assign S_imm = {I_imm[31], B_imm[31:12], instr[30:25], instr[11:7]};
  assign U_imm = {B_imm[12], instr[30:12], {12{1'b0}}};

  // Notes on the sheet:
  //   I-imm
  //   S-imm
  //   B-imm
  //   U-imm
  //   J-imm
endmodule

module rv32i_aludec (
  input  [2:0] funct3,
  input  [6:0] funct7,
  input  ar_i,
  input  ar,
  input  br,
  input  lui_auipc,
  output op_add,
  output op_sub,
  output op_sll,
  output op_slt,
  output op_sltu,
  output op_xor,
  output op_srl,
  output op_sra,
  output op_or,
  output op_and,
  output op_beq,
  output op_bne,
  output op_blt,
  output op_bge,
  output op_bltu,
  output op_bgeu,
  output op_rs2_imm
);

  wire and_1_out, and_2_out, and_3_out, and_4_out, and_5_out, and_6_out, and_7_out, and_8_out, and_9_out,
       and_10_out, and_11_out, and_12_out, or_1_out, or_2_out;

  and and_1 (and_1_out, funct3[2], funct3[1], funct3[0]);
  or or_1 (or_1_out, ar_i, ar);
  and and_2 (and_2_out, funct3[2], funct3[1], ~funct3[0]);  // AND_Gate
  and and_3 (and_3_out, funct3[2], ~funct3[1], funct3[0]);  // AND_Gate
  and and_4 (and_4_out, funct7[5], and_3_out);
  and and_5 (and_5_out, and_3_out, ~funct7[5]);  // AND_Gate
  and and_6 (and_6_out, funct3[2], ~funct3[1], ~funct3[0]);  // AND_Gate
  and and_7 (and_7_out, ~funct3[2], funct3[1], funct3[0]);  // AND_Gate
  and and_8 (and_8_out, ~funct3[2], funct3[1], ~funct3[0]);  // AND_Gate
  and and_9 (and_9_out, ~funct3[2], ~funct3[1], funct3[0]);  // AND_Gate
  and and_10 (and_10_out, funct7[5], and_11_out);
  and and_11 (and_11_out, ~funct3[2], ~funct3[1], ~funct3[0]);  // AND_Gate
  and and_12 (and_12_out, ~ar_i, and_10_out);  // AND_Gate
  and and_13 (op_sub, or_1_out, and_12_out);
  and and_14 (op_sll, and_9_out, or_1_out);
  and and_15 (op_slt, and_8_out, or_1_out);
  and and_16 (op_sltu, and_7_out, or_1_out);
  and and_17 (op_xor, and_6_out, or_1_out);
  and and_18 (op_srl, and_5_out, or_1_out);
  and and_19 (op_sra, and_4_out, or_1_out);
  and and_20 (op_or, and_2_out, or_1_out);
  and and_21 (op_and, and_1_out, or_1_out);
  and and_22 (op_beq, and_11_out, br);
  and and_23 (op_bne, and_9_out, br);
  and and_24 (op_blt, and_6_out, br);
  and and_25 (op_bge, and_3_out, br);
  and and_26 (op_bltu, and_2_out, br);
  and and_27 (op_bgeu, and_1_out, br);
  or or_2 (or_2_out, ~funct7[5], ar_i);  // OR_Gate
  and and_28 (op_add, and_11_out, or_2_out);

  assign op_rs2_imm = lui_auipc;
endmodule

module rv32i (
  input  [31:0] instr,
  input  [31:0] mem_din_i,
  input  clk,
  input  rst_n,
  output [31:0] instr_addr,
  output [31:0] mem_addr_o,
  output [31:0] mem_dout_o,
  output mem_wen_o,
  output mem_be0_o,
  output mem_be1_o,
  output mem_be2_o,
  output mem_be3_o
);

  wire and_1_out, i_decoder_p7, i_decoder_p8, i_decoder_p9, i_decoder_p10, i_decoder_p11, i_decoder_p12,
       i_decoder_p13, i_decoder_p14, i_decoder_p15, i_decoder_p16, i_decoder_p17, i_decoder_p18,
       i_decoder_p19, i_decoder_p20, i_decoder_p21, i_decoder_p22, i_decoder_p23, i_indec_p2, i_indec_p7,
       i_indec_p8, i_indec_p14, i_indec_p15, i_indec_p17, not_1_out, not_2_out, not_3_out, or_1_out,
       or_2_out, or_3_out, or_4_out, or_5_out, or_6_out, or_7_out, or_8_out;
  wire [0:0] multiplexer_7_out;
  wire [2:0] ld;
  wire [4:0] i_indec_p3, i_indec_p4, i_indec_p5;
  wire [31:0] adder_1_out, i_alu_dout, i_indec_p6, i_regfile_rsa, i_regfile_rsb, multiplexer_1_out,
       multiplexer_2_out, multiplexer_3_out, multiplexer_4_out, multiplexer_5_out, multiplexer_6_out,
       rv32i_lsu_1_rdat_o;
  wire [31:1] multiplexer_7_out_2;

  // Probe on instr
  // rv32i_indec i_indec: pin names not known; wires that end beside it: instr, i_indec_p2, i_indec_p3, i_indec_p4, i_indec_p5, i_indec_p6, i_indec_p7, i_indec_p8, ld, ld, ld, ld, ld, i_indec_p14, i_indec_p15, ld, i_indec_p17
  // NoConnect on i_indec_p2
  Multiplexer #(.width(32)) multiplexer_1 (.in0(32'h4), .in1(i_indec_p6), .out(multiplexer_1_out), .sel(and_1_out));
  and and_1 (and_1_out, ld[0], multiplexer_7_out[0]);
  // Probe on i_indec_p3
  // Probe on i_indec_p4
  // Probe on i_indec_p6
  or or_1 (or_1_out, i_indec_p7, i_indec_p8);
  // Probe on i_indec_p5
  or or_2 (or_2_out, i_indec_p14, i_indec_p15);
  Adder #(.width(32)) adder_1 (.a(instr_addr), .b(multiplexer_1_out), .out(adder_1_out));  // open: cin, cout
  // Probe on multiplexer_2_out
  not not_1 (not_1_out, or_1_out);
  Multiplexer #(.width(32)) multiplexer_2 (
    .in0(adder_1_out), .in1({multiplexer_7_out_2, multiplexer_7_out[0]}), .out(multiplexer_2_out),
    .sel(not_1_out));
  rv32i_regfile i_regfile (
    .rs1(i_indec_p3), .din(multiplexer_2_out), .rd(i_indec_p5), .wen(or_3_out), .rs2(i_indec_p4), .clk(clk),
    .rst_n(rst_n), .rsa(i_regfile_rsa), .rsb(i_regfile_rsb));
  or or_3 (or_3_out, ld[0], or_1_out, or_2_out, ld[0], ld[0]);
  // Probe on i_regfile_rsb
  or or_4 (or_4_out, ld[0], or_2_out, i_indec_p17, ld[0], or_1_out);
  Multiplexer #(.width(32)) multiplexer_3 (
    .in0(i_indec_p6), .in1(i_regfile_rsb), .out(multiplexer_3_out), .sel(i_indec_p17));
  // Probe on i_regfile_rsa
  Multiplexer #(.width(32)) multiplexer_4 (
    .in0(instr_addr), .in1(i_regfile_rsa), .out(multiplexer_4_out), .sel(not_2_out));
  Multiplexer #(.width(32)) multiplexer_5 (
    .in0(i_regfile_rsb), .in1(i_indec_p6), .out(multiplexer_5_out), .sel(or_4_out));
  not not_2 (not_2_out, or_5_out);
  or or_5 (or_5_out, i_indec_p7, or_2_out);
  // Probe on multiplexer_6_out
  Multiplexer #(.width(32)) multiplexer_6 (
    .in0(adder_1_out), .in1({multiplexer_7_out_2, 1'b0}), .out(multiplexer_6_out), .sel(or_1_out));
  or or_6 (or_6_out, or_1_out, i_decoder_p7);
  or or_7 (or_7_out, i_decoder_p10, i_decoder_p11);
  // rv32i_aludec i_decoder: pin names not known; wires that end beside it: ld, ld, ld, ld, ld, or_2_out, i_decoder_p7, i_decoder_p8, i_decoder_p9, i_decoder_p10, i_decoder_p11, i_decoder_p12, i_decoder_p13, i_decoder_p14, i_decoder_p15, i_decoder_p16, i_decoder_p17, i_decoder_p18, i_decoder_p19, i_decoder_p20, i_decoder_p21, i_decoder_p22, i_decoder_p23
  Register #(.width(32)) pc (.D(multiplexer_6_out), .Q(instr_addr), .clk(clk), .clr(rst_n));  // open: en
  or or_8 (or_8_out, i_decoder_p12, i_decoder_p13);
  Multiplexer #(.width(32)) multiplexer_7 (
    .in0(rv32i_lsu_1_rdat_o), .in1(i_alu_dout), .out({multiplexer_7_out_2, multiplexer_7_out[0]}),
    .sel(not_3_out));
  rv32i_alu i_alu (
    .op_or(i_decoder_p17), .op_xor(i_decoder_p14), .op_sll(i_decoder_p9), .op_srl(i_decoder_p15),
    .op_sra(i_decoder_p16), .op_rs2_imm(i_decoder_p23), .rsb_imm(multiplexer_5_out), .rsa(multiplexer_4_out),
    .op_add(or_6_out), .op_ge(i_decoder_p21), .op_eq(i_decoder_p19), .op_ne(i_decoder_p20), .op_lt(or_7_out),
    .op_geu(i_decoder_p22), .op_ltu(or_8_out), .op_sub(i_decoder_p8), .op_and(i_decoder_p18),
    .dout(i_alu_dout));
  not not_3 (not_3_out, ld[0]);
  // Probe on i_alu_dout
  rv32i_lsu rv32i_lsu_1 (
    .func3_i(ld), .wdat_i(multiplexer_3_out), .mem_addr_i(i_alu_dout), .rmem_i(mem_din_i),
    .st_i(i_indec_p17), .wenmem_o(mem_wen_o), .wmem_o(mem_dout_o), .mem_addr_o(mem_addr_o),
    .rdat_o(rv32i_lsu_1_rdat_o), .be0_o(mem_be0_o), .be1_o(mem_be1_o), .be2_o(mem_be2_o), .be3_o(mem_be3_o));
  // Pins of 1 and 3 bits meet at ld

  // Other names for the same wires on the sheet: pc[31:0] = instr_addr

  // Notes on the sheet:
  //   take branch
endmodule

module rv32i_lsu (
  input  [31:0] wdat_i,
  input  [31:0] mem_addr_i,
  input  st_i,
  input  [31:0] rmem_i,
  input  [2:0] func3_i,
  output [31:0] wmem_o,
  output [31:0] mem_addr_o,
  output wenmem_o,
  output [31:0] rdat_o,
  output be0_o,
  output be1_o,
  output be2_o,
  output be3_o
);

  wire is_b, is_h, is_w;
  wire [3:0] multiplexer_10_out, shifter_11_out, shifter_12_out;
  wire [7:0] multiplexer_2_out;
  wire [15:0] multiplexer_6_out;
  wire [31:0] bit_extender_1_out, bit_extender_2_out, bit_extender_3_out, bit_extender_4_out,
       multiplexer_1_out, multiplexer_3_out, multiplexer_4_out, multiplexer_5_out, multiplexer_8_out,
       multiplexer_9_out, shifter_1_out, shifter_2_out, shifter_3_out, shifter_4_out, shifter_5_out,
       shifter_6_out, shifter_7_out, shifter_8_out, shifter_9_out, shifter_10_out;

  Shifter #(.width(32)) shifter_1 (.in(wdat_i), .\dist (5'b01000), .out(shifter_1_out));
  Shifter #(.width(32)) shifter_2 (.in(wdat_i), .\dist (5'b10000), .out(shifter_2_out));
  Shifter #(.width(32)) shifter_3 (.in(wdat_i), .\dist (5'b11000), .out(shifter_3_out));
  Shifter #(.shift("lr"), .width(32)) shifter_4 (.in(rmem_i), .\dist (5'b01000), .out(shifter_4_out));
  Shifter #(.shift("lr"), .width(32)) shifter_5 (.in(rmem_i), .\dist (5'b10000), .out(shifter_5_out));
  Shifter #(.shift("lr"), .width(32)) shifter_6 (.in(rmem_i), .\dist (5'b11000), .out(shifter_6_out));
  and and_1 (is_b, ~func3_i[0], ~func3_i[1]);  // AND_Gate
  and and_2 (is_h, func3_i[0], ~func3_i[1]);  // AND_Gate
  and and_3 (is_w, ~func3_i[0], func3_i[1]);  // AND_Gate
  Multiplexer #(.select(2), .width(32)) multiplexer_1 (
    .in0(wdat_i), .in1(shifter_1_out), .in2(shifter_2_out), .in3(shifter_3_out), .out(multiplexer_1_out),
    .sel(mem_addr_i[1:0]));
  Multiplexer #(.select(2), .width(8)) multiplexer_2 (
    .in0(rmem_i[7:0]), .in1(shifter_4_out[7:0]), .in2(shifter_5_out[7:0]), .in3(shifter_6_out[7:0]),
    .out(multiplexer_2_out), .sel(mem_addr_i[1:0]));
  Shifter #(.width(32)) shifter_7 (.in(wdat_i), .\dist (5'b01000), .out(shifter_7_out));
  Shifter #(.width(32)) shifter_8 (.in(wdat_i), .\dist (5'b10000), .out(shifter_8_out));
  Shifter #(.shift("lr"), .width(32)) shifter_9 (.in(rmem_i), .\dist (5'b01000), .out(shifter_9_out));
  Shifter #(.shift("lr"), .width(32)) shifter_10 (.in(rmem_i), .\dist (5'b10000), .out(shifter_10_out));
  assign bit_extender_1_out = {{24{multiplexer_2_out[7]}}, multiplexer_2_out};  // Bit_Extender bit_extender_1
  Multiplexer #(.width(32)) multiplexer_3 (
    .in0(bit_extender_1_out), .in1(bit_extender_2_out), .out(multiplexer_3_out), .sel(func3_i[2]));
  assign bit_extender_2_out = {{24{1'b0}}, multiplexer_2_out};  // Bit_Extender bit_extender_2
  Multiplexer #(.width(32)) multiplexer_4 (.in0(wdat_i), .in1(multiplexer_5_out), .out(multiplexer_4_out), .sel(is_h));
  Multiplexer #(.select(2), .width(32)) multiplexer_5 (
    .in0(wdat_i), .in1(shifter_7_out), .in2(shifter_8_out), .in3({32{1'b1}}), .out(multiplexer_5_out),
    .sel(mem_addr_i[1:0]));
  Multiplexer #(.select(2), .width(16)) multiplexer_6 (
    .in0(rmem_i[15:0]), .in1(shifter_9_out[15:0]), .in2(shifter_10_out[15:0]), .in3({16{1'b1}}),
    .out(multiplexer_6_out), .sel(mem_addr_i[1:0]));
  Multiplexer #(.width(32)) multiplexer_7 (.in0(multiplexer_4_out), .in1(multiplexer_1_out), .out(wmem_o), .sel(is_b));
  assign bit_extender_3_out = {{16{multiplexer_6_out[15]}}, multiplexer_6_out};  // Bit_Extender bit_extender_3
  Multiplexer #(.width(32)) multiplexer_8 (
    .in0(bit_extender_3_out), .in1(bit_extender_4_out), .out(multiplexer_8_out), .sel(func3_i[2]));
  assign bit_extender_4_out = {{16{1'b0}}, multiplexer_6_out};  // Bit_Extender bit_extender_4
  Shifter #(.width(4)) shifter_11 (.in(4'b0011), .\dist (mem_addr_i[1:0]), .out(shifter_11_out));
  Shifter #(.width(4)) shifter_12 (.in(4'b0001), .\dist (mem_addr_i[1:0]), .out(shifter_12_out));
  Multiplexer #(.width(32)) multiplexer_9 (.in0(rmem_i), .in1(multiplexer_8_out), .out(multiplexer_9_out), .sel(is_h));
  Multiplexer #(.width(4)) multiplexer_10 (.in0(4'b1111), .in1(shifter_11_out), .out(multiplexer_10_out), .sel(is_h));
  Multiplexer #(.width(32)) multiplexer_11 (.in0(multiplexer_9_out), .in1(multiplexer_3_out), .out(rdat_o), .sel(is_b));
  Multiplexer #(.width(4)) multiplexer_12 (
    .in0(multiplexer_10_out), .in1(shifter_12_out), .out({be3_o, be2_o, be1_o, be0_o}), .sel(is_b));

  assign mem_addr_o = mem_addr_i;
  assign wenmem_o = st_i;

  // Other names for the same wires on the sheet: is_unsigned = func3_i[2]; low_addr[1:0] = mem_addr_i[1:0]

  // Notes on the sheet:
  //   byte
  //   byte
  //   halfword
  //   WRITE
  //   READ
  //   halfword
endmodule

module sc_bus (
  input  be0_i,
  input  [31:0] wdata_i,
  input  be1_i,
  input  be2_i,
  input  be3_i,
  input  [31:0] addr_i,
  input  [31:0] lb_data_i,
  input  [31:0] mem_data_i,
  input  we_i,
  output lb_be0_0,
  output [31:0] lb_data_o,
  output mem_be0_o,
  output lb_be1_0,
  output mem_be1_o,
  output [31:0] mem_data_o,
  output lb_be2_0,
  output mem_be2_o,
  output [31:0] tty_data_o,
  output lb_be3_0,
  output mem_be3_o,
  output [31:0] mem_addr_o,
  output [31:0] rdata_o,
  output mem_we_o,
  output tty_we_o,
  output lb_we_o
);

  wire comparator_1_lt, comparator_2_eq, comparator_2_gt, comparator_3_lt, comparator_4_eq, comparator_4_gt,
       comparator_5_lt, comparator_6_eq, comparator_6_gt, is_lb_addr, is_mem_addr, is_tty_addr, or_1_out,
       or_2_out, or_3_out;
  wire [31:0] multiplexer_2_out;

  or or_1 (or_1_out, comparator_2_gt, comparator_2_eq);
  Comparator #(.mode("unsigned"), .width(32)) comparator_1 (
    .a(addr_i), .b(32'hff000000), .lt(comparator_1_lt));  // open: gt, eq
  Comparator #(.mode("unsigned"), .width(32)) comparator_2 (
    .a(addr_i), .b({32{1'b0}}), .gt(comparator_2_gt), .eq(comparator_2_eq));  // open: lt
  or or_2 (or_2_out, comparator_4_gt, comparator_4_eq);
  Comparator #(.mode("unsigned"), .width(32)) comparator_3 (
    .a(addr_i), .b(32'hff000004), .lt(comparator_3_lt));  // open: gt, eq
  Comparator #(.mode("unsigned"), .width(32)) comparator_4 (
    .a(addr_i), .b(32'hff000000), .gt(comparator_4_gt), .eq(comparator_4_eq));  // open: lt
  or or_3 (or_3_out, comparator_6_gt, comparator_6_eq);
  Comparator #(.mode("unsigned"), .width(32)) comparator_5 (
    .a(addr_i), .b(32'hff000008), .lt(comparator_5_lt));  // open: gt, eq
  Comparator #(.mode("unsigned"), .width(32)) comparator_6 (
    .a(addr_i), .b(32'hff000004), .gt(comparator_6_gt), .eq(comparator_6_eq));  // open: lt
  and and_1 (is_mem_addr, comparator_1_lt, or_1_out);
  and and_2 (is_lb_addr, comparator_3_lt, or_2_out);
  and and_3 (is_tty_addr, comparator_5_lt, or_3_out);
  Multiplexer #(.width(32)) multiplexer_1 (.in0(multiplexer_2_out), .in1(mem_data_i), .out(rdata_o), .sel(is_mem_addr));
  Multiplexer #(.width(32)) multiplexer_2 (
    .in0({32{1'b0}}), .in1(lb_data_i), .out(multiplexer_2_out), .sel(is_lb_addr));
  and and_4 (mem_we_o, we_i, is_mem_addr);
  and and_5 (tty_we_o, we_i, is_tty_addr);
  and and_6 (lb_we_o, we_i, is_lb_addr);

  assign lb_be0_0 = be0_i;
  assign lb_be1_0 = be1_i;
  assign lb_be2_0 = be2_i;
  assign lb_be3_0 = be3_i;
  assign lb_data_o = wdata_i;
  assign mem_addr_o = addr_i;
  assign mem_be0_o = be0_i;
  assign mem_be1_o = be1_i;
  assign mem_be2_o = be2_i;
  assign mem_be3_o = be3_i;
  assign mem_data_o = wdata_i;
  assign tty_data_o = wdata_i;
endmodule

module d_ledbar (
  input  [31:0] d_i,
  input  be0_i,
  input  be1_i,
  input  be2_i,
  input  be3_i,
  input  wen_i,
  input  clk_i,
  input  rst_in,
  output [31:0] data_o,
  output [31:0] d_rd_o
);

  wire and_1_out, and_2_out, and_3_out, and_4_out;

  Register register_1 (.D(d_i[7:0]), .en(and_1_out), .clk(clk_i), .Q(d_rd_o[7:0]), .clr(rst_in));
  and and_1 (and_1_out, be0_i, wen_i);
  Register register_2 (.D(d_i[15:8]), .en(and_2_out), .clk(clk_i), .Q(d_rd_o[15:8]), .clr(rst_in));
  and and_2 (and_2_out, be1_i, wen_i);
  Register register_3 (.D(d_i[23:16]), .en(and_3_out), .clk(clk_i), .Q(d_rd_o[23:16]), .clr(rst_in));
  and and_3 (and_3_out, be2_i, wen_i);
  Register register_4 (.D(d_i[31:24]), .en(and_4_out), .clk(clk_i), .Q(d_rd_o[31:24]), .clr(rst_in));
  and and_4 (and_4_out, be3_i, wen_i);

  assign data_o = d_rd_o;
endmodule

module InmExtractor (
  input  [31:0] instr,
  output [31:0] I_imm,
  output [31:0] S_imm,
  output [31:0] B_imm,
  output [31:0] U_imm,
  output [31:0] J_imm
);

  // NoConnect on instr[6:0]
  assign {I_imm[31], B_imm[31:12]} = {{20{instr[31]}}, instr[31]};  // Bit_Extender bit_extender_1
  // NoConnect on I_imm[31]
  // NoConnect on {I_imm[31], B_imm[31:13]}
  // NoConnect on {I_imm[31], B_imm[31:24]}

  assign B_imm[11:0] = {instr[7], instr[30:25], instr[11:8], 1'b0};
  assign I_imm[30:0] = {B_imm[31:12], instr[30:20]};
  assign J_imm = {B_imm[23:12], instr[19:12], instr[20], instr[30:21], 1'b0};
  assign S_imm = {I_imm[31], B_imm[31:12], instr[30:25], instr[11:7]};
  assign U_imm = {B_imm[12], instr[30:12], {12{1'b0}}};

  // Notes on the sheet:
  //   I-imm
  //   S-imm
  //   B-imm
  //   U-imm
  //   J-imm
endmodule

module IDecode (
  input  [31:0] instr,
  output [4:0] rd,
  output [2:0] funct3,
  output [4:0] rs1,
  output [4:0] rs2,
  output [6:0] funct7,
  output [31:0] imm,
  output ar_r,
  output ar_i,
  output ld,
  output st,
  output br,
  output jal,
  output jalr,
  output lui,
  output auipc,
  output ebc
);

  wire or_1_out;
  wire [31:0] inmextractor_1_b_imm, inmextractor_1_i_imm, inmextractor_1_j_imm, inmextractor_1_s_imm,
       inmextractor_1_u_imm, multiplexer_1_out, multiplexer_2_out, multiplexer_3_out;

  Comparator #(.width(7)) comparator_1 (.a(instr[6:0]), .b(7'b0110011), .eq(ar_r));  // open: gt, lt
  Comparator #(.width(7)) comparator_2 (.a(instr[6:0]), .b(7'b0010011), .eq(ar_i));  // open: gt, lt
  Comparator #(.width(7)) comparator_3 (.a(instr[6:0]), .b(7'b0000011), .eq(ld));  // open: gt, lt
  Comparator #(.width(7)) comparator_4 (.a(instr[6:0]), .b(7'b0100011), .eq(st));  // open: gt, lt
  Comparator #(.width(7)) comparator_5 (.a(instr[6:0]), .b(7'b1100011), .eq(br));  // open: gt, lt
  Comparator #(.width(7)) comparator_6 (.a(instr[6:0]), .b(7'b1101111), .eq(jal));  // open: gt, lt
  Comparator #(.width(7)) comparator_7 (.a(instr[6:0]), .b(7'b1100111), .eq(jalr));  // open: gt, lt
  Comparator #(.width(7)) comparator_8 (.a(instr[6:0]), .b(7'b0110111), .eq(lui));  // open: gt, lt
  Comparator #(.width(7)) comparator_9 (.a(instr[6:0]), .b(7'b0010111), .eq(auipc));  // open: gt, lt
  Comparator #(.width(7)) comparator_10 (.a(instr[6:0]), .b(7'b1110011), .eq(ebc));  // open: gt, lt
  InmExtractor inmextractor_1 (
    .instr(instr), .I_imm(inmextractor_1_i_imm), .S_imm(inmextractor_1_s_imm), .B_imm(inmextractor_1_b_imm),
    .U_imm(inmextractor_1_u_imm), .J_imm(inmextractor_1_j_imm));
  Multiplexer #(.width(32)) multiplexer_1 (
    .in0(inmextractor_1_i_imm), .in1(inmextractor_1_s_imm), .out(multiplexer_1_out), .sel(st));
  Multiplexer #(.width(32)) multiplexer_2 (
    .in0(multiplexer_1_out), .in1(inmextractor_1_b_imm), .out(multiplexer_2_out), .sel(br));
  Multiplexer #(.width(32)) multiplexer_3 (
    .in0(multiplexer_2_out), .in1(inmextractor_1_u_imm), .out(multiplexer_3_out), .sel(or_1_out));
  or or_1 (or_1_out, auipc, lui);
  Multiplexer #(.width(32)) multiplexer_4 (.in0(multiplexer_3_out), .in1(inmextractor_1_j_imm), .out(imm), .sel(jal));

  assign funct3 = instr[14:12];
  assign funct7 = instr[31:25];
  assign rd = instr[11:7];
  assign rs1 = instr[19:15];
  assign rs2 = instr[24:20];
endmodule

// VHDL entity ALU, as the project stores it:
LIBRARY ieee;
USE ieee.std_logic_1164.all;

ENTITY ALU IS
  PORT (
  ------------------------------------------------------------------------------
  --Insert input ports below
    clock      : IN  std_logic;                    -- input bit example
    val        : IN  std_logic_vector(3 DOWNTO 0); -- input vector example
  ------------------------------------------------------------------------------
  --Insert output ports below
    max        : OUT std_logic;                    -- output bit example
    cpt        : OUT std_logic_vector(3 DOWNTO 0)  -- output vector example
    );
END ALU;

--------------------------------------------------------------------------------
--Complete your VHDL description below
--------------------------------------------------------------------------------

ARCHITECTURE TypeArchitecture OF ALU IS

BEGIN


END TypeArchitecture;
