// Logisim project 32RV.circ as structural Verilog
module test_sdram (
  input  OPERATION1,
  input  OPERATION2,
  input  READY1,
  input  READY2,
  input  [2:0] ADDR1,
  input  [2:0] ADDR2,
  input  [31:0] DATA_IN1,
  input  [31:0] DATA_IN2,
  output [31:0] DATA_OUT1,
  output [31:0] DATA_OUT2
);

  wire clock_1_out, RESET_out;

  LED led_1 (.in(clock_1_out));
  LED led_2 (.in(RESET_out));
  Clock clock_1 (.out(clock_1_out));
  Button RESET (.out(RESET_out));
  Hex_Digit_Display #(.decimalPoint("false")) hex_digit_display_1 (.value(DATA_OUT2[31:28]));
  Hex_Digit_Display #(.decimalPoint("false")) hex (.value(DATA_OUT1[31:28]));
  Hex_Digit_Display #(.decimalPoint("false")) hex_1 (.value(DATA_OUT1[27:24]));
  Hex_Digit_Display #(.decimalPoint("false")) hex_digit_display_2 (.value(DATA_OUT2[27:24]));
  Hex_Digit_Display #(.decimalPoint("false")) hex_digit_display_3 (.value(DATA_OUT2[23:20]));
  Hex_Digit_Display #(.decimalPoint("false")) hex_2 (.value(DATA_OUT1[23:20]));
  Hex_Digit_Display #(.decimalPoint("false")) hex_3 (.value(DATA_OUT1[19:16]));
  Hex_Digit_Display #(.decimalPoint("false")) hex_digit_display_4 (.value(DATA_OUT2[19:16]));
  Hex_Digit_Display #(.decimalPoint("false")) hex_digit_display_5 (.value(DATA_OUT2[15:12]));
  Hex_Digit_Display #(.decimalPoint("false")) hex_4 (.value(DATA_OUT1[15:12]));
  Hex_Digit_Display #(.decimalPoint("false")) hex_5 (.value(DATA_OUT1[11:8]));
  Hex_Digit_Display #(.decimalPoint("false")) hex_digit_display_6 (.value(DATA_OUT2[11:8]));
  Hex_Digit_Display #(.decimalPoint("false")) hex_digit_display_7 (.value(DATA_OUT2[7:4]));
  Hex_Digit_Display #(.decimalPoint("false")) hex_6 (.value(DATA_OUT1[7:4]));
  Hex_Digit_Display #(.decimalPoint("false")) hex_7 (.value(DATA_OUT1[3:0]));
  sdram sdram_1 (
    .clk(clock_1_out), .reset(RESET_out), .operation1(OPERATION1), .operation2(OPERATION2), .ready1(READY1),
    .ready2(READY2), .addr1(ADDR1), .addr2(ADDR2), .data_in1(DATA_IN1), .data_in2(DATA_IN2),
    .data_out1(DATA_OUT1), .data_out2(DATA_OUT2));
  Hex_Digit_Display #(.decimalPoint("false")) hex_digit_display_8 (.value(DATA_OUT2[3:0]));
endmodule

module test_cache_controller (
  input  \priority ,
  input  [2:0] wantedAddress,
  input  [31:0] Sdram_data_in,
  input  cpu_wr_req_in,
  input  cpu_rd_req_in,
  input  [2:0] cpu_req_addr_in,
  input  cache_to_cache_req_in,
  input  [2:0] cache_to_cache_req_address_in,
  input  cache_to_cache_resp_in,
  input  cache_to_cache_resp_in_ready,
  input  [31:0] cache_to_cache_resp_in_data,
  output [2:0] Sdram_addr,
  output [31:0] Sdram_data_out,
  output [2:0] cpu_req_addr_out,
  output [2:0] cache_to_cache_req_address_out,
  output [31:0] cache_to_cache_resp_out_data,
  output [2:0] debug_cpu_state,
  output [2:0] debug_cache_state,
  output [2:0] debug_current_addr,
  output [1:0] debug_evict_index,
  output [3:0] debug_cycle_counter,
  output [1:0] debug_cache_line0_state,
  output [2:0] debug_cache_line0_addr,
  output [31:0] debug_cache_line0_data,
  output [1:0] debug_cache_line1_state,
  output [2:0] debug_cache_line1_addr,
  output [31:0] debug_cache_line1_data,
  output [1:0] debug_cache_line2_state,
  output [2:0] debug_cache_line2_addr,
  output [31:0] debug_cache_line2_data,
  output [1:0] debug_cache_line3_state,
  output [2:0] debug_cache_line3_addr,
  output [31:0] debug_cache_line3_data
);

  wire cache_controller_1_cache_to_cache_req_out, cache_controller_1_cache_to_cache_resp_out,
       cache_controller_1_cache_to_cache_resp_out_ready, cache_controller_1_cpu_rd_req_out,
       cache_controller_1_cpu_wr_req_out, cache_controller_1_debug_cache_hit,
       cache_controller_1_debug_cache_line0_valid, cache_controller_1_debug_cache_line1_valid,
       cache_controller_1_debug_cache_line2_valid, cache_controller_1_debug_cache_line3_valid,
       cache_controller_1_debug_operation_type, cache_controller_1_read_en, cache_controller_1_write_en,
       clk_out, reset_out;

  Button reset (.out(reset_out));
  Clock clk (.out(clk_out));
  Cache_Controller cache_controller_1 (
    .clk(clk_out), .reset(reset_out), .\priority (\priority ), .wantedAddress(wantedAddress),
    .Sdram_data_in(Sdram_data_in), .cpu_wr_req_in(cpu_wr_req_in), .cpu_rd_req_in(cpu_rd_req_in),
    .cpu_req_addr_in(cpu_req_addr_in), .cache_to_cache_req_in(cache_to_cache_req_in),
    .cache_to_cache_req_address_in(cache_to_cache_req_address_in),
    .cache_to_cache_resp_in(cache_to_cache_resp_in),
    .cache_to_cache_resp_in_ready(cache_to_cache_resp_in_ready),
    .cache_to_cache_resp_in_data(cache_to_cache_resp_in_data), .read_en(cache_controller_1_read_en),
    .write_en(cache_controller_1_write_en), .Sdram_addr(Sdram_addr), .Sdram_data_out(Sdram_data_out),
    .cpu_wr_req_out(cache_controller_1_cpu_wr_req_out), .cpu_rd_req_out(cache_controller_1_cpu_rd_req_out),
    .cpu_req_addr_out(cpu_req_addr_out), .cache_to_cache_req_out(cache_controller_1_cache_to_cache_req_out),
    .cache_to_cache_req_address_out(cache_to_cache_req_address_out),
    .cache_to_cache_resp_out(cache_controller_1_cache_to_cache_resp_out),
    .cache_to_cache_resp_out_ready(cache_controller_1_cache_to_cache_resp_out_ready),
    .cache_to_cache_resp_out_data(cache_to_cache_resp_out_data), .debug_cpu_state(debug_cpu_state),
    .debug_cache_state(debug_cache_state), .debug_cache_hit(cache_controller_1_debug_cache_hit),
    .debug_current_addr(debug_current_addr), .debug_operation_type(cache_controller_1_debug_operation_type),
    .debug_evict_index(debug_evict_index), .debug_cycle_counter(debug_cycle_counter),
    .debug_cache_line0_valid(cache_controller_1_debug_cache_line0_valid),
    .debug_cache_line0_state(debug_cache_line0_state), .debug_cache_line0_addr(debug_cache_line0_addr),
    .debug_cache_line0_data(debug_cache_line0_data),
    .debug_cache_line1_valid(cache_controller_1_debug_cache_line1_valid),
    .debug_cache_line1_state(debug_cache_line1_state), .debug_cache_line1_addr(debug_cache_line1_addr),
    .debug_cache_line1_data(debug_cache_line1_data),
    .debug_cache_line2_valid(cache_controller_1_debug_cache_line2_valid),
    .debug_cache_line2_state(debug_cache_line2_state), .debug_cache_line2_addr(debug_cache_line2_addr),
    .debug_cache_line2_data(debug_cache_line2_data),
    .debug_cache_line3_valid(cache_controller_1_debug_cache_line3_valid),
    .debug_cache_line3_state(debug_cache_line3_state), .debug_cache_line3_addr(debug_cache_line3_addr),
    .debug_cache_line3_data(debug_cache_line3_data));
  LED read_en (.in(cache_controller_1_read_en));
  LED cpu_wr_req_out (.in(cache_controller_1_cpu_wr_req_out));
  LED debug_cache_line0_valid (.in(cache_controller_1_debug_cache_line0_valid));
  LED debug_cache_line1_valid (.in(cache_controller_1_debug_cache_line1_valid));
  LED debug_cache_line2_valid (.in(cache_controller_1_debug_cache_line2_valid));
  LED debug_cache_line3_valid (.in(cache_controller_1_debug_cache_line3_valid));
  LED write_en (.in(cache_controller_1_write_en));
  LED cpu_rd_req_out (.in(cache_controller_1_cpu_rd_req_out));
  LED debug_cache_hit (.in(cache_controller_1_debug_cache_hit));
  LED cache_to_cache_req_out (.in(cache_controller_1_cache_to_cache_req_out));
  LED cache_to_cache_resp_out (.in(cache_controller_1_cache_to_cache_resp_out));
  LED cache_to_cache_resp_out_ready (.in(cache_controller_1_cache_to_cache_resp_out_ready));
  LED debug_operation_type (.in(cache_controller_1_debug_operation_type));
endmodule

module test_fifo (
);

  FIFO fifo_1 ();  // open: clk, rst, cpu0_read_in, cpu0_write_in, cpu0_data_in, cpu0_addr, cpu1_read_in, cpu1_write_in, cpu1_data_in, cpu1_addr, read_out, write_out, addr_out, data_out
endmodule

// VHDL entity msi_protocol, as the project stores it:
library ieee;
use ieee.std_logic_1164.all;
use ieee.numeric_std.all;

entity msi_protocol is
    port (
        clk             : in std_logic;
        reset           : in std_logic;
        cpu0_state      : in std_logic_vector(1 downto 0); -- MSI state for cpu0
        cpu1_state      : in std_logic_vector(1 downto 0); -- MSI state for cpu1
        cpu0_addr       : in std_logic_vector(31 downto 0);   -- Address from cpu0
        cpu1_addr       : in std_logic_vector(31 downto 0);   -- Address from cpu1
        invalidate_cpu0 : out std_logic;                      -- Invalidate signal for cpu0
        invalidate_cpu1 : out std_logic                       -- Invalidate signal for cpu1
    );
end msi_protocol;

architecture Behavioral of msi_protocol is
begin
    process(clk, reset)
    begin
        if reset = '1' then
            invalidate_cpu0 <= '0';
            invalidate_cpu1 <= '0';
        elsif rising_edge(clk) then
            -- If CPU0 modifies a cache line, invalidate the corresponding line in CPU1
            if cpu0_state = "10" then -- Modified state in cpu0
                if cpu1_state = "01" and cpu0_addr = cpu1_addr then -- Shared state in cpu1 for the same address
                    invalidate_cpu1 <= '1'; -- Invalidate the cache line in cpu1
                else
                    invalidate_cpu1 <= '0';
                end if;
            end if;
            
            -- If CPU1 modifies a cache line, invalidate the corresponding line in CPU0
            if cpu1_state = "10" then -- Modified state in cpu1
                if cpu0_state = "01" and cpu1_addr = cpu0_addr then -- Shared state in cpu0 for the same address
                    invalidate_cpu0 <= '1'; -- Invalidate the cache line in cpu0
                else
                    invalidate_cpu0 <= '0';
                end if;
            end if;
        end if;
    end process;
end Behavioral;

// VHDL entity FIFO, as the project stores it:
library ieee;
use ieee.std_logic_1164.all;
use ieee.numeric_std.all;

entity FIFO is
  port(
    clk            : in  std_logic;	-- system clock
    rst            : in  std_logic;	-- synchronous reset

    -- CPU0 interface
    cpu0_read_in   : in  std_logic;					-- CPU0 read request (1 = read)
    cpu0_write_in  : in  std_logic;					-- CPU0 write request (1 = write)
    cpu0_data_in   : in  std_logic_vector(31 downto 0);	-- CPU0 write data
    cpu0_addr      : in  std_logic_vector(2 downto 0);	-- CPU0 address

    -- CPU1 interface
    cpu1_read_in   : in  std_logic;
    cpu1_write_in  : in  std_logic;
    cpu1_data_in   : in  std_logic_vector(31 downto 0);
    cpu1_addr      : in  std_logic_vector(2 downto 0);

    -- Output to SDRAM
    read_out       : out std_logic;	-- 1 = perform read
    write_out      : out std_logic;	-- 1 = perform write

    addr_out       : out std_logic_vector(2 downto 0);	-- address to SDRAM
    data_out       : out std_logic_vector(31 downto 0)	-- data to SDRAM (for writes)
  );
end entity FIFO;

architecture behavior of FIFO is
  -- record and array _types_
  type sdramrequest is record
    requester : std_logic;			-- '0' = CPU0, '1' = CPU1
    operation : std_logic;            	-- 0 = read, 1 = write
    address   : std_logic_vector(2 downto 0);
    data      : std_logic_vector(31 downto 0);
    valid     : std_logic;
  end record sdramrequest;

  -- circular buffer of 1024 requests
  type sdramRequestBuffer is array(0 to 1023) of sdramrequest;

  -- allocate the buffer signal 
  signal request_buf : sdramRequestBuffer := (
    others => (
      requester => '0',
      operation => '0',
      address   => (others => '0'),
      data      => (others => '0'),
      valid     => '0'
    )
  );

  -- track which CPU was last served 
  signal previousRequester : std_logic;  -- 0 is cpu0, 1 is cpu1

begin

  process(clk, rst)
  begin
    if rst = '1' then
    	 -- synchronous reset: clear buffer and outputs
      -- clear buffer on reset
      request_buf <= (others => (
        requester => '0',
        operation => '0',
        address   => (others => '0'),
        data      => (others => '0'),
        valid     => '0'
      ));
      read_out  <= '0';
      write_out <= '0';
      previousRequester <= '0';

    elsif rising_edge(clk) then

    	 -- if there’s a pending SDRAM request at buffer slot 0
      if request_buf(0).valid = '1' then
        -- dequeue slot 0
        read_out  <= not request_buf(0).operation;
        write_out <=     request_buf(0).operation;
        addr_out  <=     request_buf(0).address;
        data_out  <=     request_buf(0).data;

        -- once served, invalidate this slot
        request_buf(0).valid <= '0';

      else
      -- buffer is empty → directly arbitrate between CPU0 & CPU1

        -- 1) No requests from either CPU
        if cpu0_read_in='0' and cpu0_write_in='0'
           and cpu1_read_in='0' and cpu1_write_in='0' then

          read_out  <= '0';
          write_out <= '0';

        -- 2) CPU1 wants to write only
        elsif cpu0_read_in='0' and cpu0_write_in='0'
           and cpu1_read_in='0' and cpu1_write_in='1' then

          read_out          <= '0';
          write_out         <= '1';
          previousRequester <= '1';

        -- 3) CPU1 wants to read only
        elsif cpu0_read_in='0' and cpu0_write_in='0'
           and cpu1_read_in='1' and cpu1_write_in='0' then

          read_out          <= '1';
          write_out         <= '0';
          previousRequester <= '1';

        -- 4) CPU0 wants to write only
        elsif cpu0_read_in='0' and cpu0_write_in='1'
           and cpu1_read_in='0' and cpu1_write_in='0' then

          read_out          <= '0';
          write_out         <= '1';
          previousRequester <= '0';

        -- 5) CPU0 wants to read only
        elsif cpu0_read_in='1' and cpu0_write_in='0'
           and cpu1_read_in='0' and cpu1_write_in='0' then

          read_out          <= '1';
          write_out         <= '0';
          previousRequester <= '0';

        -- 6) Both CPUs want to read → enqueue CPU1’s read
        elsif cpu0_read_in='1' and cpu0_write_in='0'
           and cpu1_read_in='1' and cpu1_write_in='0' then

          read_out          <= '1';
          write_out         <= '0';
          previousRequester <= '0';

          request_buf(0).requester <= '1';        -- from CPU1
          request_buf(0).operation <= '0';        -- read
          request_buf(0).address   <= cpu1_addr;
          request_buf(0).valid     <= '1';

        -- 7) CPU0 read & CPU1 write → enqueue CPU1’s write
        elsif cpu0_read_in='1' and cpu0_write_in='0'
           and cpu1_read_in='0' and cpu1_write_in='1' then

          read_out          <= '1';
          write_out         <= '0';
          previousRequester <= '0';

          request_buf(0).requester <= '1';
          request_buf(0).operation <= '1';        -- write
          request_buf(0).address   <= cpu1_addr;
          request_buf(0).data      <= cpu1_data_in;
          request_buf(0).valid     <= '1';

        -- 8) CPU0 write & CPU1 read → enqueue CPU1’s read
        elsif cpu0_read_in='0' and cpu0_write_in='1'
           and cpu1_read_in='1' and cpu1_write_in='0' then

          read_out          <= '0';
          write_out         <= '1';
          previousRequester <= '0';

          request_buf(0).requester <= '1';
          request_buf(0).operation <= '0';        -- read
          request_buf(0).address   <= cpu1_addr;
          request_buf(0).valid     <= '1';

        -- 9) Both CPUs want to write → enqueue CPU1’s write
        elsif cpu0_read_in='0' and cpu0_write_in='1'
           and cpu1_read_in='0' and cpu1_write_in='1' then

          read_out          <= '0';
          write_out         <= '1';
          previousRequester <= '0';

          request_buf(0).requester <= '1';
          request_buf(0).operation <= '1';
          request_buf(0).address   <= cpu1_addr;
          request_buf(0).data      <= cpu1_data_in;
          request_buf(0).valid     <= '1';

        end if;
      end if;

    end if;
  end process;

end architecture behavior;

// VHDL entity TransactionsBetweenCPU, as the project stores it:
library ieee;
use ieee.std_logic_1164.all;

LIBRARY work;

entity TransactionsBetweenCPU is
  port(
    clk             : in  std_logic;                    -- system clock
    rst             : in  std_logic;                    -- synchronous reset
    cpu0_prio       : in  std_logic;                    -- arbitration priority for CPU0
    cpu1_prio       : in  std_logic;                    -- arbitration priority for CPU1
    cpu0_wantedAddr : in  std_logic_vector(2 downto 0); -- CPU0 target address
    cpu1_wantedAddr : in  std_logic_vector(2 downto 0)  -- CPU1 target address
  );
end entity TransactionsBetweenCPU;

architecture bdf_type of TransactionsBetweenCPU is

  -- Cache controller component
  component Cache_Controller is
    port(
      clk                          : in  std_logic;
      reset                        : in  std_logic;
      priority                     : in  std_logic;
      cpu_wr_req_in                : in  std_logic;
      cpu_rd_req_in                : in  std_logic;
      cache_to_cache_resp_in_ready: in  std_logic;
      cache_to_cache_resp_in       : in  std_logic;
      cache_to_cache_req_in        : in  std_logic;
      cache_to_cache_req_address_in: in  std_logic_vector(2 downto 0);
      cache_to_cache_resp_in_data  : in  std_logic_vector(31 downto 0);
      cpu_req_addr_in              : in  std_logic_vector(2 downto 0);
      Sdram_data_in                : in  std_logic_vector(31 downto 0);
      wantedAddress                : in  std_logic_vector(2 downto 0);
      read_en                      : out std_logic;
      write_en                     : out std_logic;
      cpu_wr_req_out               : out std_logic;
      cpu_rd_req_out               : out std_logic;
      cache_to_cache_resp_out_ready: out std_logic;
      cache_to_cache_resp_out      : out std_logic;
      cache_to_cache_req_out       : out std_logic;
      cache_to_cache_req_address_out: out std_logic_vector(2 downto 0);
      cache_to_cache_resp_out_data : out std_logic_vector(31 downto 0);
      cpu_req_addr_out             : out std_logic_vector(2 downto 0);
      Sdram_addr                   : out std_logic_vector(2 downto 0);
      Sdram_data_out               : out std_logic_vector(31 downto 0)
    );
  end component;


  -- SDRAM component
  component sdram is
    port(
      clk        : in  std_logic;
      reset      : in  std_logic;
      operation1 : in  std_logic;                     -- 0=read, 1=write on port1
      operation2 : in  std_logic;                     -- 0=read, 1=write on port2
      ready1     : in  std_logic;                     -- handshake from CPU1
      ready2     : in  std_logic;                     -- handshake from CPU2
      addr1      : in  std_logic_vector(2 downto 0);
      addr2      : in  std_logic_vector(2 downto 0);
      data_in1   : in  std_logic_vector(31 downto 0); -- CPU→SDRAM data
      data_in2   : in  std_logic_vector(31 downto 0);
      data_out1  : out std_logic_vector(31 downto 0); -- SDRAM→CPU data
      data_out2  : out std_logic_vector(31 downto 0)
    );
  end component;

  -- Internal signals for cache‐to‐cache traffic
  signal cpu0_cache_to_cache_req              : std_logic;
  signal cpu0_cache_to_cache_req_addr         : std_logic_vector(2 downto 0);
  signal cpu0_cache_to_cache_resp_data        : std_logic_vector(31 downto 0);
  signal cpu0_cache_to_cache_response         : std_logic;
  signal cpu0_cache_to_cache_response_out_ready : std_logic;
  signal cpu0_wr_req_out                      : std_logic;
  signal cpu0_rd_req_out                      : std_logic;
  signal cpu0_req_addr_out                    : std_logic_vector(2 downto 0);

  signal cpu1_cache_to_cache_req              : std_logic;
  signal cpu1_cache_to_cache_req_addr         : std_logic_vector(2 downto 0);
  signal cpu1_cache_to_cache_resp_data        : std_logic_vector(31 downto 0);
  signal cpu1_cache_to_cache_response         : std_logic;
  signal cpu1_cache_to_cache_response_out_ready : std_logic;
  signal cpu1_wr_req_out                      : std_logic;
  signal cpu1_rd_req_out                      : std_logic;
  signal cpu1_req_addr_out                    : std_logic_vector(2 downto 0);

  -- Read/Write enable flags from each CPU
  signal r_en1  : std_logic;
  signal wr_en1 : std_logic;
  signal r_en2  : std_logic;
  signal wr_en2 : std_logic;

  -- Combined “ready” lines into SDRAM
  signal ready1_sig : std_logic;
  signal ready2_sig : std_logic;

  -- Address buses from CPU → SDRAM
  signal sdram_addr1 : std_logic_vector(2 downto 0);
  signal sdram_addr2 : std_logic_vector(2 downto 0);

  -- Data buses CPU → SDRAM
  signal sdram_data_out1 : std_logic_vector(31 downto 0);
  signal sdram_data_out2 : std_logic_vector(31 downto 0);

  -- Data buses SDRAM → CPU
  signal sdram_data_in1  : std_logic_vector(31 downto 0);
  signal sdram_data_in2  : std_logic_vector(31 downto 0);

begin

  -- Generate “ready” handshake for SDRAM ports
  ready1_sig <= wr_en1 or r_en1;
  ready2_sig <= wr_en2 or r_en2;

  -- CPU Core #0 instance
  core0: Cache_Controller
    port map(
      clk                            => clk,
      reset                          => rst,
      priority                       => cpu0_prio,
      cpu_wr_req_in                  => cpu1_wr_req_out,
      cpu_rd_req_in                  => cpu1_rd_req_out,
      cache_to_cache_resp_in_ready   => cpu1_cache_to_cache_response_out_ready,
      cache_to_cache_resp_in         => cpu1_cache_to_cache_response,
      cache_to_cache_req_in          => cpu1_cache_to_cache_req,
      cache_to_cache_req_address_in  => cpu1_cache_to_cache_req_addr,
      cache_to_cache_resp_in_data    => cpu1_cache_to_cache_resp_data,
      cpu_req_addr_in                => cpu1_req_addr_out,
      Sdram_data_in                  => sdram_data_in1,     -- from SDRAM
      wantedAddress                  => cpu0_wantedAddr,
      read_en                        => r_en1,
      write_en                       => wr_en1,
      cpu_wr_req_out                 => cpu0_wr_req_out,
      cpu_rd_req_out                 => cpu0_rd_req_out,
      cache_to_cache_resp_out_ready  => cpu0_cache_to_cache_response_out_ready,
      cache_to_cache_resp_out        => cpu0_cache_to_cache_response,
      cache_to_cache_req_out         => cpu0_cache_to_cache_req,
      cache_to_cache_req_address_out => cpu0_cache_to_cache_req_addr,
      cache_to_cache_resp_out_data   => cpu0_cache_to_cache_resp_data,
      cpu_req_addr_out               => cpu0_req_addr_out,
      Sdram_addr                     => sdram_addr1,         -- to SDRAM
      Sdram_data_out                 => sdram_data_out1      -- to SDRAM
    );

  -- CPU Core #1 instance
  core1: Cache_Controller
    port map(
      clk                            => clk,
      reset                          => rst,
      priority                       => cpu1_prio,
      cpu_wr_req_in                  => cpu0_wr_req_out,
      cpu_rd_req_in                  => cpu0_rd_req_out,
      cache_to_cache_resp_in_ready   => cpu0_cache_to_cache_response_out_ready,
      cache_to_cache_resp_in         => cpu0_cache_to_cache_response,
      cache_to_cache_req_in          => cpu0_cache_to_cache_req,
      cache_to_cache_req_address_in  => cpu0_cache_to_cache_req_addr,
      cache_to_cache_resp_in_data    => cpu0_cache_to_cache_resp_data,
      cpu_req_addr_in                => cpu0_req_addr_out,
      Sdram_data_in                  => sdram_data_in2,     -- from SDRAM
      wantedAddress                  => cpu1_wantedAddr,
      read_en                        => r_en2,
      write_en                       => wr_en2,
      cpu_wr_req_out                 => cpu1_wr_req_out,
      cpu_rd_req_out                 => cpu1_rd_req_out,
      cache_to_cache_resp_out_ready  => cpu1_cache_to_cache_response_out_ready,
      cache_to_cache_resp_out        => cpu1_cache_to_cache_response,
      cache_to_cache_req_out         => cpu1_cache_to_cache_req,
      cache_to_cache_req_address_out => cpu1_cache_to_cache_req_addr,
      cache_to_cache_resp_out_data   => cpu1_cache_to_cache_resp_data,
      cpu_req_addr_out               => cpu1_req_addr_out,
      Sdram_addr                     => sdram_addr2,         -- to SDRAM
      Sdram_data_out                 => sdram_data_out2      -- to SDRAM
    );

  -- SDRAM instance (port‐interleaved two‐port memory)
  sdram0: sdram
    port map(
      clk        => clk,
      reset      => rst,
      operation1 => wr_en1,           -- write when wr_en1='1'
      operation2 => wr_en2,           -- write when wr_en2='1'
      ready1     => ready1_sig,
      ready2     => ready2_sig,
      addr1      => sdram_addr1,
      addr2      => sdram_addr2,
      data_in1   => sdram_data_out1,  -- CPU0 → SDRAM
      data_in2   => sdram_data_out2,  -- CPU1 → SDRAM
      data_out1  => sdram_data_in1,   -- SDRAM → CPU0
      data_out2  => sdram_data_in2    -- SDRAM → CPU1
    );

end architecture bdf_type;

// VHDL entity Cache_Controller, as the project stores it:
library ieee;
use ieee.std_logic_1164.all;
use ieee.numeric_std.all;

entity Cache_Controller is
    port (
        clk            : in std_logic;
        reset          : in std_logic;
        priority       : in std_logic;
        
        -- CPU interface
        wantedAddress  : in std_logic_vector(2 downto 0);
        
        -- SDRAM interface
        read_en        : out std_logic;
        write_en       : out std_logic;
        Sdram_addr     : out std_logic_vector(2 downto 0);
        Sdram_data_in  : in std_logic_vector(31 downto 0);
        Sdram_data_out : out std_logic_vector(31 downto 0);
        
        -- MSI protocol - outgoing requests
        cpu_wr_req_out : out std_logic;
        cpu_rd_req_out : out std_logic;
        cpu_req_addr_out : out std_logic_vector(2 downto 0);
        
        -- MSI protocol - incoming requests (snooping)
        cpu_wr_req_in  : in std_logic;
        cpu_rd_req_in  : in std_logic;
        cpu_req_addr_in : in std_logic_vector(2 downto 0);
        
        -- Cache-to-cache communication - outgoing
        cache_to_cache_req_out : out std_logic;
        cache_to_cache_req_address_out : out std_logic_vector(2 downto 0);
        cache_to_cache_resp_out : out std_logic;
        cache_to_cache_resp_out_ready : out std_logic;
        cache_to_cache_resp_out_data : out std_logic_vector(31 downto 0);
        
        -- Cache-to-cache communication - incoming
        cache_to_cache_req_in : in std_logic;
        cache_to_cache_req_address_in : in std_logic_vector(2 downto 0);
        cache_to_cache_resp_in : in std_logic;
        cache_to_cache_resp_in_ready : in std_logic;
        cache_to_cache_resp_in_data : in std_logic_vector(31 downto 0);
        
        -- DEBUG OUTPUTS - Estado del controlador de cache
        debug_cpu_state      : out std_logic_vector(2 downto 0);    -- Estado de la CPU (idle/read/write/wait)
        debug_cache_state    : out std_logic_vector(2 downto 0);    -- Estado de la cache (check/hit/miss/coherence/sdram)
        debug_cache_hit      : out std_logic;                       -- Señal de cache hit
        debug_current_addr   : out std_logic_vector(2 downto 0);    -- Dirección actual siendo procesada
        debug_operation_type : out std_logic;                       -- Tipo de operación (0=read, 1=write)
        debug_evict_index    : out std_logic_vector(1 downto 0);    -- Índice de evicción actual
        debug_cycle_counter  : out std_logic_vector(3 downto 0);    -- Contador de ciclos
        
        -- DEBUG OUTPUTS - Estado de las líneas de cache
        debug_cache_line0_valid : out std_logic;                    -- Línea 0 válida
        debug_cache_line0_state : out std_logic_vector(1 downto 0); -- Estado MSI línea 0 (00=Invalid, 01=Shared, 10=Modified)
        debug_cache_line0_addr  : out std_logic_vector(2 downto 0); -- Dirección línea 0
        debug_cache_line0_data  : out std_logic_vector(31 downto 0);-- Datos línea 0
        
        debug_cache_line1_valid : out std_logic;                    -- Línea 1 válida
        debug_cache_line1_state : out std_logic_vector(1 downto 0); -- Estado MSI línea 1
        debug_cache_line1_addr  : out std_logic_vector(2 downto 0); -- Dirección línea 1
        debug_cache_line1_data  : out std_logic_vector(31 downto 0);-- Datos línea 1
        
        debug_cache_line2_valid : out std_logic;                    -- Línea 2 válida
        debug_cache_line2_state : out std_logic_vector(1 downto 0); -- Estado MSI línea 2
        debug_cache_line2_addr  : out std_logic_vector(2 downto 0); -- Dirección línea 2
        debug_cache_line2_data  : out std_logic_vector(31 downto 0);-- Datos línea 2
        
        debug_cache_line3_valid : out std_logic;                    -- Línea 3 válida
        debug_cache_line3_state : out std_logic_vector(1 downto 0); -- Estado MSI línea 3
        debug_cache_line3_addr  : out std_logic_vector(2 downto 0); -- Dirección línea 3
        debug_cache_line3_data  : out std_logic_vector(31 downto 0) -- Datos línea 3
    );
end Cache_Controller;

architecture Behavioral of Cache_Controller is
    -- Cache configuration
    constant CACHE_SIZE : integer := 4;
    
    -- MSI states
    type msi_state_type is (MSI_INVALID, MSI_SHARED, MSI_MODIFIED);
    
    -- Cache line structure
    type cache_line_type is record
        msi_state : msi_state_type;
        address   : std_logic_vector(2 downto 0);
        data      : std_logic_vector(31 downto 0);
        valid     : std_logic;
    end record;
    
    type cache_array_type is array (0 to CACHE_SIZE-1) of cache_line_type;
    
    -- CPU operation states
    type cpu_state_type is (CPU_IDLE, CPU_READ, CPU_WRITE, CPU_WAIT_CACHE, CPU_WAIT_SDRAM);
    
    -- Cache operation states  
    type cache_state_type is (CACHE_CHECK, CACHE_HIT, CACHE_MISS, CACHE_COHERENCE, CACHE_SDRAM_ACCESS);
    
    -- Signals
    signal cache_mem : cache_array_type;
    signal cpu_state : cpu_state_type;
    signal cache_state : cache_state_type;
    signal current_address : std_logic_vector(2 downto 0);
    signal current_data : std_logic_vector(31 downto 0);
    signal cache_hit_flag : std_logic;
    signal cache_hit_index : integer range 0 to CACHE_SIZE-1;
    signal evict_index : integer range 0 to CACHE_SIZE-1;
    signal operation_type : std_logic; -- 0 = read, 1 = write
    signal cycle_counter : integer range 0 to 15;
    
    -- Helper functions
    function find_cache_line(addr : std_logic_vector(2 downto 0); cache_mem : cache_array_type) 
        return integer is
    begin
        for i in 0 to CACHE_SIZE-1 loop
            if cache_mem(i).valid = '1' and cache_mem(i).address = addr then
                return i;
            end if;
        end loop;
        return -1; -- Not found
    end function;
    
    function find_empty_line(cache_mem : cache_array_type) return integer is
    begin
        for i in 0 to CACHE_SIZE-1 loop
            if cache_mem(i).valid = '0' then
                return i;
            end if;
        end loop;
        return -1; -- Cache full
    end function;

begin

    -- Asignaciones continuas para señales de debug
    debug_current_addr <= current_address;
    debug_operation_type <= operation_type;
    debug_cache_hit <= cache_hit_flag;
    debug_evict_index <= std_logic_vector(to_unsigned(evict_index, 2));
    debug_cycle_counter <= std_logic_vector(to_unsigned(cycle_counter, 4));
    
    -- Codificación de estados de CPU para debug
    with cpu_state select debug_cpu_state <=
        "000" when CPU_IDLE,
        "001" when CPU_READ,
        "010" when CPU_WRITE,
        "011" when CPU_WAIT_CACHE,
        "100" when CPU_WAIT_SDRAM,
        "111" when others;
    
    -- Codificación de estados de cache para debug
    with cache_state select debug_cache_state <=
        "000" when CACHE_CHECK,
        "001" when CACHE_HIT,
        "010" when CACHE_MISS,
        "011" when CACHE_COHERENCE,
        "100" when CACHE_SDRAM_ACCESS,
        "111" when others;
    
    -- Debug outputs para líneas de cache (línea 0)
    debug_cache_line0_valid <= cache_mem(0).valid;
    debug_cache_line0_addr <= cache_mem(0).address;
    debug_cache_line0_data <= cache_mem(0).data;
    with cache_mem(0).msi_state select debug_cache_line0_state <=
        "00" when MSI_INVALID,
        "01" when MSI_SHARED,
        "10" when MSI_MODIFIED,
        "11" when others;
    
    -- Debug outputs para líneas de cache (línea 1)
    debug_cache_line1_valid <= cache_mem(1).valid;
    debug_cache_line1_addr <= cache_mem(1).address;
    debug_cache_line1_data <= cache_mem(1).data;
    with cache_mem(1).msi_state select debug_cache_line1_state <=
        "00" when MSI_INVALID,
        "01" when MSI_SHARED,
        "10" when MSI_MODIFIED,
        "11" when others;
    
    -- Debug outputs para líneas de cache (línea 2)
    debug_cache_line2_valid <= cache_mem(2).valid;
    debug_cache_line2_addr <= cache_mem(2).address;
    debug_cache_line2_data <= cache_mem(2).data;
    with cache_mem(2).msi_state select debug_cache_line2_state <=
        "00" when MSI_INVALID,
        "01" when MSI_SHARED,
        "10" when MSI_MODIFIED,
        "11" when others;
    
    -- Debug outputs para líneas de cache (línea 3)
    debug_cache_line3_valid <= cache_mem(3).valid;
    debug_cache_line3_addr <= cache_mem(3).address;
    debug_cache_line3_data <= cache_mem(3).data;
    with cache_mem(3).msi_state select debug_cache_line3_state <=
        "00" when MSI_INVALID,
        "01" when MSI_SHARED,
        "10" when MSI_MODIFIED,
        "11" when others;

    -- Main cache controller process
    main_process: process(clk, reset)
        variable hit_index : integer;
        variable empty_index : integer;
    begin
        if reset = '1' then
            -- Initialize cache
            for i in 0 to CACHE_SIZE-1 loop
                cache_mem(i).msi_state <= MSI_INVALID;
                cache_mem(i).address <= (others => '0');
                cache_mem(i).data <= (others => '0');
                cache_mem(i).valid <= '0';
            end loop;
            
            -- Reset state machines
            cpu_state <= CPU_IDLE;
            cache_state <= CACHE_CHECK;
            
            -- Reset outputs
            read_en <= '0';
            write_en <= '0';
            cpu_wr_req_out <= '0';
            cpu_rd_req_out <= '0';
            cache_to_cache_req_out <= '0';
            cache_to_cache_resp_out <= '0';
            cache_to_cache_resp_out_ready <= '0';
            
            -- Reset internal signals
            current_address <= (others => '0');
            current_data <= (others => '0');
            cache_hit_flag <= '0';
            cache_hit_index <= 0;
            operation_type <= '0';
            evict_index <= 0;
            cycle_counter <= 0;
            
        elsif rising_edge(clk) then
            -- Default signal values
            read_en <= '0';
            write_en <= '0';
            cache_to_cache_req_out <= '0';
            cache_to_cache_resp_out <= '0';
            cache_to_cache_resp_out_ready <= '0';
            
            -- Handle snooping requests from other caches
            if cache_to_cache_req_in = '1' then
                hit_index := find_cache_line(cache_to_cache_req_address_in, cache_mem);
                if hit_index >= 0 then
                    if cache_mem(hit_index).msi_state = MSI_MODIFIED then
                        -- Provide data and transition to shared
                        cache_to_cache_resp_out <= '1';
                        cache_to_cache_resp_out_data <= cache_mem(hit_index).data;
                        cache_mem(hit_index).msi_state <= MSI_SHARED;
                    elsif cache_mem(hit_index).msi_state = MSI_SHARED then
                        -- Provide data, stay shared
                        cache_to_cache_resp_out <= '1';
                        cache_to_cache_resp_out_data <= cache_mem(hit_index).data;
                    end if;
                else
                    cache_to_cache_resp_out <= '0';
                end if;
                cache_to_cache_resp_out_ready <= '1';
            end if;
            
            -- Handle invalidation requests
            if cpu_wr_req_in = '1' then
                hit_index := find_cache_line(cpu_req_addr_in, cache_mem);
                if hit_index >= 0 then
                    cache_mem(hit_index).msi_state <= MSI_INVALID;
                    cache_mem(hit_index).valid <= '0';
                end if;
            end if;
            
            -- Main CPU state machine
            case cpu_state is
                when CPU_IDLE =>
                    cycle_counter <= cycle_counter + 1;
                    
                    -- Simple test pattern - MODIFIED FOR READ TEST
                    if cycle_counter = 3 then
                        cpu_state <= CPU_READ;
                        current_address <= wantedAddress;
                        operation_type <= '0'; -- read
                        cpu_rd_req_out <= '1';
                        cpu_req_addr_out <= wantedAddress;
                        cache_state <= CACHE_CHECK;
                        cycle_counter <= 0;
                    elsif cycle_counter = 8 then
                        cpu_state <= CPU_WRITE;
                        current_address <= wantedAddress;
                        current_data <= x"DEADBEEF";
                        operation_type <= '1'; -- write
                        cpu_wr_req_out <= '1';
                        cpu_req_addr_out <= wantedAddress;
                        cache_state <= CACHE_CHECK;
                        cycle_counter <= 0;
                    end if;
                
                when CPU_READ | CPU_WRITE =>
                    case cache_state is
                        when CACHE_CHECK =>
                            hit_index := find_cache_line(current_address, cache_mem);
                            if hit_index >= 0 and cache_mem(hit_index).msi_state /= MSI_INVALID then
                                -- Cache hit
                                cache_hit_flag <= '1';
                                cache_hit_index <= hit_index;
                                cache_state <= CACHE_HIT;
                            else
                                -- Cache miss
                                cache_hit_flag <= '0';
                                cache_state <= CACHE_MISS;
                            end if;
                        
                        when CACHE_HIT =>
                            if operation_type = '0' then
                                -- Read hit - return data
                                cpu_state <= CPU_IDLE;
                                cpu_rd_req_out <= '0';
                                cache_state <= CACHE_CHECK;
                            else
                                -- Write hit - update data and set modified
                                cache_mem(cache_hit_index).data <= current_data;
                                cache_mem(cache_hit_index).msi_state <= MSI_MODIFIED;
                                cpu_state <= CPU_IDLE;
                                cpu_wr_req_out <= '0';
                                cache_state <= CACHE_CHECK;
                            end if;
                        
                        when CACHE_MISS =>
                            -- Try cache-to-cache transfer first
                            cache_to_cache_req_out <= '1';
                            cache_to_cache_req_address_out <= current_address;
                            cache_state <= CACHE_COHERENCE;
                        
                        when CACHE_COHERENCE =>
                            if cache_to_cache_resp_in_ready = '1' then
                                if cache_to_cache_resp_in = '1' then
                                    -- Cache-to-cache hit
                                    empty_index := find_empty_line(cache_mem);
                                    if empty_index >= 0 then
                                        -- Use empty line
                                        cache_mem(empty_index).valid <= '1';
                                        cache_mem(empty_index).address <= current_address;
                                        cache_mem(empty_index).data <= cache_to_cache_resp_in_data;
                                        if operation_type = '0' then
                                            cache_mem(empty_index).msi_state <= MSI_SHARED;
                                        else
                                            cache_mem(empty_index).msi_state <= MSI_MODIFIED;
                                            cache_mem(empty_index).data <= current_data;
                                        end if;
                                    else
                                        -- Evict using round-robin
                                        if cache_mem(evict_index).msi_state = MSI_MODIFIED then
                                            -- Write back to SDRAM
                                            write_en <= '1';
                                            Sdram_addr <= cache_mem(evict_index).address;
                                            Sdram_data_out <= cache_mem(evict_index).data;
                                        end if;
                                        cache_mem(evict_index).valid <= '1';
                                        cache_mem(evict_index).address <= current_address;
                                        cache_mem(evict_index).data <= cache_to_cache_resp_in_data;
                                        if operation_type = '0' then
                                            cache_mem(evict_index).msi_state <= MSI_SHARED;
                                        else
                                            cache_mem(evict_index).msi_state <= MSI_MODIFIED;
                                            cache_mem(evict_index).data <= current_data;
                                        end if;
                                        evict_index <= (evict_index + 1) mod CACHE_SIZE;
                                    end if;
                                    cpu_state <= CPU_IDLE;
                                    if operation_type = '0' then
                                        cpu_rd_req_out <= '0';
                                    else
                                        cpu_wr_req_out <= '0';
                                    end if;
                                    cache_state <= CACHE_CHECK;
                                else
                                    -- Cache-to-cache miss, go to SDRAM
                                    cache_state <= CACHE_SDRAM_ACCESS;
                                end if;
                            end if;
                        
                        when CACHE_SDRAM_ACCESS =>
                            if operation_type = '0' then
                                read_en <= '1';
                            else
                                write_en <= '1';
                                Sdram_data_out <= current_data;
                            end if;
                            Sdram_addr <= current_address;
                            
                            -- Allocate cache line
                            empty_index := find_empty_line(cache_mem);
                            if empty_index >= 0 then
                                cache_mem(empty_index).valid <= '1';
                                cache_mem(empty_index).address <= current_address;
                                if operation_type = '0' then
                                    cache_mem(empty_index).data <= Sdram_data_in;
                                    cache_mem(empty_index).msi_state <= MSI_SHARED;
                                else
                                    cache_mem(empty_index).data <= current_data;
                                    cache_mem(empty_index).msi_state <= MSI_MODIFIED;
                                end if;
                            else
                                -- Evict using round-robin
                                if cache_mem(evict_index).msi_state = MSI_MODIFIED then
                                    write_en <= '1';
                                    Sdram_addr <= cache_mem(evict_index).address;
                                    Sdram_data_out <= cache_mem(evict_index).data;
                                end if;
                                cache_mem(evict_index).valid <= '1';
                                cache_mem(evict_index).address <= current_address;
                                if operation_type = '0' then
                                    cache_mem(evict_index).data <= Sdram_data_in;
                                    cache_mem(evict_index).msi_state <= MSI_SHARED;
                                else
                                    cache_mem(evict_index).data <= current_data;
                                    cache_mem(evict_index).msi_state <= MSI_MODIFIED;
                                end if;
                                evict_index <= (evict_index + 1) mod CACHE_SIZE;
                            end if;
                            
                            cpu_state <= CPU_IDLE;
                            if operation_type = '0' then
                                cpu_rd_req_out <= '0';
                            else
                                cpu_wr_req_out <= '0';
                            end if;
                            cache_state <= CACHE_CHECK;
                    end case;
                
                when others =>
                    cpu_state <= CPU_IDLE;
            end case;
        end if;
    end process;

end Behavioral;

// VHDL entity sdram, as the project stores it:
library ieee;
use ieee.std_logic_1164.all;
use ieee.numeric_std.all;

entity sdram is
    port(
        clk        : in  std_logic;
        reset      : in  std_logic;
        operation1 : in  std_logic;                     -- 0=read, 1=write on port1
        operation2 : in  std_logic;                     -- 0=read, 1=write on port2
        ready1     : in  std_logic;                     -- handshake from CPU1
        ready2     : in  std_logic;                     -- handshake from CPU2
        addr1      : in  std_logic_vector(2 downto 0);
        addr2      : in  std_logic_vector(2 downto 0);
        data_in1   : in  std_logic_vector(31 downto 0); -- CPU→SDRAM data
        data_in2   : in  std_logic_vector(31 downto 0);
        data_out1  : out std_logic_vector(31 downto 0); -- SDRAM→CPU data
        data_out2  : out std_logic_vector(31 downto 0)
    );
end sdram;

architecture Behavioral of sdram is
    type memory_array is array (0 to 7) of std_logic_vector(31 downto 0);
    signal memory : memory_array;
begin
    process(clk, reset)
    begin
        if reset = '1' then
            -- Initialize memory with test pattern
            memory(0) <= x"00000000";
            memory(1) <= x"11111111";
            memory(2) <= x"22222222";
            memory(3) <= x"33333333";
            memory(4) <= x"44444444";
            memory(5) <= x"55555555";
            memory(6) <= x"66666666";
            memory(7) <= x"77777777";
        elsif rising_edge(clk) then
            -- Port 1 operations
            if ready1 = '1' then
                if operation1 = '1' then
                    -- Write
                    memory(to_integer(unsigned(addr1))) <= data_in1;
                else
                    -- Read
                    data_out1 <= memory(to_integer(unsigned(addr1)));
                end if;
            end if;
            
            -- Port 2 operations
            if ready2 = '1' then
                if operation2 = '1' then
                    -- Write
                    memory(to_integer(unsigned(addr2))) <= data_in2;
                else
                    -- Read
                    data_out2 <= memory(to_integer(unsigned(addr2)));
                end if;
            end if;
        end if;
    end process;
end Behavioral;
