// Logisim project Cache.circ as structural Verilog: 8 circuits, main circuit Cache 32KB
module Main_Architecture (
  input  [31:0] CPU_Address,
  input  CPU_write,
  input  CPU_request,
  input  [31:0] Data_write,
  output [31:0] Data_read,
  output cache_ready
);

  wire cache_32kb_1_request_to_ram, cache_32kb_1_write_to_ram, clock_1_out, n64_mb_ram_1_ready_busy_;
  wire [5:0] cache_32kb_1_address_to_ram_2;
  wire [25:0] cache_32kb_1_address_to_ram;
  wire [31:0] cache_32kb_1_data_to_ram, n64_mb_ram_1_data_out;

  Clock clock_1 (.out(clock_1_out));
  Cache_32KB cache_32kb_1 (
    .Address_from_CPU(CPU_Address), .CPU_data_read(Data_read), .CPU_data_write(Data_write),
    .CPU_query(CPU_request), .CPU_write(CPU_write), .data_to_RAM(cache_32kb_1_data_to_ram),
    .data_from_RAM(n64_mb_ram_1_data_out), .clk(clock_1_out), .write_to_RAM(cache_32kb_1_write_to_ram),
    .Address_to_RAM({cache_32kb_1_address_to_ram_2, cache_32kb_1_address_to_ram}),
    .RAM_ready(n64_mb_ram_1_ready_busy_), .request_to_RAM(cache_32kb_1_request_to_ram),
    .cache_ready(cache_ready));
  _64_MB_RAM u_64_mb_ram_1 (
    .Address(cache_32kb_1_address_to_ram), .Data_in(cache_32kb_1_data_to_ram),
    .Data_out(n64_mb_ram_1_data_out), .clk(clock_1_out), .resquest(cache_32kb_1_request_to_ram),
    .write(cache_32kb_1_write_to_ram), .ready_busy_(n64_mb_ram_1_ready_busy_));

  // Notes on the sheet:
  //   request to RAM
  //   write to RAM
  //   RAM ready
  //   address
  //   read from RAM
endmodule

module Cache_32KB (
  input  clk,
  input  CPU_write,
  input  CPU_query,
  input  [31:0] Address_from_CPU,
  input  [31:0] CPU_data_write,
  input  [31:0] data_from_RAM,
  input  RAM_ready,
  output [31:0] CPU_data_read,
  output request_to_RAM,
  output [31:0] Address_to_RAM,
  output [31:0] data_to_RAM,
  output write_to_RAM,
  output cache_ready
);

  wire and_4_out, and_6_out, cache_controller_fsm_1_finishing, cache_not_ready, comparator_1_eq,
       comparator_2_eq, comparator_3_gt, copy_from_RAM, copy_to_RAM, D0, D1, Hit, Hit0, Hit1, loader_ready,
       loader_request_to_RAM, miss, multiplexer_2_out, multiplexer_6_out, multiplexer_12_out, or_3_out,
       start_line_loader, start_line_storer, storer_ready, storer_request_to_RAM, way, Word0_write,
       Word1_write, Word2_write, Word3_write, Word4_write, Word5_write, Word6_write, Word7_write,
       Word8_write, Word9_write, Word10_write, Word11_write, Word12_write, Word13_write, Word14_write,
       Word15_write, write_new_line, write_new_tag, write_while_finishing;
  wire [3:0] line_loader_offset, line_storer_offset, multiplexer_3_out, multiplexer_5_out;
  wire [19:0] Set0_D_U_V_tag, Set1_D_U_V_tag;
  wire [20:0] multiplexer_7_out, new_Set0_tag, new_Set1_tag;
  wire [31:0] loader_address, multiplexer_1_out, register_1_q, storer_address, Word0_read, Word1_read,
       Word2_read, Word3_read, Word4_read, Word5_read, Word6_read, Word7_read, Word8_read, Word9_read,
       Word10_read, Word11_read, Word12_read, Word13_read, Word14_read, Word15_read;

  or or_1 (Hit, Hit1, Hit0);
  Multiplexer #(.width(32), .enable("false")) multiplexer_1 (
    .in0(CPU_data_write), .in1(data_from_RAM), .out(multiplexer_1_out), .sel(copy_from_RAM));
  Comparator #(.width(18), .mode("unsigned")) comparator_1 (
    .a(Address_from_CPU[31:14]), .b(Set0_D_U_V_tag[17:0]), .eq(comparator_1_eq));  // open: gt, lt
  Comparator #(.width(18), .mode("unsigned")) comparator_2 (
    .a(Address_from_CPU[31:14]), .b(Set1_D_U_V_tag[17:0]), .eq(comparator_2_eq));  // open: gt, lt
  and and_1 (Hit1, Set1_D_U_V_tag[18], comparator_2_eq);
  and and_2 (Hit0, comparator_1_eq, Set0_D_U_V_tag[18]);
  RAM #(.dataWidth(21), .bus("separate")) ram_1 (
    .addr(Address_from_CPU[13:6]), .din(new_Set0_tag), .data({D0, Set0_D_U_V_tag}), .str(write_new_tag),
    .clk(clk));  // open: sel, ld, clr
  RAM #(.dataWidth(21), .bus("separate")) ram_2 (
    .addr(Address_from_CPU[13:6]), .din(new_Set1_tag), .data({D1, Set1_D_U_V_tag}), .str(write_new_tag),
    .clk(clk));  // open: sel, ld, clr
  and and_3 (miss, CPU_query, ~Hit, cache_ready);  // AND_Gate
  and and_4 (and_4_out, Hit, CPU_query, cache_ready);
  or or_2 (write_new_tag, and_4_out, miss);
  RAM #(.dataWidth(32), .bus("separate")) ram_3 (
    .addr(Address_from_CPU[13:6]), .din(multiplexer_1_out), .data(Word15_read), .str(Word15_write),
    .sel(multiplexer_12_out), .clk(clk), .ld(1'b1));  // open: clr
  RAM #(.dataWidth(32), .bus("separate")) ram_4 (
    .addr(Address_from_CPU[13:6]), .din(multiplexer_1_out), .data(Word15_read), .str(Word15_write),
    .sel(way), .clk(clk), .ld(1'b1));  // open: clr
  Multiplexer #(.enable("false")) multiplexer_2 (.in0(D0), .in1(D1), .out(multiplexer_2_out), .sel(way));
  RAM #(.dataWidth(32), .bus("separate")) ram_5 (
    .addr(Address_from_CPU[13:6]), .din(multiplexer_1_out), .data(Word14_read), .str(Word14_write),
    .sel(multiplexer_12_out), .clk(clk), .ld(1'b1));  // open: clr
  RAM #(.dataWidth(32), .bus("separate")) ram_6 (
    .addr(Address_from_CPU[13:6]), .din(multiplexer_1_out), .data(Word14_read), .str(Word14_write),
    .sel(way), .clk(clk), .ld(1'b1));  // open: clr
  Cache_controller_FSM cache_controller_fsm_1 (
    .start_when_miss(miss), .dirty(multiplexer_2_out), .store_ready(storer_ready), .load_ready(loader_ready),
    .start_store(start_line_storer), .start_load(start_line_loader), .clk(clk), .cache_ready(cache_ready),
    .finishing(cache_controller_fsm_1_finishing));
  RAM #(.dataWidth(32), .bus("separate")) ram_7 (
    .addr(Address_from_CPU[13:6]), .din(multiplexer_1_out), .data(Word13_read), .str(Word13_write),
    .sel(multiplexer_12_out), .clk(clk), .ld(1'b1));  // open: clr
  RAM #(.dataWidth(32), .bus("separate")) ram_8 (
    .addr(Address_from_CPU[13:6]), .din(multiplexer_1_out), .data(Word13_read), .str(Word13_write),
    .sel(way), .clk(clk), .ld(1'b1));  // open: clr
  not not_1 (cache_not_ready, cache_ready);
  Multiplexer #(.width(4), .enable("false")) multiplexer_3 (
    .in0(Address_from_CPU[5:2]), .in1(line_storer_offset), .out(multiplexer_3_out), .sel(copy_to_RAM));
  and and_5 (write_while_finishing, cache_controller_fsm_1_finishing, multiplexer_2_out);
  RAM #(.dataWidth(32), .bus("separate")) ram_9 (
    .addr(Address_from_CPU[13:6]), .din(multiplexer_1_out), .data(Word12_read), .str(Word12_write),
    .sel(multiplexer_12_out), .clk(clk), .ld(1'b1));  // open: clr
  RAM #(.dataWidth(32), .bus("separate")) ram_10 (
    .addr(Address_from_CPU[13:6]), .din(multiplexer_1_out), .data(Word12_read), .str(Word12_write),
    .sel(way), .clk(clk), .ld(1'b1));  // open: clr
  Multiplexer #(.select(4), .width(32), .enable("false")) multiplexer_4 (
    .in0(Word0_read), .in1(Word1_read), .in2(Word2_read), .in3(Word3_read), .in4(Word4_read),
    .in5(Word5_read), .in6(Word6_read), .in7(Word7_read), .in8(Word8_read), .in9(Word9_read),
    .in10(Word10_read), .in11(Word11_read), .in12(Word12_read), .in13(Word13_read), .in14(Word14_read),
    .in15(Word15_read), .out(CPU_data_read), .sel(multiplexer_3_out));
  RAM #(.dataWidth(32), .bus("separate")) ram_11 (
    .addr(Address_from_CPU[13:6]), .din(multiplexer_1_out), .data(Word11_read), .str(Word11_write),
    .sel(multiplexer_12_out), .clk(clk), .ld(1'b1));  // open: clr
  RAM #(.dataWidth(32), .bus("separate")) ram_12 (
    .addr(Address_from_CPU[13:6]), .din(multiplexer_1_out), .data(Word11_read), .str(Word11_write),
    .sel(way), .clk(clk), .ld(1'b1));  // open: clr
  not not_2 (copy_from_RAM, loader_ready);
  RAM #(.dataWidth(32), .bus("separate")) ram_13 (
    .addr(Address_from_CPU[13:6]), .din(multiplexer_1_out), .data(Word10_read), .str(Word10_write),
    .sel(multiplexer_12_out), .clk(clk), .ld(1'b1));  // open: clr
  RAM #(.dataWidth(32), .bus("separate")) ram_14 (
    .addr(Address_from_CPU[13:6]), .din(multiplexer_1_out), .data(Word10_read), .str(Word10_write),
    .sel(way), .clk(clk), .ld(1'b1));  // open: clr
  Line_Loader line_loader_1 (
    .address_to_RAM(loader_address), .RAM_ready(RAM_ready), .request_to_RAM(loader_request_to_RAM),
    .clk(clk), .start_loading(start_line_loader), .\address_from_CÜ (Address_from_CPU),
    .write_to_cache(write_new_line), .loader_ready(loader_ready), .offset(line_loader_offset));
  Multiplexer #(.width(4), .enable("false")) multiplexer_5 (
    .in0(multiplexer_3_out), .in1(line_loader_offset), .out(multiplexer_5_out), .sel(copy_from_RAM));
  RAM #(.dataWidth(32), .bus("separate")) ram_15 (
    .addr(Address_from_CPU[13:6]), .din(multiplexer_1_out), .data(Word9_read), .str(Word9_write),
    .sel(multiplexer_12_out), .clk(clk), .ld(1'b1));  // open: clr
  RAM #(.dataWidth(32), .bus("separate")) ram_16 (
    .addr(Address_from_CPU[13:6]), .din(multiplexer_1_out), .data(Word9_read), .str(Word9_write), .sel(way),
    .clk(clk), .ld(1'b1));  // open: clr
  and and_6 (and_6_out, CPU_write, Hit);
  RAM #(.dataWidth(32), .bus("separate")) ram_17 (
    .addr(Address_from_CPU[13:6]), .din(multiplexer_1_out), .data(Word8_read), .str(Word8_write),
    .sel(multiplexer_12_out), .clk(clk), .ld(1'b1));  // open: clr
  RAM #(.dataWidth(32), .bus("separate")) ram_18 (
    .addr(Address_from_CPU[13:6]), .din(multiplexer_1_out), .data(Word8_read), .str(Word8_write), .sel(way),
    .clk(clk), .ld(1'b1));  // open: clr
  Decoder #(.select(4), .disabled(0)) decoder_1 (
    .out0(Word0_write), .out1(Word1_write), .out2(Word2_write), .out3(Word3_write), .out4(Word4_write),
    .out5(Word5_write), .out6(Word6_write), .out7(Word7_write), .out8(Word8_write), .out9(Word9_write),
    .out10(Word10_write), .out11(Word11_write), .out12(Word12_write), .out13(Word13_write),
    .out14(Word14_write), .out15(Word15_write), .sel(multiplexer_5_out), .en(multiplexer_6_out));
  Multiplexer #(.enable("false")) multiplexer_6 (
    .in0(and_6_out), .in1(or_3_out), .out(multiplexer_6_out), .sel(cache_not_ready));
  or or_3 (or_3_out, write_new_line, write_while_finishing);
  Multiplexer #(.width(21), .enable("false")) multiplexer_7 (
    .in0({D0, Set0_D_U_V_tag}), .in1({D1, Set1_D_U_V_tag}), .out(multiplexer_7_out), .sel(way));
  RAM #(.dataWidth(32), .bus("separate")) ram_19 (
    .addr(Address_from_CPU[13:6]), .din(multiplexer_1_out), .data(Word7_read), .str(Word7_write),
    .sel(multiplexer_12_out), .clk(clk), .ld(1'b1));  // open: clr
  RAM #(.dataWidth(32), .bus("separate")) ram_20 (
    .addr(Address_from_CPU[13:6]), .din(multiplexer_1_out), .data(Word7_read), .str(Word7_write), .sel(way),
    .clk(clk), .ld(1'b1));  // open: clr
  RAM #(.dataWidth(32), .bus("separate")) ram_21 (
    .addr(Address_from_CPU[13:6]), .din(multiplexer_1_out), .data(Word6_read), .str(Word6_write),
    .sel(multiplexer_12_out), .clk(clk), .ld(1'b1));  // open: clr
  RAM #(.dataWidth(32), .bus("separate")) ram_22 (
    .addr(Address_from_CPU[13:6]), .din(multiplexer_1_out), .data(Word6_read), .str(Word6_write), .sel(way),
    .clk(clk), .ld(1'b1));  // open: clr
  not not_3 (copy_to_RAM, storer_ready);
  Line_Storer line_storer_1 (
    .address_to_RAM(storer_address), .RAM_ready(RAM_ready), .request_to_RAM(storer_request_to_RAM),
    .clk(clk), .start_storing(start_line_storer), .\address_from_CÜ (register_1_q),
    .write_to_RAM(write_to_RAM), .storer_ready(storer_ready), .offset(line_storer_offset));
  Register #(.width(32)) register_1 (
    .D({multiplexer_7_out[17:0], Address_from_CPU[13:2], 2'b00}), .en(start_line_storer), .Q(register_1_q),
    .clk(clk));  // open: clr
  RAM #(.dataWidth(32), .bus("separate")) ram_23 (
    .addr(Address_from_CPU[13:6]), .din(multiplexer_1_out), .data(Word5_read), .str(Word5_write),
    .sel(multiplexer_12_out), .clk(clk), .ld(1'b1));  // open: clr
  RAM #(.dataWidth(32), .bus("separate")) ram_24 (
    .addr(Address_from_CPU[13:6]), .din(multiplexer_1_out), .data(Word5_read), .str(Word5_write), .sel(way),
    .clk(clk), .ld(1'b1));  // open: clr
  Multiplexer #(.width(21), .enable("false")) multiplexer_8 (
    .in0({D1, 1'b0, Set1_D_U_V_tag[18:0]}), .in1({CPU_write, 2'b11, Address_from_CPU[31:14]}),
    .out(new_Set1_tag), .sel(way));
  RAM #(.dataWidth(32), .bus("separate")) ram_25 (
    .addr(Address_from_CPU[13:6]), .din(multiplexer_1_out), .data(Word4_read), .str(Word4_write),
    .sel(multiplexer_12_out), .clk(clk), .ld(1'b1));  // open: clr
  RAM #(.dataWidth(32), .bus("separate")) ram_26 (
    .addr(Address_from_CPU[13:6]), .din(multiplexer_1_out), .data(Word4_read), .str(Word4_write), .sel(way),
    .clk(clk), .ld(1'b1));  // open: clr
  RAM #(.dataWidth(32), .bus("separate")) ram_27 (
    .addr(Address_from_CPU[13:6]), .din(multiplexer_1_out), .data(Word3_read), .str(Word3_write),
    .sel(multiplexer_12_out), .clk(clk), .ld(1'b1));  // open: clr
  RAM #(.dataWidth(32), .bus("separate")) ram_28 (
    .addr(Address_from_CPU[13:6]), .din(multiplexer_1_out), .data(Word3_read), .str(Word3_write), .sel(way),
    .clk(clk), .ld(1'b1));  // open: clr
  RAM #(.dataWidth(32), .bus("separate")) ram_29 (
    .addr(Address_from_CPU[13:6]), .din(multiplexer_1_out), .data(Word2_read), .str(Word2_write),
    .sel(multiplexer_12_out), .clk(clk), .ld(1'b1));  // open: clr
  RAM #(.dataWidth(32), .bus("separate")) ram_30 (
    .addr(Address_from_CPU[13:6]), .din(multiplexer_1_out), .data(Word2_read), .str(Word2_write), .sel(way),
    .clk(clk), .ld(1'b1));  // open: clr
  Multiplexer #(.width(21), .enable("false")) multiplexer_9 (
    .in0({CPU_write, 2'b11, Address_from_CPU[31:14]}), .in1({D0, 1'b0, Set0_D_U_V_tag[18:0]}),
    .out(new_Set0_tag), .sel(way));
  Multiplexer #(.enable("false")) multiplexer_10 (
    .in0(loader_request_to_RAM), .in1(storer_request_to_RAM), .out(request_to_RAM), .sel(copy_to_RAM));
  Multiplexer #(.width(32), .enable("false")) multiplexer_11 (
    .in0(loader_address), .in1(storer_address), .out(Address_to_RAM), .sel(copy_to_RAM));
  RAM #(.dataWidth(32), .bus("separate")) ram_31 (
    .addr(Address_from_CPU[13:6]), .din(multiplexer_1_out), .data(Word1_read), .str(Word1_write),
    .sel(multiplexer_12_out), .clk(clk), .ld(1'b1));  // open: clr
  RAM #(.dataWidth(32), .bus("separate")) ram_32 (
    .addr(Address_from_CPU[13:6]), .din(multiplexer_1_out), .data(Word1_read), .str(Word1_write), .sel(way),
    .clk(clk), .ld(1'b1));  // open: clr
  RAM #(.dataWidth(32), .bus("separate")) ram_33 (
    .addr(Address_from_CPU[13:6]), .din(multiplexer_1_out), .data(Word0_read), .str(Word0_write),
    .sel(multiplexer_12_out), .clk(clk), .ld(1'b1));  // open: clr
  RAM #(.dataWidth(32), .bus("separate")) ram_34 (
    .addr(Address_from_CPU[13:6]), .din(multiplexer_1_out), .data(Word0_read), .str(Word0_write), .sel(way),
    .clk(clk), .ld(1'b1));  // open: clr
  Comparator #(.width(2), .mode("unsigned")) comparator_3 (
    .a({Set1_D_U_V_tag[18], Set1_D_U_V_tag[19]}), .b({Set0_D_U_V_tag[18], Set0_D_U_V_tag[19]}),
    .gt(comparator_3_gt));  // open: eq, lt
  Multiplexer #(.enable("false")) multiplexer_12 (
    .in0(comparator_3_gt), .in1(Hit0), .out(multiplexer_12_out), .sel(Hit));
  not not_4 (way, multiplexer_12_out);

  assign data_to_RAM = CPU_data_read;

  // Other names for the same wires on the sheet: address[31:0] = Address_from_CPU;
  //   offset[3:0] = Address_from_CPU[5:2]; set[7:0] = Address_from_CPU[13:6]; Set1_D_U_V_tag[20] = D1;
  //   tag[17:0] = Address_from_CPU[31:14]; U1 = Set1_D_U_V_tag[19]; V1 = Set1_D_U_V_tag[18]; U0 = Set0_D_U_V_tag[19];
  //   V0 = Set0_D_U_V_tag[18]; return_word[31:0] = CPU_data_read; Set0_D_U_V_tag[20] = D0

  // Notes on the sheet:
  //   set0 tag
  //   set1 tag
  //   tag
  //   Set
  //   Offset
  //   Register to save the storing address
endmodule

// RAM 64 MB
module _64_MB_RAM (
  input  clk,
  input  resquest,
  input  write,
  input  [25:0] Address,
  input  [31:0] Data_in,
  output [31:0] Data_out,
  output ready_busy_
);

  wire and_1_out, buffer, comparator_1_eq, comparator_1_lt, d_ff_1_q, d_ff_2_q, or_1_out;
  wire [3:0] counter_1_q;
  wire [23:0] register_1_q;
  wire [31:0] ram_1_data, register_2_q;

  Register #(.width(24)) register_1 (.D(Address[25:2]), .en(buffer), .Q(register_1_q), .clk(clk));  // open: clr
  Register #(.width(32)) register_2 (.D(Data_in), .en(buffer), .Q(register_2_q), .clk(clk));  // open: clr
  Counter #(.width(4), .max('hf)) counter_1 (
    .Q(counter_1_q), .clk(clk), .clr(ready_busy_));  // open: load, D, count, carry
  Comparator #(.width(4), .mode("unsigned")) comparator_1 (
    .a(counter_1_q), .b(4'b1001), .eq(comparator_1_eq), .lt(comparator_1_lt));  // open: gt
  D_Flip_Flop d_ff_1 (.clk(clk), .D(write), .Q(d_ff_1_q), .en(buffer));  // open: Qn, preset, reset
  or or_1 (or_1_out, resquest, d_ff_2_q);
  and and_1 (and_1_out, or_1_out, comparator_1_lt);
  D_Flip_Flop d_ff_2 (.clk(clk), .D(and_1_out), .Q(d_ff_2_q), .Qn(ready_busy_));  // open: preset, en, reset
  RAM #(.addrWidth(24), .dataWidth(32), .bus("separate")) ram_1 (
    .addr(register_1_q), .din(register_2_q), .data(ram_1_data), .str(d_ff_1_q), .clk(clk), .ld(1'b1));  // open: sel, clr
  Register #(.width(32)) register_3 (.D(ram_1_data), .en(comparator_1_eq), .Q(Data_out), .clk(clk));  // open: clr
  and and_2 (buffer, resquest, ready_busy_);

  // Notes on the sheet:
  //   Reg
  //   Reg
  //   Count to 10
  //   DFF
  //   State DFF
  //   Ready/Busy
  //   RAM
  //   16M x 32bit
  //   Reg
endmodule

module Line_Loader (
  input  start_loading,
  input  clk,
  input  [31:0] \address_from_CÜ ,
  input  RAM_ready,
  output [31:0] address_to_RAM,
  output request_to_RAM,
  output write_to_cache,
  output loader_ready,
  output [3:0] offset
);

  wire comparator_1_eq, loader_control_fsm_1_increment_counter;

  Loader_Control_FSM loader_control_fsm_1 (
    .start_loading(start_loading), .RAM_ready(RAM_ready), .count_equal_zero(comparator_1_eq),
    .cache_ready(loader_ready), .request_to_RAM(request_to_RAM), .write_in_cache(write_to_cache),
    .increment_counter(loader_control_fsm_1_increment_counter), .clk(clk));
  Counter #(.width(4), .max('hf)) counter_1 (
    .count(loader_control_fsm_1_increment_counter), .Q(address_to_RAM[5:2]), .clk(clk));  // open: load, D, carry, clr
  Comparator #(.width(4)) comparator_1 (.a(address_to_RAM[5:2]), .b(4'b1111), .eq(comparator_1_eq));  // open: gt, lt

  assign {address_to_RAM[31:6], address_to_RAM[1:0]} = {\address_from_CÜ [31:6], 2'b00};
  assign offset = address_to_RAM[5:2];

  // Notes on the sheet:
  //   Loader
  //   FSM
endmodule

// Control
module Loader_Control_FSM (
  input  clk,
  input  start_loading,
  input  RAM_ready,
  input  count_equal_zero,
  output cache_ready,
  output request_to_RAM,
  output write_in_cache,
  output increment_counter
);

  wire and_1_out, and_2_out, and_3_out, and_4_out, and_5_out, and_6_out, not_1_out, not_2_out, not_3_out,
       or_1_out, or_2_out, S0_q, S0_qn, S1_q, S1_qn;

  not not_1 (not_1_out, count_equal_zero);
  not not_2 (not_2_out, start_loading);
  not not_3 (not_3_out, RAM_ready);
  and and_1 (and_1_out, S1_qn, S0_q, RAM_ready);
  and and_2 (and_2_out, S1_q, S0_qn);
  and and_3 (and_3_out, S1_qn, S0_qn, start_loading);
  and and_4 (and_4_out, S1_qn, S0_q, not_3_out);
  and and_5 (and_5_out, S1_q, S0_qn, RAM_ready);
  and and_6 (and_6_out, S1_q, S0_q, not_1_out);
  or or_1 (or_1_out, and_1_out, and_2_out);
  or or_2 (or_2_out, and_3_out, and_4_out, and_5_out, and_6_out);
  D_Flip_Flop S1 (.clk(clk), .D(or_1_out), .Q(S1_q), .Qn(S1_qn));  // open: preset, en, reset
  D_Flip_Flop S0 (.clk(clk), .D(or_2_out), .Q(S0_q), .Qn(S0_qn));  // open: preset, en, reset
  and and_7 (cache_ready, S0_qn, S1_qn);
  and and_8 (request_to_RAM, S1_qn, S0_q);
  and and_9 (increment_counter, S1_q, S0_q);

  assign write_in_cache = increment_counter;
endmodule

module Line_Storer (
  input  start_storing,
  input  clk,
  input  [31:0] \address_from_CÜ ,
  input  RAM_ready,
  output [31:0] address_to_RAM,
  output request_to_RAM,
  output write_to_RAM,
  output storer_ready,
  output [3:0] offset
);

  wire comparator_1_eq, store_control_fsm_1_increment_counter;

  Store_Control_FSM store_control_fsm_1 (
    .start_loading(start_storing), .RAM_ready(RAM_ready), .count_equal_zero(comparator_1_eq),
    .cache_ready(storer_ready), .request_to_RAM(request_to_RAM), .write_in_RAM(write_to_RAM),
    .increment_counter(store_control_fsm_1_increment_counter), .clk(clk));
  Counter #(.width(4), .max('hf)) counter_1 (
    .count(store_control_fsm_1_increment_counter), .Q(address_to_RAM[5:2]), .clk(clk));  // open: load, D, carry, clr
  Comparator #(.width(4)) comparator_1 (.a(address_to_RAM[5:2]), .b(4'b1111), .eq(comparator_1_eq));  // open: gt, lt

  assign {address_to_RAM[31:6], address_to_RAM[1:0]} = {\address_from_CÜ [31:6], 2'b00};
  assign offset = address_to_RAM[5:2];

  // Notes on the sheet:
  //   Storer
  //   FSM
endmodule

// Control
module Store_Control_FSM (
  input  clk,
  input  start_loading,
  input  RAM_ready,
  input  count_equal_zero,
  output cache_ready,
  output request_to_RAM,
  output write_in_RAM,
  output increment_counter
);

  wire and_1_out, and_2_out, and_3_out, and_4_out, and_5_out, and_6_out, not_1_out, not_2_out, not_3_out,
       or_1_out, or_2_out, S0_q, S0_qn, S1_q, S1_qn;

  not not_1 (not_1_out, RAM_ready);
  not not_2 (not_2_out, count_equal_zero);
  not not_3 (not_3_out, start_loading);
  and and_1 (and_1_out, S1_qn, S0_q, RAM_ready);
  and and_2 (and_2_out, S1_q, S0_qn);
  and and_3 (and_3_out, S1_qn, S0_qn, start_loading);
  and and_4 (and_4_out, S1_qn, S0_q, not_1_out);
  and and_5 (and_5_out, S1_q, S0_qn, RAM_ready);
  and and_6 (and_6_out, S1_q, S0_q, not_2_out);
  or or_1 (or_1_out, and_1_out, and_2_out);
  or or_2 (or_2_out, and_3_out, and_4_out, and_5_out, and_6_out);
  D_Flip_Flop S1 (.clk(clk), .D(or_1_out), .Q(S1_q), .Qn(S1_qn));  // open: preset, en, reset
  D_Flip_Flop S0 (.clk(clk), .D(or_2_out), .Q(S0_q), .Qn(S0_qn));  // open: preset, en, reset
  and and_7 (cache_ready, S0_qn, S1_qn);
  and and_8 (request_to_RAM, S1_qn, S0_q);
  and and_9 (increment_counter, S1_q, S0_q);

  assign write_in_RAM = request_to_RAM;
endmodule

// Cache Controller
module Cache_controller_FSM (
  input  clk,
  input  start_when_miss,
  input  dirty,
  input  store_ready,
  input  load_ready,
  output start_store,
  output start_load,
  output cache_ready,
  output finishing
);

  wire and_1_out, and_2_out, and_3_out, and_4_out, and_5_out, and_7_out, and_8_out, not_1_out, not_2_out,
       not_3_out, not_4_out, or_1_out, or_2_out, S0_q, S0_qn, S1_q, S1_qn;

  not not_1 (not_1_out, start_when_miss);
  not not_2 (not_2_out, store_ready);
  not not_3 (not_3_out, dirty);
  not not_4 (not_4_out, load_ready);
  and and_1 (and_1_out, S1_qn, S0_qn, start_when_miss, not_3_out);
  and and_2 (and_2_out, S1_qn, S0_q, store_ready);
  and and_3 (and_3_out, S1_q, S0_qn, not_4_out);
  and and_4 (and_4_out, S1_qn, S0_qn, start_when_miss, dirty);
  and and_5 (and_5_out, S1_qn, S0_q, not_2_out);
  or or_1 (or_1_out, and_1_out, and_2_out, and_3_out);
  or or_2 (or_2_out, and_4_out, and_5_out);
  D_Flip_Flop S1 (.clk(clk), .D(or_1_out), .Q(S1_q), .Qn(S1_qn));  // open: preset, en, reset
  D_Flip_Flop S0 (.clk(clk), .D(or_2_out), .Q(S0_q), .Qn(S0_qn));  // open: preset, en, reset
  and and_6 (start_store, S1_qn, S0_qn, start_when_miss, dirty);
  and and_7 (and_7_out, S1_qn, S0_qn, start_when_miss, not_3_out);
  and and_8 (and_8_out, S1_qn, S0_q, store_ready);
  and and_9 (finishing, S1_q, load_ready);
  and and_10 (cache_ready, S1_qn, S0_qn);
  or or_3 (start_load, and_7_out, and_8_out);
endmodule
