// Logisim project mips16_logisim_cpu.circ as structural Verilog: 7 circuits, main circuit main
// Result
module main (
);

  wire bt_1_burbuja, clk, Do_bubble, Do_forwarding, enable_ALU, Enable_ALU_q, enable_LOAD, Enable_LOAD_q,
       enable_LOADI, enable_PC, enable_STORE, Enable_STORE_q, enable_STOREI, enableLOADI_q, enableSTOREI_q,
       execute_1_enable_alu, execute_1_load, execute_1_load_i, execute_1_store, execute_1_store_i,
       Forwarding_op, memory_1_alu, memory_1_enable_load, memory_1_loadi, memory_1_store, memory_1_storei,
       or_1_out;
  wire [3:0] decode_1_destiny, decode_1_inmediato, decode_1_instruction, decode_1_op1, decode_1_op1_second,
       decode_1_op2, decode_1_op2_second, decode_1_pos_mem, decode_1_register, decode_1_rflags, Destino_q,
       Destiny_q, execute_1_dest, execute_1_forward_value, execute_1_inm, execute_1_op_code,
       execute_1_registeroutput, execute_1_resultado, Inmediate_q, Inmediato_q, LOAD_Destiny_q,
       memory_1_destino, memory_1_value, OP1_q, OP2_q, PC_q, pos_mem, POS_MEM_q, POSMEM_q, R_FLAGS_q,
       Register_EXEMEM_q, Registro_q, Result_q, VALUE_q;
  wire [15:0] decode_1_decodes, Decodes_q, OP_code_q, rom_1_data;

  Counter #(.max('hf), .width(4)) PC (
    .load(enable_PC), .D(pos_mem), .Q(PC_q), .up(Do_bubble), .clk(clk));  // open: count, carry, clr
  ROM #(.addrWidth(4), .dataWidth(16)) rom_1 (.addr(PC_q), .data(rom_1_data));
  Clock clock_1 (.out(clk));
  Register #(.width(16)) OP_code (.D(rom_1_data), .en(Do_bubble), .Q(OP_code_q), .clk(clk));  // open: clr
  or or_1 (or_1_out, enable_ALU, enable_LOAD, enable_LOADI);
  Decode decode_1 (
    .Clock(clk), .OP_CODE(OP_code_q), .Enable_write(or_1_out), .Forward_value(execute_1_forward_value),
    .Forward_enable(Do_forwarding), .Forwarding_op(Forwarding_op), .WB_Destiny(LOAD_Destiny_q),
    .WB_value(VALUE_q), .OP1_Second(decode_1_op1_second), .POS_MEM(decode_1_pos_mem),
    .OP2_Second(decode_1_op2_second), .Inmediato(decode_1_inmediato), .Destiny(decode_1_destiny),
    .OP1(decode_1_op1), .Register(decode_1_register), .OP2(decode_1_op2), .RFlags(decode_1_rflags),
    .Instruction(decode_1_instruction), .Decodes(decode_1_decodes));
  Register #(.width(4)) u_POS_MEM (.D(decode_1_pos_mem), .Q(POS_MEM_q), .clk(clk));  // open: en, clr
  Register #(.width(4)) Inmediate (.D(decode_1_inmediato), .Q(Inmediate_q), .clk(clk));  // open: en, clr
  Register #(.width(4)) Destiny (.D(decode_1_destiny), .Q(Destiny_q), .clk(clk));  // open: en, clr
  Register #(.width(4)) Registro (.D(decode_1_register), .Q(Registro_q), .clk(clk));  // open: en, clr
  Register #(.width(4)) OP1 (.D(decode_1_op1), .Q(OP1_q), .clk(clk));  // open: en, clr
  Register #(.width(4)) OP2 (.D(decode_1_op2), .Q(OP2_q), .clk(clk));  // open: en, clr
  Register #(.width(4)) R_FLAGS (.D(decode_1_rflags), .Q(R_FLAGS_q), .clk(clk));  // open: en, clr
  Register #(.width(16)) Decodes (.D(decode_1_decodes), .Q(Decodes_q), .clk(clk));  // open: en, clr
  Execute execute_1 (
    .Decodes(Decodes_q), .POSMEM(POS_MEM_q), .Regsiter(Registro_q), .Inmediato(Inmediate_q),
    .Destino(Destiny_q), .OP1(OP1_q), .OP2(OP2_q), .Function(decode_1_instruction), .clock(clk),
    .Load(execute_1_load), .Load_I(execute_1_load_i), .Store(execute_1_store), .Store_I(execute_1_store_i),
    .Enable_ALU(execute_1_enable_alu), .POS_MEM(pos_mem), .RegisterOutput(execute_1_registeroutput),
    .INM(execute_1_inm), .DEST(execute_1_dest), .Forward_value(execute_1_forward_value),
    .Resultado(execute_1_resultado), .OP_Code(execute_1_op_code), .Enable_PC(enable_PC));
  BT bt_1 (
    .ckl(clk), .OP_code_First(execute_1_dest), .Destiny_First(execute_1_op_code),
    .OP1_Second(decode_1_op1_second), .OP2_Second(decode_1_op2_second), .enable_Forwarding(Do_forwarding),
    .Forwarding_operator(Forwarding_op), .Burbuja(bt_1_burbuja));
  not not_1 (Do_bubble, bt_1_burbuja);
  Register #(.width(4)) POSMEM (.D(pos_mem), .Q(POSMEM_q), .clk(clk));  // open: en, clr
  Register #(.width(4)) Register_EXEMEM (
    .D(execute_1_registeroutput), .Q(Register_EXEMEM_q), .clk(clk));  // open: en, clr
  Register #(.width(4)) Inmediato (.D(execute_1_inm), .Q(Inmediato_q), .clk(clk));  // open: en, clr
  Register #(.width(4)) Destino (.D(execute_1_dest), .Q(Destino_q), .clk(clk));  // open: en, clr
  Register #(.width(4)) Result (.D(execute_1_resultado), .Q(Result_q), .clk(clk));  // open: en, clr
  Register #(.width(1)) u_Enable_LOAD (.D(execute_1_load), .Q(Enable_LOAD_q), .clk(clk));  // open: en, clr
  Register #(.width(1)) enableLOADI (.D(execute_1_load_i), .Q(enableLOADI_q), .clk(clk));  // open: en, clr
  Register #(.width(1)) u_Enable_STORE (.D(execute_1_store), .Q(Enable_STORE_q), .clk(clk));  // open: en, clr
  Register #(.width(1)) enableSTOREI (.D(execute_1_store_i), .Q(enableSTOREI_q), .clk(clk));  // open: en, clr
  Register #(.width(1)) u_Enable_ALU (.D(execute_1_enable_alu), .Q(Enable_ALU_q), .clk(clk));  // open: en, clr
  Memory memory_1 (
    .clock(clk), .LOAD(Enable_LOAD_q), .Enable_LOADI(enableLOADI_q), .Enable_STORE(Enable_STORE_q),
    .Enable_STORE_I(enableSTOREI_q), .Enable_ALU(Enable_ALU_q), .Destiny(Destino_q), .POS_MEM(POSMEM_q),
    .Register(Register_EXEMEM_q), .Inmediato(Inmediato_q), .Result(Result_q),
    .Enable_LOAD(memory_1_enable_load), .LOADI(memory_1_loadi), .STORE(memory_1_store),
    .STOREI(memory_1_storei), .ALU(memory_1_alu), .Value(memory_1_value), .Destino(memory_1_destino));
  Register #(.width(1)) enableLOAD (.D(memory_1_enable_load), .Q(enable_LOAD), .clk(clk));  // open: en, clr
  Register #(.width(1)) Enable_LOAD_I (.D(memory_1_loadi), .Q(enable_LOADI), .clk(clk));  // open: en, clr
  Register #(.width(1)) enableSTORE (.D(memory_1_store), .Q(enable_STORE), .clk(clk));  // open: en, clr
  Register #(.width(1)) Enable_STORE_I (.D(memory_1_storei), .Q(enable_STOREI), .clk(clk));  // open: en, clr
  Register #(.width(1)) enableALU (.D(memory_1_alu), .Q(enable_ALU), .clk(clk));  // open: en, clr
  Register #(.width(4)) LOAD_Destiny (.D(memory_1_destino), .Q(LOAD_Destiny_q), .clk(clk));  // open: en, clr
  Register #(.width(4)) VALUE (.D(memory_1_value), .Q(VALUE_q), .clk(clk));  // open: en, clr

  // Notes on the sheet:
  //   CPU
  //   STOREI 1 0000
  //   LOAD 2 0000
  //   STORE 2 0001
  //   LOADI 0 3
  //   LOADI 1 2
  //   CMP 0 1
  //   BB 2
  //   0100 0000 0001 0000 -> 4010
  //   0001 0010 0000 0000 -> 1200
  //   0010 0000 0010 0001 -> 2021  
  //   0011 0000 0011 0000 -> 3030
  //   0011 0001 0010 0000 -> 3120
  //   0101 0000 0001 0000 -> 5010
  //   0111 0000 0000 0010 -> 7002
  //   contents of rom_1 (hex, n*v repeats v):
  //   3030 3130 0 0 0 5010 7002
  //   FETCH
  //   DECODE
  //   EXECUTE
  //   MEM
  //   WB
endmodule

module ALU (
  input  [3:0] op1,
  input  [3:0] op2,
  input  [3:0] shift_op,
  input  [3:0] \function ,
  output [2:0] cmp,
  output [3:0] result
);

  wire [3:0] adder_1_out, and_1_out, not_1_out, or_1_out, shifter_1_out, subtractor_1_out, xor_1_out;

  Comparator #(.width(4)) comparator_1 (.a(op1), .b(op2), .gt(cmp[0]), .eq(cmp[1]), .lt(cmp[2]));
  assign and_1_out = op1 & op2;  // AND_Gate and_1, 4 bits wide
  assign or_1_out = op1 | op2;  // OR_Gate or_1, 4 bits wide
  assign xor_1_out = op1 ^ op2;  // XOR_Gate xor_1, 4 bits wide
  assign not_1_out = ~op2;  // NOT_Gate not_1, 4 bits wide
  Adder #(.width(4)) adder_1 (.a(op1), .b(op2), .out(adder_1_out));  // open: cin, cout
  Subtractor #(.width(4)) subtractor_1 (.a(op1), .b(op2), .out(subtractor_1_out));  // open: bin, bout
  Shifter #(.width(4)) shifter_1 (.in(op2), .\dist (shift_op[1:0]), .out(shifter_1_out));
  Multiplexer #(.select(4), .width(4)) multiplexer_1 (
    .in9(and_1_out), .in10(or_1_out), .in11(xor_1_out), .in12(not_1_out), .in13(adder_1_out),
    .in14(subtractor_1_out), .in15(shifter_1_out), .out(result), .sel(\function ));  // open: in0, in1, in2, in3, in4, in5, in6, in7, in8

  // Notes on the sheet:
  //   001000000000
endmodule

module REGS (
  input  [3:0] INOP1,
  input  [3:0] INOP2,
  input  CLK,
  input  [3:0] DESTINO,
  input  WRITE,
  input  [3:0] writevalue,
  output [3:0] OP1,
  output [3:0] OP2,
  output [3:0] RFLAGS
);

  wire and_1_out, and_2_out, and_3_out, and_4_out, and_5_out, and_6_out, and_7_out, and_8_out, and_9_out,
       and_10_out, and_11_out, and_12_out, and_13_out, and_14_out, and_15_out, and_16_out, decoder_1_out0,
       decoder_1_out1, decoder_1_out2, decoder_1_out3, decoder_1_out4, decoder_1_out5, decoder_1_out6,
       decoder_1_out7, decoder_1_out8, decoder_1_out9, decoder_1_out10, decoder_1_out11, decoder_1_out12,
       decoder_1_out13, decoder_1_out14, decoder_1_out15;
  wire [3:0] R0_q, R1_q, R2_q, R3_q, R4_q, R5_q, R6_q, R7_q, R8_q, R9_q, R10_q, R11_q, R12_q, R13_q, R14_q;

  Decoder #(.enable("false"), .select(4)) decoder_1 (
    .out0(decoder_1_out0), .out1(decoder_1_out1), .out2(decoder_1_out2), .out3(decoder_1_out3),
    .out4(decoder_1_out4), .out5(decoder_1_out5), .out6(decoder_1_out6), .out7(decoder_1_out7),
    .out8(decoder_1_out8), .out9(decoder_1_out9), .out10(decoder_1_out10), .out11(decoder_1_out11),
    .out12(decoder_1_out12), .out13(decoder_1_out13), .out14(decoder_1_out14), .out15(decoder_1_out15),
    .sel(DESTINO));
  and and_1 (and_1_out, decoder_1_out0, WRITE);
  and and_2 (and_2_out, decoder_1_out1, WRITE);
  and and_3 (and_3_out, decoder_1_out2, WRITE);
  and and_4 (and_4_out, decoder_1_out3, WRITE);
  and and_5 (and_5_out, decoder_1_out4, WRITE);
  and and_6 (and_6_out, decoder_1_out5, WRITE);
  and and_7 (and_7_out, decoder_1_out6, WRITE);
  and and_8 (and_8_out, decoder_1_out7, WRITE);
  and and_9 (and_9_out, decoder_1_out8, WRITE);
  and and_10 (and_10_out, decoder_1_out9, WRITE);
  and and_11 (and_11_out, decoder_1_out10, WRITE);
  and and_12 (and_12_out, decoder_1_out11, WRITE);
  and and_13 (and_13_out, decoder_1_out12, WRITE);
  and and_14 (and_14_out, decoder_1_out13, WRITE);
  and and_15 (and_15_out, decoder_1_out14, WRITE);
  and and_16 (and_16_out, decoder_1_out15, WRITE);
  Register #(.width(4)) R0 (.D(writevalue), .en(and_1_out), .Q(R0_q), .clk(CLK));  // open: clr
  Register #(.width(4)) R1 (.D(writevalue), .en(and_2_out), .Q(R1_q), .clk(CLK));  // open: clr
  Register #(.width(4)) R2 (.D(writevalue), .en(and_3_out), .Q(R2_q), .clk(CLK));  // open: clr
  Register #(.width(4)) R3 (.D(writevalue), .en(and_4_out), .Q(R3_q), .clk(CLK));  // open: clr
  Register #(.width(4)) R4 (.D(writevalue), .en(and_5_out), .Q(R4_q), .clk(CLK));  // open: clr
  Register #(.width(4)) R5 (.D(writevalue), .en(and_6_out), .Q(R5_q), .clk(CLK));  // open: clr
  Register #(.width(4)) R6 (.D(writevalue), .en(and_7_out), .Q(R6_q), .clk(CLK));  // open: clr
  Register #(.width(4)) R7 (.D(writevalue), .en(and_8_out), .Q(R7_q), .clk(CLK));  // open: clr
  Register #(.width(4)) R8 (.D(writevalue), .en(and_9_out), .Q(R8_q), .clk(CLK));  // open: clr
  Register #(.width(4)) R9 (.D(writevalue), .en(and_10_out), .Q(R9_q), .clk(CLK));  // open: clr
  Register #(.width(4)) R10 (.D(writevalue), .en(and_11_out), .Q(R10_q), .clk(CLK));  // open: clr
  Register #(.width(4)) R11 (.D(writevalue), .en(and_12_out), .Q(R11_q), .clk(CLK));  // open: clr
  Register #(.width(4)) R12 (.D(writevalue), .en(and_13_out), .Q(R12_q), .clk(CLK));  // open: clr
  Register #(.width(4)) R13 (.D(writevalue), .en(and_14_out), .Q(R13_q), .clk(CLK));  // open: clr
  Register #(.width(4)) R14 (.D(writevalue), .en(and_15_out), .Q(R14_q), .clk(CLK));  // open: clr
  Register #(.width(4)) R_FLAGS (.D(writevalue), .en(and_16_out), .Q(RFLAGS), .clk(CLK));  // open: clr
  Multiplexer #(.select(4), .width(4)) multiplexer_1 (
    .in0(R0_q), .in1(R1_q), .in2(R2_q), .in3(R3_q), .in4(R4_q), .in5(R5_q), .in6(R6_q), .in7(R7_q),
    .in8(R8_q), .in9(R9_q), .in10(R10_q), .in11(R11_q), .in12(R12_q), .in13(R13_q), .in14(R14_q), .out(OP1),
    .sel(INOP1));  // open: in15
  Multiplexer #(.select(4), .width(4)) multiplexer_2 (
    .in0(R0_q), .in1(R1_q), .in2(R2_q), .in3(R3_q), .in4(R4_q), .in5(R5_q), .in6(R6_q), .in7(R7_q),
    .in8(R8_q), .in9(R9_q), .in10(R10_q), .in11(R11_q), .in12(R12_q), .in13(R13_q), .in14(R14_q), .out(OP2),
    .sel(INOP2));  // open: in15

  // Other names for the same wires on the sheet: OP_1[3:0] = INOP1; OP_2[3:0] = INOP2; value[3:0] = writevalue
endmodule

module BT (
  input  [3:0] OP_code_First,
  input  [3:0] Destiny_First,
  input  [3:0] OP1_Second,
  input  [3:0] OP2_Second,
  input  ckl,
  output Burbuja,
  output enable_Forwarding,
  output Forwarding_operator
);

  wire comparator_1_eq, comparator_3_eq, decoder_1_out1, decoder_1_out2, decoder_1_out3, decoder_1_out5,
       decoder_1_out9, decoder_1_out10, decoder_1_out11, decoder_1_out12, decoder_1_out13, decoder_1_out14,
       decoder_1_out15, do_bubble, not_1_out, or_1_out, or_2_out, or_3_out;
  wire [1:0] counter_1_q;

  Decoder #(.enable("false"), .select(4)) decoder_1 (
    .out1(decoder_1_out1), .out2(decoder_1_out2), .out3(decoder_1_out3), .out5(decoder_1_out5),
    .out9(decoder_1_out9), .out10(decoder_1_out10), .out11(decoder_1_out11), .out12(decoder_1_out12),
    .out13(decoder_1_out13), .out14(decoder_1_out14), .out15(decoder_1_out15), .sel(OP_code_First));  // open: out0, out4, out6, out7, out8
  Comparator #(.width(4)) comparator_1 (.a(Destiny_First), .b(OP1_Second), .eq(comparator_1_eq));  // open: gt, lt
  Comparator #(.width(4)) comparator_2 (.a(Destiny_First), .b(OP2_Second), .eq(Forwarding_operator));  // open: gt, lt
  or or_1 (or_1_out, comparator_1_eq, Forwarding_operator);
  Counter #(.max('h3), .width(2)) counter_1 (
    .Q(counter_1_q), .up(do_bubble), .clk(ckl), .clr(comparator_3_eq));  // open: load, D, count, carry
  or or_2 (or_2_out, decoder_1_out1, decoder_1_out2, decoder_1_out3);
  or or_3 (or_3_out, decoder_1_out5, decoder_1_out9, decoder_1_out10, decoder_1_out11, decoder_1_out12, decoder_1_out13, decoder_1_out14, decoder_1_out15);
  Comparator #(.width(2)) comparator_3 (.a(2'b10), .b(counter_1_q), .eq(comparator_3_eq));  // open: gt, lt
  and and_1 (do_bubble, or_2_out, or_1_out);
  and and_2 (enable_Forwarding, or_3_out, or_1_out);
  Multiplexer multiplexer_1 (.in0(do_bubble), .in1(not_1_out), .out(Burbuja), .sel(comparator_3_eq));
  not not_1 (not_1_out, do_bubble);

  // Other names for the same wires on the sheet: bubble_state = Burbuja; clock = ckl
endmodule

module Decode (
  input  Clock,
  input  [15:0] OP_CODE,
  input  Enable_write,
  input  [3:0] Forward_value,
  input  Forward_enable,
  input  Forwarding_op,
  input  [3:0] WB_Destiny,
  input  [3:0] WB_value,
  output [3:0] OP1_Second,
  output [3:0] POS_MEM,
  output [3:0] OP2_Second,
  output [3:0] Inmediato,
  output [3:0] Destiny,
  output [3:0] OP1,
  output [3:0] Register,
  output [3:0] OP2,
  output [3:0] RFlags,
  output [3:0] Instruction,
  output [15:0] Decodes
);

  wire and_1_out, and_2_out, not_1_out;
  wire [3:0] fv_op1, fv_op2, regs_1_op1;

  REGS regs_1 (
    .CLK(Clock), .WRITE(Enable_write), .INOP1(OP_CODE[3:0]), .INOP2(OP_CODE[7:4]), .DESTINO(WB_Destiny),
    .writevalue(WB_value), .OP1(regs_1_op1), .OP2(Register), .RFLAGS(RFlags));
  Demultiplexer #(.width(4)) demultiplexer_1 (.out0(fv_op1), .out1(fv_op2), .in(Forward_value), .sel(Forwarding_op));
  Decoder #(.enable("false"), .select(4)) decoder_1 (
    .out0(Decodes[0]), .out1(Decodes[1]), .out2(Decodes[2]), .out3(Decodes[3]), .out4(Decodes[4]),
    .out5(Decodes[5]), .out6(Decodes[6]), .out7(Decodes[7]), .out8(Decodes[8]), .out9(Decodes[9]),
    .out10(Decodes[10]), .out11(Decodes[11]), .out12(Decodes[12]), .out13(Decodes[13]), .out14(Decodes[14]),
    .out15(Decodes[15]), .sel(OP_CODE[15:12]));
  and and_1 (and_1_out, Forward_enable, not_1_out);
  not not_1 (not_1_out, Forwarding_op);
  and and_2 (and_2_out, Forward_enable, Forwarding_op);
  Multiplexer #(.width(4)) multiplexer_1 (.in0(regs_1_op1), .in1(fv_op1), .out(OP1), .sel(and_1_out));
  Multiplexer #(.width(4)) multiplexer_2 (.in0(Register), .in1(fv_op2), .out(OP2), .sel(and_2_out));

  assign Destiny = OP_CODE[11:8];
  assign Inmediato = OP_CODE[7:4];
  assign Instruction = OP_CODE[15:12];
  assign OP1_Second = OP_CODE[3:0];
  assign OP2_Second = OP_CODE[7:4];
  assign POS_MEM = OP_CODE[3:0];

  // Other names for the same wires on the sheet: Do_forwarding = Forward_enable; fv[3:0] = Forward_value;
  //   OPcode[15:0] = OP_CODE; write = Enable_write

  // Notes on the sheet:
  //   DECODE
endmodule

module Execute (
  input  [3:0] POSMEM,
  input  [3:0] Regsiter,
  input  [3:0] Inmediato,
  input  [3:0] Destino,
  input  [3:0] OP1,
  input  [3:0] OP2,
  input  [3:0] Function,
  input  [15:0] Decodes,
  input  clock,
  output [3:0] POS_MEM,
  output [3:0] RegisterOutput,
  output [3:0] INM,
  output [3:0] DEST,
  output [3:0] Forward_value,
  output [3:0] Resultado,
  output [3:0] OP_Code,
  output Load,
  output Load_I,
  output Store,
  output Store_I,
  output Enable_ALU,
  output Enable_PC
);

  wire and_1_out, and_2_out, flag_igual, flag_mayor, flag_menor, register_1_q, register_2_q;
  wire [2:0] alu_1_cmp;

  ALU alu_1 (.shift_op(Destino), .\function (Function), .op1(OP1), .op2(OP2), .cmp(alu_1_cmp), .result(Forward_value));
  Decoder #(.enable("false"), .select(3)) decoder_1 (
    .out1(flag_mayor), .out2(flag_igual), .out4(flag_menor), .sel(alu_1_cmp));  // open: out0, out3, out5, out6, out7
  Register #(.width(1)) register_1 (.D(flag_mayor), .Q(register_1_q), .clk(clock));  // open: en, clr
  Register #(.width(1)) register_2 (.D(flag_igual), .Q(register_2_q), .clk(clock));  // open: en, clr
  and and_1 (and_1_out, register_1_q, Decodes[7]);
  and and_2 (and_2_out, register_2_q, Decodes[8]);
  or or_1 (Enable_ALU, Decodes[9], Decodes[10], Decodes[11], Decodes[12], Decodes[13], Decodes[14]);
  or or_2 (Enable_PC, and_1_out, Decodes[6], and_2_out);

  assign DEST = Destino;
  assign INM = Inmediato;
  assign Load = Decodes[1];
  assign Load_I = Decodes[3];
  assign OP_Code = Function;
  assign POS_MEM = POSMEM;
  assign RegisterOutput = Regsiter;
  assign Resultado = Forward_value;
  assign Store = Decodes[2];
  assign Store_I = Decodes[4];

  // Other names for the same wires on the sheet: NO_OP_133d16a6 = Decodes[0]; LOADI = Decodes[3]; STOREI = Decodes[4];
  //   CMP = Decodes[5]; JMP = Decodes[6]; BB = Decodes[7]; BEQ = Decodes[8]; AND = Decodes[9]; OR = Decodes[10];
  //   XOR = Decodes[11]; NOT = Decodes[12]; ADD = Decodes[13]; SUB = Decodes[14]; SHIFT = Decodes[15]

  // Notes on the sheet:
  //   STORE I
  //   LOAD, STORE
  //   LOAD I
endmodule

module Memory (
  input  [3:0] Destiny,
  input  [3:0] POS_MEM,
  input  [3:0] Register,
  input  [3:0] Inmediato,
  input  [3:0] Result,
  input  clock,
  input  LOAD,
  input  Enable_LOADI,
  input  Enable_STORE,
  input  Enable_STORE_I,
  input  Enable_ALU,
  output [3:0] Destino,
  output [3:0] Value,
  output Enable_LOAD,
  output LOADI,
  output STORE,
  output STOREI,
  output ALU
);

  wire loadMEM, or_1_out;
  wire [3:0] controlled_buffer_1_out, multiplexer_1_out, multiplexer_2_out;

  RAM #(.addrWidth(4), .dataWidth(4), .databus("bidir")) ram_1 (
    .addr(POS_MEM), .oe(loadMEM), .clk(clock));  // open: we, data
  Multiplexer #(.width(4)) multiplexer_1 (
    .in0(Inmediato), .in1(controlled_buffer_1_out), .out(multiplexer_1_out), .sel(LOAD));
  not not_1 (loadMEM, or_1_out);
  or or_1 (or_1_out, Enable_STORE, Enable_STORE_I);
  assign controlled_buffer_1_out = or_1_out ? multiplexer_2_out : 4'bz;  // Controlled_Buffer controlled_buffer_1
  Multiplexer #(.width(4)) multiplexer_2 (
    .in0(Register), .in1(Inmediato), .out(multiplexer_2_out), .sel(Enable_STORE_I));
  Multiplexer #(.width(4)) multiplexer_3 (.in0(multiplexer_1_out), .in1(Result), .out(Value), .sel(Enable_ALU));

  assign ALU = Enable_ALU;
  assign Destino = Destiny;
  assign Enable_LOAD = LOAD;
  assign LOADI = Enable_LOADI;
  assign STORE = Enable_STORE;
  assign STOREI = Enable_STORE_I;

  // Other names for the same wires on the sheet: enable_ALU_MEM = Enable_ALU; enable_LOAD_MEM = LOAD;
  //   enable_STORE_MEM = Enable_STORE; enable_STOREI_MEM = Enable_STORE_I

  // Notes on the sheet:
  //   LOAD o LOADI
endmodule
