// Logisim project 32RV.circ as structural Verilog
module main (
);

  wire cachecontroller1_1_cpu_rd_requestout, cachecontroller1_1_cpu_wr_requestout,
       cachecontroller1_2_cpu_rd_requestout, cachecontroller1_2_cpu_wr_requestout, clock_1_out,
       core_1_memread_out, core_1_memwrite_out, core_2_memread_out, core_2_memwrite_out;
  wire [2:0] cachecontroller1_1_cpu_rqaddr_out, cachecontroller1_2_cpu_rqaddr_out;
  wire [14:0] core_1_aludir_out, core_2_aludir_out;
  wire [31:0] cachecontroller1_1_sdram_dataout, cachecontroller1_2_sdram_dataout, core_1_rd2_out,
       core_2_rd2_out;

  Clock clock_1 (.out(clock_1_out));
  Core core_1 (
    .CLK(clock_1_out), .cache_data_in(cachecontroller1_1_sdram_dataout), .ALUDIR_out(core_1_aludir_out),
    .RD2_out(core_1_rd2_out), .MemRead_out(core_1_memread_out), .MemWrite_out(core_1_memwrite_out));  // open: systemErrorFlag
  Core core_2 (
    .CLK(clock_1_out), .cache_data_in(cachecontroller1_2_sdram_dataout), .ALUDIR_out(core_2_aludir_out),
    .RD2_out(core_2_rd2_out), .MemRead_out(core_2_memread_out), .MemWrite_out(core_2_memwrite_out));  // open: systemErrorFlag
  CacheController1 cachecontroller1_1 (
    .CLK(clock_1_out), .wantedAddress(core_1_aludir_out[2:0]), .SDRAM_dataIn(core_1_rd2_out),
    .CPU_wr_requestIn(core_1_memwrite_out), .CPU_rd_requestIn(core_1_memread_out),
    .SDRAM_dataOut(cachecontroller1_1_sdram_dataout),
    .CPU_wr_requestOut(cachecontroller1_1_cpu_wr_requestout),
    .CPU_rd_requestOut(cachecontroller1_1_cpu_rd_requestout),
    .CPU_rqAddr_out(cachecontroller1_1_cpu_rqaddr_out));  // open: reset, priority, CPU_rqAddr_in, c2c_req_in, c2c_reqAddr_in, c2c_resp_in, c2c_respIn_ready, c2c_respIn_data, read_enable, write_enable, SDRAM_addr, c2c_req_out, c2c_reqAddr_out, c2c_resp_out, c2c_respOut_ready, c2c_respOut_data
  CacheController1 cachecontroller1_2 (
    .CLK(clock_1_out), .wantedAddress(core_2_aludir_out[2:0]), .SDRAM_dataIn(core_2_rd2_out),
    .CPU_wr_requestIn(core_2_memwrite_out), .CPU_rd_requestIn(core_2_memread_out),
    .SDRAM_dataOut(cachecontroller1_2_sdram_dataout),
    .CPU_wr_requestOut(cachecontroller1_2_cpu_wr_requestout),
    .CPU_rd_requestOut(cachecontroller1_2_cpu_rd_requestout),
    .CPU_rqAddr_out(cachecontroller1_2_cpu_rqaddr_out));  // open: reset, priority, CPU_rqAddr_in, c2c_req_in, c2c_reqAddr_in, c2c_resp_in, c2c_respIn_ready, c2c_respIn_data, read_enable, write_enable, SDRAM_addr, c2c_req_out, c2c_reqAddr_out, c2c_resp_out, c2c_respOut_ready, c2c_respOut_data
  FIFO fifo_1 (
    .clk(clock_1_out), .cpu0_read_in(cachecontroller1_1_cpu_rd_requestout),
    .cpu0_write_in(cachecontroller1_1_cpu_wr_requestout), .cpu0_addr(cachecontroller1_1_cpu_rqaddr_out),
    .cpu1_read_in(cachecontroller1_2_cpu_rd_requestout),
    .cpu1_write_in(cachecontroller1_2_cpu_wr_requestout), .cpu1_addr(cachecontroller1_2_cpu_rqaddr_out));  // open: rst, cpu0_data_in, cpu1_data_in, read_out, write_out, addr_out, data_out
  TransactionsBetweenCPU transactionsbetweencpu_1 ();  // open: clk, rst, cpu0_prio, cpu1_prio, cpu0_wantedAddr, cpu1_wantedAddr
  sdram sdram_1 (.clk(clock_1_out));  // open: reset, operation1, operation2, ready1, ready2, addr1, addr2, data_in1, data_in2, data_out1, data_out2
  msi_protocol msi_protocol_1 ();  // open: clk, reset, cpu0_state, cpu1_state, cpu0_addr, cpu1_addr, invalidate_cpu0, invalidate_cpu1
endmodule

module ProgramCounter (
  input  [31:0] inPC,
  input  CLK,
  output [31:0] outPCPlus4,
  output [31:0] outPC
);

  Register #(.width(32)) register_1 (.D(inPC), .en(1'b1), .clk(CLK), .Q(outPC));  // open: clr
  Adder #(.width(32)) adder_1 (.a(outPC), .b(32'h1), .out(outPCPlus4));  // open: cin, cout

  // Other names for the same wires on the sheet: CLK_t = CLK; inPC_t[31:0] = inPC; outPC_t[31:0] = outPC;
  //   outPCPlus4_t[31:0] = outPCPlus4
endmodule

module RegisterFile (
  input  [4:0] rsi1,
  input  [4:0] rsi2,
  input  [4:0] rdi,
  input  [31:0] rd,
  input  we,
  input  CLK,
  output [31:0] rs1,
  output [31:0] rs2,
  output ERR
);

  wire x1we_t, x2we_t, x3we_t, x4we_t, x5we_t, x6we_t, x7we_t, x8we_t, x9we_t, x10we_t, x11we_t, x12we_t,
       x13we_t, x14we_t, x15we_t, x16we_t, x17we_t, x18we_t, x19we_t, x20we_t, x21we_t, x22we_t, x23we_t,
       x24we_t, x25we_t, x26we_t, x27we_t, x28we_t, x29we_t, x30we_t, x31we_t;
  wire [31:0] x1q_t, x2q_t, x3q_t, x4q_t, x5q_t, x6q_t, x7q_t, x8q_t, x9q_t, x10q_t, x11q_t, x12q_t, x13q_t,
       x14q_t, x15q_t, x16q_t, x17q_t, x18q_t, x19q_t, x20q_t, x21q_t, x22q_t, x23q_t, x24q_t, x25q_t,
       x26q_t, x27q_t, x28q_t, x29q_t, x30q_t, x31q_t;

  Demultiplexer #(.select(5)) demultiplexer_1 (
    .out0(ERR), .out1(x1we_t), .out2(x2we_t), .out3(x3we_t), .out4(x4we_t), .out5(x5we_t), .out6(x6we_t),
    .out7(x7we_t), .out8(x8we_t), .out9(x9we_t), .out10(x10we_t), .out11(x11we_t), .out12(x12we_t),
    .out13(x13we_t), .out14(x14we_t), .out15(x15we_t), .out16(x16we_t), .out17(x17we_t), .out18(x18we_t),
    .out19(x19we_t), .out20(x20we_t), .out21(x21we_t), .out22(x22we_t), .out23(x23we_t), .out24(x24we_t),
    .out25(x25we_t), .out26(x26we_t), .out27(x27we_t), .out28(x28we_t), .out29(x29we_t), .out30(x30we_t),
    .out31(x31we_t), .in(we), .sel(rdi));
  Register #(.width(32)) x4 (.D(rd), .en(x4we_t), .clk(CLK), .Q(x4q_t));  // open: clr
  Register #(.width(32)) x8 (.D(rd), .en(x8we_t), .clk(CLK), .Q(x8q_t));  // open: clr
  Register #(.width(32)) x12 (.D(rd), .en(x12we_t), .clk(CLK), .Q(x12q_t));  // open: clr
  Register #(.width(32)) x16 (.D(rd), .en(x16we_t), .clk(CLK), .Q(x16q_t));  // open: clr
  Register #(.width(32)) x20 (.D(rd), .en(x20we_t), .clk(CLK), .Q(x20q_t));  // open: clr
  Register #(.width(32)) x24 (.D(rd), .en(x24we_t), .clk(CLK), .Q(x24q_t));  // open: clr
  Register #(.width(32)) x28 (.D(rd), .en(x28we_t), .clk(CLK), .Q(x28q_t));  // open: clr
  Register #(.width(32)) x1 (.D(rd), .en(x1we_t), .clk(CLK), .Q(x1q_t));  // open: clr
  Register #(.width(32)) x5 (.D(rd), .en(x5we_t), .clk(CLK), .Q(x5q_t));  // open: clr
  Register #(.width(32)) x9 (.D(rd), .en(x9we_t), .clk(CLK), .Q(x9q_t));  // open: clr
  Register #(.width(32)) x13 (.D(rd), .en(x13we_t), .clk(CLK), .Q(x13q_t));  // open: clr
  Register #(.width(32)) x17 (.D(rd), .en(x17we_t), .clk(CLK), .Q(x17q_t));  // open: clr
  Register #(.width(32)) x21 (.D(rd), .en(x21we_t), .clk(CLK), .Q(x21q_t));  // open: clr
  Register #(.width(32)) x25 (.D(rd), .en(x25we_t), .clk(CLK), .Q(x25q_t));  // open: clr
  Register #(.width(32)) x29 (.D(rd), .en(x29we_t), .clk(CLK), .Q(x29q_t));  // open: clr
  Register #(.width(32)) x2 (.D(rd), .en(x2we_t), .clk(CLK), .Q(x2q_t));  // open: clr
  Register #(.width(32)) x6 (.D(rd), .en(x6we_t), .clk(CLK), .Q(x6q_t));  // open: clr
  Register #(.width(32)) x10 (.D(rd), .en(x10we_t), .clk(CLK), .Q(x10q_t));  // open: clr
  Register #(.width(32)) x14 (.D(rd), .en(x14we_t), .clk(CLK), .Q(x14q_t));  // open: clr
  Register #(.width(32)) x18 (.D(rd), .en(x18we_t), .clk(CLK), .Q(x18q_t));  // open: clr
  Register #(.width(32)) x22 (.D(rd), .en(x22we_t), .clk(CLK), .Q(x22q_t));  // open: clr
  Register #(.width(32)) x26 (.D(rd), .en(x26we_t), .clk(CLK), .Q(x26q_t));  // open: clr
  Register #(.width(32)) x30 (.D(rd), .en(x30we_t), .clk(CLK), .Q(x30q_t));  // open: clr
  Register #(.width(32)) x3 (.D(rd), .en(x3we_t), .clk(CLK), .Q(x3q_t));  // open: clr
  Register #(.width(32)) x7 (.D(rd), .en(x7we_t), .clk(CLK), .Q(x7q_t));  // open: clr
  Register #(.width(32)) x11 (.D(rd), .en(x11we_t), .clk(CLK), .Q(x11q_t));  // open: clr
  Register #(.width(32)) x15 (.D(rd), .en(x15we_t), .clk(CLK), .Q(x15q_t));  // open: clr
  Register #(.width(32)) x19 (.D(rd), .en(x19we_t), .clk(CLK), .Q(x19q_t));  // open: clr
  Register #(.width(32)) x23 (.D(rd), .en(x23we_t), .clk(CLK), .Q(x23q_t));  // open: clr
  Register #(.width(32)) x27 (.D(rd), .en(x27we_t), .clk(CLK), .Q(x27q_t));  // open: clr
  Register #(.width(32)) x31 (.D(rd), .en(x31we_t), .clk(CLK), .Q(x31q_t));  // open: clr
  Multiplexer #(.select(5), .width(32)) multiplexer_1 (
    .in0({32{1'b0}}), .in1(x1q_t), .in2(x2q_t), .in3(x3q_t), .in4(x4q_t), .in5(x5q_t), .in6(x6q_t),
    .in7(x7q_t), .in8(x8q_t), .in9(x9q_t), .in10(x10q_t), .in11(x11q_t), .in12(x12q_t), .in13(x13q_t),
    .in14(x14q_t), .in15(x15q_t), .in16(x16q_t), .in17(x17q_t), .in18(x18q_t), .in19(x19q_t), .in20(x20q_t),
    .in21(x21q_t), .in22(x22q_t), .in23(x23q_t), .in24(x24q_t), .in25(x25q_t), .in26(x26q_t), .in27(x27q_t),
    .in28(x28q_t), .in29(x29q_t), .in30(x30q_t), .in31(x31q_t), .out(rs2), .sel(rsi2));
  Multiplexer #(.select(5), .width(32)) multiplexer_2 (
    .in0({32{1'b0}}), .in1(x1q_t), .in2(x2q_t), .in3(x3q_t), .in4(x4q_t), .in5(x5q_t), .in6(x6q_t),
    .in7(x7q_t), .in8(x8q_t), .in9(x9q_t), .in10(x10q_t), .in11(x11q_t), .in12(x12q_t), .in13(x13q_t),
    .in14(x14q_t), .in15(x15q_t), .in16(x16q_t), .in17(x17q_t), .in18(x18q_t), .in19(x19q_t), .in20(x20q_t),
    .in21(x21q_t), .in22(x22q_t), .in23(x23q_t), .in24(x24q_t), .in25(x25q_t), .in26(x26q_t), .in27(x27q_t),
    .in28(x28q_t), .in29(x29q_t), .in30(x30q_t), .in31(x31q_t), .out(rs1), .sel(rsi1));

  // Other names for the same wires on the sheet: CLK_t = CLK; rd_t[31:0] = rd; rdi_t[4:0] = rdi; rs1_t[31:0] = rs1;
  //   rs2_t[31:0] = rs2; rsi1_t[4:0] = rsi1; rsi2_t[4:0] = rsi2; we_t = we; x0we_t = ERR

  // Notes on the sheet:
  //   Register Destination Index
  //   Register Destination Value
  //   Write Enable
  //   Clock
  //   Register Source Index
  //   si x0we enciende, es falta
  //   x0 siempre es 0
  //   Output Register Values
endmodule

module InmExtractor (
  input  [31:0] instr,
  output [31:0] I_imm,
  output [31:0] S_imm,
  output [31:0] B_imm,
  output [31:0] U_imm,
  output [31:0] J_imm
);

  // NoConnect on instr[6:0]
  assign {I_imm[31], B_imm[31:12]} = {{20{instr[31]}}, instr[31]};  // Bit_Extender bit_extender_1
  // NoConnect on I_imm[31]
  // NoConnect on {I_imm[31], B_imm[31:13]}
  // NoConnect on {I_imm[31], B_imm[31:24]}

  assign B_imm[11:0] = {instr[7], instr[30:25], instr[11:8], 1'b0};
  assign I_imm[30:0] = {B_imm[31:12], instr[30:20]};
  assign J_imm = {B_imm[23:12], instr[19:12], instr[20], instr[30:21], 1'b0};
  assign S_imm = {I_imm[31], B_imm[31:12], instr[30:25], instr[11:7]};
  assign U_imm = {B_imm[12], instr[30:12], {12{1'b0}}};

  // Notes on the sheet:
  //   I-imm
  //   S-imm
  //   B-imm
  //   U-imm
  //   J-imm
endmodule

module IDecode (
  input  [31:0] instr,
  output [6:0] OPcode,
  output [4:0] rd,
  output [2:0] funct3,
  output [4:0] rs1,
  output [4:0] rs2,
  output [6:0] funct7,
  output [31:0] imm,
  output ar_r,
  output ar_i,
  output ld,
  output st,
  output br,
  output jal,
  output jalr,
  output lui,
  output auipc,
  output ebc
);

  wire or_1_out;
  wire [31:0] inmextractor_1_b_imm, inmextractor_1_i_imm, inmextractor_1_j_imm, inmextractor_1_s_imm,
       inmextractor_1_u_imm, multiplexer_1_out, multiplexer_2_out, multiplexer_3_out;

  Comparator #(.width(7)) comparator_1 (.a(instr[6:0]), .b(7'b0110011), .eq(ar_r));  // open: gt, lt
  Comparator #(.width(7)) comparator_2 (.a(instr[6:0]), .b(7'b0010011), .eq(ar_i));  // open: gt, lt
  Comparator #(.width(7)) comparator_3 (.a(instr[6:0]), .b(7'b0000011), .eq(ld));  // open: gt, lt
  Comparator #(.width(7)) comparator_4 (.a(instr[6:0]), .b(7'b0100011), .eq(st));  // open: gt, lt
  Comparator #(.width(7)) comparator_5 (.a(instr[6:0]), .b(7'b1100011), .eq(br));  // open: gt, lt
  Comparator #(.width(7)) comparator_6 (.a(instr[6:0]), .b(7'b1101111), .eq(jal));  // open: gt, lt
  Comparator #(.width(7)) comparator_7 (.a(instr[6:0]), .b(7'b1100111), .eq(jalr));  // open: gt, lt
  Comparator #(.width(7)) comparator_8 (.a(instr[6:0]), .b(7'b0110111), .eq(lui));  // open: gt, lt
  Comparator #(.width(7)) comparator_9 (.a(instr[6:0]), .b(7'b0010111), .eq(auipc));  // open: gt, lt
  Comparator #(.width(7)) comparator_10 (.a(instr[6:0]), .b(7'b1110011), .eq(ebc));  // open: gt, lt
  InmExtractor inmextractor_1 (
    .instr(instr), .I_imm(inmextractor_1_i_imm), .S_imm(inmextractor_1_s_imm), .B_imm(inmextractor_1_b_imm),
    .U_imm(inmextractor_1_u_imm), .J_imm(inmextractor_1_j_imm));
  Multiplexer #(.width(32)) multiplexer_1 (
    .in0(inmextractor_1_i_imm), .in1(inmextractor_1_s_imm), .out(multiplexer_1_out), .sel(st));
  Multiplexer #(.width(32)) multiplexer_2 (
    .in0(multiplexer_1_out), .in1(inmextractor_1_b_imm), .out(multiplexer_2_out), .sel(br));
  Multiplexer #(.width(32)) multiplexer_3 (
    .in0(multiplexer_2_out), .in1(inmextractor_1_u_imm), .out(multiplexer_3_out), .sel(or_1_out));
  or or_1 (or_1_out, auipc, lui);
  Multiplexer #(.width(32)) multiplexer_4 (.in0(multiplexer_3_out), .in1(inmextractor_1_j_imm), .out(imm), .sel(jal));

  assign funct3 = instr[14:12];
  assign funct7 = instr[31:25];
  assign OPcode = instr[6:0];
  assign rd = instr[11:7];
  assign rs1 = instr[19:15];
  assign rs2 = instr[24:20];
endmodule

module Core1 (
  input  [31:0] jumpTEMP,
  input  branchFlagTEMP,
  input  CLK,
  input  [31:0] cache_data_in,
  output [14:0] ALUDIR_out,
  output [31:0] RD2_out,
  output systemErrorFlag,
  output MemRead_out,
  output MemWrite_out
);

  wire alu_decoder_1_is_imm, ALUSrc, Branch, EX_MEM_MemToReg_t, EX_MEM_RegWrite_t, Flag, idecode_1_ar_i,
       idecode_1_ar_r, idecode_1_auipc, idecode_1_ebc, idecode_1_jal, idecode_1_jalr, idecode_1_lui,
       Immediate_q, MEM_WB_MemtoReg_q, MEM_WB_RegWrite, MemRead, MemWrite, not_1_out, or_5_out, RegWrite,
       x0_write_err;
  wire [2:0] idecode_1_funct3;
  wire [3:0] alu_decoder_1_instr_code, Code_q;
  wire [4:0] DestinationRegister, EX_MEM_RD_t, idecode_1_rs1, idecode_1_rs2, MEM_WB_RDI, RD_q;
  wire [6:0] bit_extender_1_out, idecode_1_funct7, idecode_1_opcode;
  wire [31:0] ALUResult, idecode_1_imm, IF_ID_q, IM_dout, Inm_q, MEM_WB_ALU_q, MEM_WB_MEMDATA_q,
       multiplexer_1_out, multiplexer_2_out, programcounter_1_outpc, programcounter_1_outpcplus4,
       registerfile_1_rs1, SecondOperand, WriteBackData;
  wire [31:15] EX_MEM_ALU_t;

  Multiplexer #(.width(32)) multiplexer_1 (
    .in0(jumpTEMP), .in1(programcounter_1_outpcplus4), .out(multiplexer_1_out), .sel(not_1_out));
  not not_1 (not_1_out, branchFlagTEMP);
  or or_1 (systemErrorFlag, x0_write_err, 1'b0);
  ProgramCounter programcounter_1 (
    .inPC(multiplexer_1_out), .CLK(CLK), .outPCPlus4(programcounter_1_outpcplus4),
    .outPC(programcounter_1_outpc));
  RAM #(.addrWidth(15), .dataWidth(32)) IM (
    .addr(programcounter_1_outpc[14:0]), .clk(CLK), .dout(IM_dout));  // open: we, oe, din
  Register #(.width(32)) IF_ID (.D(IM_dout), .en(1'b1), .clk(CLK), .Q(IF_ID_q));  // open: clr
  IDecode idecode_1 (
    .instr(IF_ID_q), .OPcode(idecode_1_opcode), .rd(DestinationRegister), .funct3(idecode_1_funct3),
    .rs1(idecode_1_rs1), .rs2(idecode_1_rs2), .funct7(idecode_1_funct7), .imm(idecode_1_imm),
    .ar_r(idecode_1_ar_r), .ar_i(idecode_1_ar_i), .ld(MemRead), .st(MemWrite), .br(Branch),
    .jal(idecode_1_jal), .jalr(idecode_1_jalr), .lui(idecode_1_lui), .auipc(idecode_1_auipc),
    .ebc(idecode_1_ebc));
  or or_2 (RegWrite, idecode_1_auipc, idecode_1_lui, idecode_1_jalr, idecode_1_jal, MemRead, idecode_1_ar_i, idecode_1_ar_r);
  or or_3 (ALUSrc, idecode_1_auipc, idecode_1_lui, idecode_1_jalr, MemWrite, MemRead, idecode_1_ar_i);
  or or_4 (Flag, idecode_1_jalr, idecode_1_jal);
  or or_5 (or_5_out, idecode_1_ar_r, idecode_1_ar_i);
  Register #(.width(5)) RD (.D(DestinationRegister), .Q(RD_q), .clk(CLK));  // open: en, clr
  alu_decoder alu_decoder_1 (
    .opcode(idecode_1_opcode), .funct3(idecode_1_funct3), .funct7(idecode_1_funct7),
    .instr_code(alu_decoder_1_instr_code), .is_imm(alu_decoder_1_is_imm));
  Register #(.width(32)) Inm (.D(idecode_1_imm), .Q(Inm_q), .clk(CLK));  // open: en, clr
  Register #(.width(4)) Code (.D(alu_decoder_1_instr_code), .Q(Code_q), .clk(CLK));  // open: en, clr
  Register #(.width(1)) Immediate (.D(alu_decoder_1_is_imm), .Q(Immediate_q), .clk(CLK));  // open: en, clr
  RegisterFile registerfile_1 (
    .rsi1(idecode_1_rs1), .rsi2(idecode_1_rs2), .rdi(MEM_WB_RDI), .rd(WriteBackData), .we(MemWrite_out),
    .CLK(CLK), .rs1(registerfile_1_rs1), .rs2(SecondOperand), .ERR(x0_write_err));
  Multiplexer #(.width(32)) multiplexer_2 (
    .in0(SecondOperand), .in1(Inm_q), .out(multiplexer_2_out), .sel(Immediate_q));
  assign bit_extender_1_out = {{3{Code_q[3]}}, Code_q};  // Bit_Extender bit_extender_1
  ALU alu_1 (.A(registerfile_1_rs1), .B(multiplexer_2_out), .Op(bit_extender_1_out), .Y(ALUResult));
  Register #(.width(32)) EX_MEM_ALU (.D(ALUResult), .clk(CLK), .Q({EX_MEM_ALU_t, ALUDIR_out}));  // open: en, clr
  Register #(.width(32)) EX_MEM_RD2 (.D(SecondOperand), .clk(CLK), .Q(RD2_out));  // open: en, clr
  Register #(.width(5)) EX_MEM_RD (.D(DestinationRegister), .clk(CLK), .Q(EX_MEM_RD_t));  // open: en, clr
  Register #(.width(1)) EX_MEM_MemRead (.D(MemRead), .clk(CLK), .Q(MemRead_out));  // open: en, clr
  Register #(.width(1)) EX_MEM_MemWrite (.D(MemWrite), .clk(CLK), .Q(MemWrite_out));  // open: en, clr
  Register #(.width(1)) EX_MEM_MemToReg (.D(MemRead), .clk(CLK), .Q(EX_MEM_MemToReg_t));  // open: en, clr
  Register #(.width(1)) EX_MEM_RegWrite (.D(RegWrite), .clk(CLK), .Q(EX_MEM_RegWrite_t));  // open: en, clr
  Register #(.width(32)) MEM_WB_ALU (.D({EX_MEM_ALU_t, ALUDIR_out}), .clk(CLK), .Q(MEM_WB_ALU_q));  // open: en, clr
  Register #(.width(32)) MEM_WB_MEMDATA (.D(cache_data_in), .clk(CLK), .Q(MEM_WB_MEMDATA_q));  // open: en, clr
  Register #(.width(5)) u_MEM_WB_RDI (.D(EX_MEM_RD_t), .clk(CLK), .Q(MEM_WB_RDI));  // open: en, clr
  Register #(.width(1)) MEM_WB_MemtoReg (.D(EX_MEM_MemToReg_t), .clk(CLK), .Q(MEM_WB_MemtoReg_q));  // open: en, clr
  Register #(.width(1)) u_MEM_WB_RegWrite (.D(EX_MEM_RegWrite_t), .clk(CLK), .Q(MEM_WB_RegWrite));  // open: en, clr
  Multiplexer #(.width(32)) multiplexer_3 (
    .in0(MEM_WB_ALU_q), .in1(MEM_WB_MEMDATA_q), .out(WriteBackData), .sel(MEM_WB_MemtoReg_q));

  // Other names for the same wires on the sheet: branch_test = branchFlagTEMP; EX_MEM_ALU_t[14:0] = ALUDIR_out;
  //   EX_MEM_MemRead_t = MemRead_out; EX_MEM_MemWrite_t = MemWrite_out; EX_MEM_RD2_t[31:0] = RD2_out;
  //   jmp_ins_idx[31:0] = jumpTEMP; MemtoReg = MemRead

  // Notes on the sheet:
  //   Fetch
  //   Decode
  //   Execute
  //   TIPO R
  //   Memory
  //   Writeback 
endmodule

module CacheController1 (
  input  CLK,
  input  reset,
  input  \priority ,
  input  [2:0] wantedAddress,
  input  [31:0] SDRAM_dataIn,
  input  CPU_wr_requestIn,
  input  CPU_rd_requestIn,
  input  [2:0] CPU_rqAddr_in,
  input  c2c_req_in,
  input  [2:0] c2c_reqAddr_in,
  input  c2c_resp_in,
  input  c2c_respIn_ready,
  input  [31:0] c2c_respIn_data,
  output read_enable,
  output write_enable,
  output [2:0] SDRAM_addr,
  output [31:0] SDRAM_dataOut,
  output CPU_wr_requestOut,
  output CPU_rd_requestOut,
  output [2:0] CPU_rqAddr_out,
  output c2c_req_out,
  output [2:0] c2c_reqAddr_out,
  output c2c_resp_out,
  output c2c_respOut_ready,
  output [31:0] c2c_respOut_data
);

  CPU_Core CacheController0 (
    .clk(CLK), .reset(reset), .\priority (\priority ), .wantedAddress(wantedAddress),
    .Sdram_data_in(SDRAM_dataIn), .cpu_wr_req_in(CPU_wr_requestIn), .cpu_rd_req_in(CPU_rd_requestIn),
    .cpu_req_addr_in(CPU_rqAddr_in), .cache_to_cache_req_in(c2c_req_in),
    .cache_to_cache_req_address_in(c2c_reqAddr_in), .cache_to_cache_resp_in(c2c_resp_in),
    .cache_to_cache_resp_in_ready(c2c_respIn_ready), .cache_to_cache_resp_in_data(c2c_respIn_data),
    .read_en(read_enable), .write_en(write_enable), .Sdram_addr(SDRAM_addr), .Sdram_data_out(SDRAM_dataOut),
    .cpu_wr_req_out(CPU_wr_requestOut), .cpu_rd_req_out(CPU_rd_requestOut),
    .cpu_req_addr_out(CPU_rqAddr_out), .cache_to_cache_req_out(c2c_req_out),
    .cache_to_cache_req_address_out(c2c_reqAddr_out), .cache_to_cache_resp_out(c2c_resp_out),
    .cache_to_cache_resp_out_ready(c2c_respOut_ready), .cache_to_cache_resp_out_data(c2c_respOut_data));
endmodule

module Core (
  input  CLK,
  input  [31:0] cache_data_in,
  output [14:0] ALUDIR_out,
  output [31:0] RD2_out,
  output systemErrorFlag,
  output MemRead_out,
  output MemWrite_out
);

  wire alu_decoder_1_is_imm, beq, bne, Branch, button_1_out, comparator_1_gt, comparator_1_lt,
       ebc_1_flag_out, EX_MEM_MemToReg_t, EX_MEM_RegWrite_t, idecode_1_ar_i, idecode_1_ar_r, idecode_1_auipc,
       idecode_1_br, idecode_1_ebc, idecode_1_jal, idecode_1_jalr, idecode_1_lui, Inmediate_q, JumpFlag,
       keyboard_1_avail, MEM_WB_MemtoReg_q, MEM_WB_RegWrite, MemRead, MemWrite, not_1_out, or_1_out,
       RegWrite, x0_write_err;
  wire [2:0] idecode_1_funct3;
  wire [3:0] alu_decoder_1_instr_code, Code_q;
  wire [4:0] DestinationRegister, EX_MEM_RD_t, idecode_1_rs1, idecode_1_rs2, MEM_WB_RDI;
  wire [6:0] bit_extender_1_out, idecode_1_funct7, idecode_1_opcode, keyboard_1_data;
  wire [31:0] ALUResult, FirstOperand, IF_ID_q, IM_dout, INM, INM2, MEM_WB_ALU_q, MEM_WB_MEMDATA_q,
       multiplexer_2_out, multiplexer_3_out, multiplexer_4_out, PC, programcounter_1_outpc,
       programcounter_1_outpcplus4, SecondOperand, WriteBackData;
  wire [31:15] EX_MEM_ALU_t;

  Multiplexer #(.width(32)) multiplexer_1 (
    .in0(multiplexer_2_out), .in1(programcounter_1_outpcplus4), .out(PC), .sel(not_1_out));
  Multiplexer #(.width(32)) multiplexer_2 (.in0(INM), .in1(INM2), .out(multiplexer_2_out), .sel(Branch));
  not not_1 (not_1_out, or_1_out);
  or or_1 (or_1_out, JumpFlag, Branch);
  ProgramCounter programcounter_1 (
    .inPC(PC), .CLK(CLK), .outPCPlus4(programcounter_1_outpcplus4), .outPC(programcounter_1_outpc));
  or or_2 (systemErrorFlag, x0_write_err, 1'b0);
  RAM #(.addrWidth(15), .dataWidth(32)) IM (
    .addr(programcounter_1_outpc[14:0]), .clk(CLK), .dout(IM_dout));  // open: we, oe, din
  Register #(.width(32)) IF_ID (.D(IM_dout), .en(1'b1), .clk(CLK), .Q(IF_ID_q));  // open: clr
  Keyboard keyboard_1 (.clk(CLK), .re(1'b1), .clr(button_1_out), .avail(keyboard_1_avail), .data(keyboard_1_data));
  Button button_1 (.out(button_1_out));
  IDecode idecode_1 (
    .instr(IF_ID_q), .OPcode(idecode_1_opcode), .rd(DestinationRegister), .funct3(idecode_1_funct3),
    .rs1(idecode_1_rs1), .rs2(idecode_1_rs2), .funct7(idecode_1_funct7), .imm(INM), .ar_r(idecode_1_ar_r),
    .ar_i(idecode_1_ar_i), .ld(MemRead), .st(MemWrite), .br(idecode_1_br), .jal(idecode_1_jal),
    .jalr(idecode_1_jalr), .lui(idecode_1_lui), .auipc(idecode_1_auipc), .ebc(idecode_1_ebc));
  or or_3 (RegWrite, idecode_1_auipc, idecode_1_lui, idecode_1_jalr, idecode_1_jal, MemRead, idecode_1_ar_i, idecode_1_ar_r);
  or or_4 (JumpFlag, idecode_1_jalr, idecode_1_jal);
  LED led_1 (.in(ebc_1_flag_out));
  ebc ebc_1 (
    .clk(CLK), .reset_n(button_1_out), .key_valid(keyboard_1_avail), .enable(idecode_1_ebc),
    .key_data(keyboard_1_data), .flag_out(ebc_1_flag_out));
  Multiplexer #(.width(32)) multiplexer_3 (.in0(WriteBackData), .in1(PC), .out(multiplexer_3_out), .sel(JumpFlag));
  alu_decoder alu_decoder_1 (
    .opcode(idecode_1_opcode), .funct3(idecode_1_funct3), .funct7(idecode_1_funct7),
    .instr_code(alu_decoder_1_instr_code), .is_imm(alu_decoder_1_is_imm));
  Register #(.width(32)) u_Inm (.D(INM), .Q(INM2), .clk(CLK));  // open: en, clr
  Register #(.width(4)) Code (.D(alu_decoder_1_instr_code), .Q(Code_q), .clk(CLK));  // open: en, clr
  Register #(.width(1)) Inmediate (.D(alu_decoder_1_is_imm), .Q(Inmediate_q), .clk(CLK));  // open: en, clr
  Register #(.width(1)) register_1 (.D(idecode_1_br), .Q(Branch), .clk(CLK));  // open: en, clr
  RegisterFile registerfile_1 (
    .rsi1(idecode_1_rs1), .rsi2(idecode_1_rs2), .rdi(MEM_WB_RDI), .rd(multiplexer_3_out), .we(MemWrite_out),
    .CLK(CLK), .rs1(FirstOperand), .rs2(SecondOperand), .ERR(x0_write_err));
  Multiplexer #(.width(32)) multiplexer_4 (.in0(SecondOperand), .in1(INM2), .out(multiplexer_4_out), .sel(Inmediate_q));
  assign bit_extender_1_out = {{3{Code_q[3]}}, Code_q};  // Bit_Extender bit_extender_1
  Comparator #(.width(32)) comparator_1 (
    .a(FirstOperand), .b(SecondOperand), .gt(comparator_1_gt), .eq(beq), .lt(comparator_1_lt));
  or or_5 (bne, comparator_1_gt, comparator_1_lt);
  ALU alu_1 (.A(FirstOperand), .B(multiplexer_4_out), .Op(bit_extender_1_out), .Y(ALUResult));
  Register #(.width(32)) EX_MEM_ALU (.D(ALUResult), .clk(CLK), .Q({EX_MEM_ALU_t, ALUDIR_out}));  // open: en, clr
  Register #(.width(32)) EX_MEM_RD2 (.D(SecondOperand), .clk(CLK), .Q(RD2_out));  // open: en, clr
  Register #(.width(5)) EX_MEM_RD (.D(DestinationRegister), .clk(CLK), .Q(EX_MEM_RD_t));  // open: en, clr
  Register #(.width(1)) EX_MEM_MemRead (.D(MemRead), .clk(CLK), .Q(MemRead_out));  // open: en, clr
  Register #(.width(1)) EX_MEM_MemWrite (.D(MemWrite), .clk(CLK), .Q(MemWrite_out));  // open: en, clr
  Register #(.width(1)) EX_MEM_MemToReg (.D(MemRead), .clk(CLK), .Q(EX_MEM_MemToReg_t));  // open: en, clr
  Register #(.width(1)) EX_MEM_RegWrite (.D(RegWrite), .clk(CLK), .Q(EX_MEM_RegWrite_t));  // open: en, clr
  Register #(.width(32)) MEM_WB_ALU (.D({EX_MEM_ALU_t, ALUDIR_out}), .clk(CLK), .Q(MEM_WB_ALU_q));  // open: en, clr
  Register #(.width(32)) MEM_WB_MEMDATA (.D(cache_data_in), .clk(CLK), .Q(MEM_WB_MEMDATA_q));  // open: en, clr
  Register #(.width(5)) u_MEM_WB_RDI (.D(EX_MEM_RD_t), .clk(CLK), .Q(MEM_WB_RDI));  // open: en, clr
  Register #(.width(1)) MEM_WB_MemtoReg (.D(EX_MEM_MemToReg_t), .clk(CLK), .Q(MEM_WB_MemtoReg_q));  // open: en, clr
  Register #(.width(1)) u_MEM_WB_RegWrite (.D(EX_MEM_RegWrite_t), .clk(CLK), .Q(MEM_WB_RegWrite));  // open: en, clr
  Multiplexer #(.width(32)) multiplexer_5 (
    .in0(MEM_WB_ALU_q), .in1(MEM_WB_MEMDATA_q), .out(WriteBackData), .sel(MEM_WB_MemtoReg_q));

  // Other names for the same wires on the sheet: EX_MEM_ALU_t[14:0] = ALUDIR_out; EX_MEM_MemRead_t = MemRead_out;
  //   EX_MEM_MemWrite_t = MemWrite_out; EX_MEM_RD2_t[31:0] = RD2_out; MemtoReg = MemRead

  // Notes on the sheet:
  //   Decode
  //   Execute
  //   TIPO R
  //   Memory
  //   Writeback 
endmodule

// VHDL entity ALU, as the project stores it:
library IEEE;
use IEEE.STD_LOGIC_1164.ALL;

entity ALU is
  port (
    A   : in  STD_LOGIC_VECTOR(31 downto 0);
    B   : in  STD_LOGIC_VECTOR(31 downto 0);
    Op  : in  STD_LOGIC_VECTOR(6 downto 0);  -- solo Op(2 downto 0) importa
         -- 000 = ADD
         -- 001 = SUB
         -- 010 = AND
         -- 011 = OR
         -- 100 = XOR
         -- 101 = SLL
         -- 110 = SRL
         -- 111 = SRA
    Y   : out STD_LOGIC_VECTOR(31 downto 0)
  );
end entity ALU;

architecture Behavioral of ALU is
begin
  process(A, B, Op)
    variable tmp    : STD_LOGIC_VECTOR(31 downto 0);
    variable carry  : STD_LOGIC;
    variable i      : integer range 0 to 31;
    variable Binv   : STD_LOGIC_VECTOR(31 downto 0);
    variable shamt  : integer range 0 to 31;
  begin
    -- 1) Calcular shift-amount (5 LSB de B)
    shamt := 0;
    for i in 0 to 4 loop
      if B(i) = '1' then
        shamt := shamt + (2**i);
      end if;
    end loop;

    -- 2) Inicializar
    tmp   := (others => '0');
    carry := '0';

    -- 3) Seleccionar operación
    case Op(2 downto 0) is

      when "000" =>  -- ADD
        for i in 0 to 31 loop
          tmp(i)  := A(i) xor B(i) xor carry;
          carry   := (A(i) and B(i)) or (carry and (A(i) xor B(i)));
        end loop;

      when "001" =>  -- SUB = A + not(B) + 1
        for i in 0 to 31 loop
          Binv(i) := not B(i);
        end loop;
        carry := '1';
        for i in 0 to 31 loop
          tmp(i)  := A(i) xor Binv(i) xor carry;
          carry   := (A(i) and Binv(i)) or (carry and (A(i) xor Binv(i)));
        end loop;

      when "010" =>  -- AND
        for i in 0 to 31 loop
          tmp(i) := A(i) and B(i);
        end loop;

      when "011" =>  -- OR
        for i in 0 to 31 loop
          tmp(i) := A(i) or B(i);
        end loop;

      when "100" =>  -- XOR
        for i in 0 to 31 loop
          tmp(i) := A(i) xor B(i);
        end loop;

      when "101" =>  -- SLL (logical left)
        for i in 31 downto 0 loop
          if i - shamt >= 0 then
            tmp(i) := A(i - shamt);
          else
            tmp(i) := '0';
          end if;
        end loop;

      when "110" =>  -- SRL (logical right)
        for i in 0 to 31 loop
          if i + shamt <= 31 then
            tmp(i) := A(i + shamt);
          else
            tmp(i) := '0';
          end if;
        end loop;

      when "111" =>  -- SRA (arithmetic right)
        for i in 0 to 31 loop
          if i + shamt <= 31 then
            tmp(i) := A(i + shamt);
          else
            tmp(i) := A(31);  -- rellena con el bit de signo
          end if;
        end loop;

      when others =>
        tmp := (others => '0');
    end case;

    -- 4) Entregar resultado
    Y <= tmp;
  end process;
end architecture Behavioral;

// VHDL entity msi_protocol, as the project stores it:
library ieee;
use ieee.std_logic_1164.all;
use ieee.numeric_std.all;

entity msi_protocol is
    port (
        clk             : in std_logic;
        reset           : in std_logic;
        cpu0_state      : in std_logic_vector(1 downto 0); -- MSI state for cpu0
        cpu1_state      : in std_logic_vector(1 downto 0); -- MSI state for cpu1
        cpu0_addr       : in std_logic_vector(31 downto 0);   -- Address from cpu0
        cpu1_addr       : in std_logic_vector(31 downto 0);   -- Address from cpu1
        invalidate_cpu0 : out std_logic;                      -- Invalidate signal for cpu0
        invalidate_cpu1 : out std_logic                       -- Invalidate signal for cpu1
    );
end msi_protocol;

architecture Behavioral of msi_protocol is
begin
    process(clk, reset)
    begin
        if reset = '1' then
            invalidate_cpu0 <= '0';
            invalidate_cpu1 <= '0';
        elsif rising_edge(clk) then
            -- If CPU0 modifies a cache line, invalidate the corresponding line in CPU1
            if cpu0_state = "10" then -- Modified state in cpu0
                if cpu1_state = "01" and cpu0_addr = cpu1_addr then -- Shared state in cpu1 for the same address
                    invalidate_cpu1 <= '1'; -- Invalidate the cache line in cpu1
                else
                    invalidate_cpu1 <= '0';
                end if;
            end if;
            
            -- If CPU1 modifies a cache line, invalidate the corresponding line in CPU0
            if cpu1_state = "10" then -- Modified state in cpu1
                if cpu0_state = "01" and cpu1_addr = cpu0_addr then -- Shared state in cpu0 for the same address
                    invalidate_cpu0 <= '1'; -- Invalidate the cache line in cpu0
                else
                    invalidate_cpu0 <= '0';
                end if;
            end if;
        end if;
    end process;
end Behavioral;

// VHDL entity FIFO, as the project stores it:
library ieee;
use ieee.std_logic_1164.all;
use ieee.numeric_std.all;

entity FIFO is
  port(
    clk            : in  std_logic;	-- system clock
    rst            : in  std_logic;	-- synchronous reset

    -- CPU0 interface
    cpu0_read_in   : in  std_logic;					-- CPU0 read request (1 = read)
    cpu0_write_in  : in  std_logic;					-- CPU0 write request (1 = write)
    cpu0_data_in   : in  std_logic_vector(31 downto 0);	-- CPU0 write data
    cpu0_addr      : in  std_logic_vector(2 downto 0);	-- CPU0 address

    -- CPU1 interface
    cpu1_read_in   : in  std_logic;
    cpu1_write_in  : in  std_logic;
    cpu1_data_in   : in  std_logic_vector(31 downto 0);
    cpu1_addr      : in  std_logic_vector(2 downto 0);

    -- Output to SDRAM
    read_out       : out std_logic;	-- 1 = perform read
    write_out      : out std_logic;	-- 1 = perform write

    addr_out       : out std_logic_vector(2 downto 0);	-- address to SDRAM
    data_out       : out std_logic_vector(31 downto 0)	-- data to SDRAM (for writes)
  );
end entity FIFO;

architecture behavior of FIFO is
  -- record and array _types_
  type sdramrequest is record
    requester : std_logic;			-- '0' = CPU0, '1' = CPU1
    operation : std_logic;            	-- 0 = read, 1 = write
    address   : std_logic_vector(2 downto 0);
    data      : std_logic_vector(31 downto 0);
    valid     : std_logic;
  end record sdramrequest;

  -- circular buffer of 1024 requests
  type sdramRequestBuffer is array(0 to 1023) of sdramrequest;

  -- allocate the buffer signal 
  signal request_buf : sdramRequestBuffer := (
    others => (
      requester => '0',
      operation => '0',
      address   => (others => '0'),
      data      => (others => '0'),
      valid     => '0'
    )
  );

  -- track which CPU was last served 
  signal previousRequester : std_logic;  -- 0 is cpu0, 1 is cpu1

begin

  process(clk, rst)
  begin
    if rst = '1' then
    	 -- synchronous reset: clear buffer and outputs
      -- clear buffer on reset
      request_buf <= (others => (
        requester => '0',
        operation => '0',
        address   => (others => '0'),
        data      => (others => '0'),
        valid     => '0'
      ));
      read_out  <= '0';
      write_out <= '0';
      previousRequester <= '0';

    elsif rising_edge(clk) then

    	 -- if there’s a pending SDRAM request at buffer slot 0
      if request_buf(0).valid = '1' then
        -- dequeue slot 0
        read_out  <= not request_buf(0).operation;
        write_out <=     request_buf(0).operation;
        addr_out  <=     request_buf(0).address;
        data_out  <=     request_buf(0).data;

        -- once served, invalidate this slot
        request_buf(0).valid <= '0';

      else
      -- buffer is empty → directly arbitrate between CPU0 & CPU1

        -- 1) No requests from either CPU
        if cpu0_read_in='0' and cpu0_write_in='0'
           and cpu1_read_in='0' and cpu1_write_in='0' then

          read_out  <= '0';
          write_out <= '0';

        -- 2) CPU1 wants to write only
        elsif cpu0_read_in='0' and cpu0_write_in='0'
           and cpu1_read_in='0' and cpu1_write_in='1' then

          read_out          <= '0';
          write_out         <= '1';
          previousRequester <= '1';

        -- 3) CPU1 wants to read only
        elsif cpu0_read_in='0' and cpu0_write_in='0'
           and cpu1_read_in='1' and cpu1_write_in='0' then

          read_out          <= '1';
          write_out         <= '0';
          previousRequester <= '1';

        -- 4) CPU0 wants to write only
        elsif cpu0_read_in='0' and cpu0_write_in='1'
           and cpu1_read_in='0' and cpu1_write_in='0' then

          read_out          <= '0';
          write_out         <= '1';
          previousRequester <= '0';

        -- 5) CPU0 wants to read only
        elsif cpu0_read_in='1' and cpu0_write_in='0'
           and cpu1_read_in='0' and cpu1_write_in='0' then

          read_out          <= '1';
          write_out         <= '0';
          previousRequester <= '0';

        -- 6) Both CPUs want to read → enqueue CPU1’s read
        elsif cpu0_read_in='1' and cpu0_write_in='0'
           and cpu1_read_in='1' and cpu1_write_in='0' then

          read_out          <= '1';
          write_out         <= '0';
          previousRequester <= '0';

          request_buf(0).requester <= '1';        -- from CPU1
          request_buf(0).operation <= '0';        -- read
          request_buf(0).address   <= cpu1_addr;
          request_buf(0).valid     <= '1';

        -- 7) CPU0 read & CPU1 write → enqueue CPU1’s write
        elsif cpu0_read_in='1' and cpu0_write_in='0'
           and cpu1_read_in='0' and cpu1_write_in='1' then

          read_out          <= '1';
          write_out         <= '0';
          previousRequester <= '0';

          request_buf(0).requester <= '1';
          request_buf(0).operation <= '1';        -- write
          request_buf(0).address   <= cpu1_addr;
          request_buf(0).data      <= cpu1_data_in;
          request_buf(0).valid     <= '1';

        -- 8) CPU0 write & CPU1 read → enqueue CPU1’s read
        elsif cpu0_read_in='0' and cpu0_write_in='1'
           and cpu1_read_in='1' and cpu1_write_in='0' then

          read_out          <= '0';
          write_out         <= '1';
          previousRequester <= '0';

          request_buf(0).requester <= '1';
          request_buf(0).operation <= '0';        -- read
          request_buf(0).address   <= cpu1_addr;
          request_buf(0).valid     <= '1';

        -- 9) Both CPUs want to write → enqueue CPU1’s write
        elsif cpu0_read_in='0' and cpu0_write_in='1'
           and cpu1_read_in='0' and cpu1_write_in='1' then

          read_out          <= '0';
          write_out         <= '1';
          previousRequester <= '0';

          request_buf(0).requester <= '1';
          request_buf(0).operation <= '1';
          request_buf(0).address   <= cpu1_addr;
          request_buf(0).data      <= cpu1_data_in;
          request_buf(0).valid     <= '1';

        end if;
      end if;

    end if;
  end process;

end architecture behavior;

// VHDL entity TransactionsBetweenCPU, as the project stores it:
library ieee;
use ieee.std_logic_1164.all;

LIBRARY work;

entity TransactionsBetweenCPU is
  port(
    clk             : in  std_logic;                    -- system clock
    rst             : in  std_logic;                    -- synchronous reset
    cpu0_prio       : in  std_logic;                    -- arbitration priority for CPU0
    cpu1_prio       : in  std_logic;                    -- arbitration priority for CPU1
    cpu0_wantedAddr : in  std_logic_vector(2 downto 0); -- CPU0 target address
    cpu1_wantedAddr : in  std_logic_vector(2 downto 0)  -- CPU1 target address
  );
end entity TransactionsBetweenCPU;

architecture bdf_type of TransactionsBetweenCPU is

  -- CPU core component
  component CPU_Core is
    port(
      clk                          : in  std_logic;
      reset                        : in  std_logic;
      priority                     : in  std_logic;
      cpu_wr_req_in                : in  std_logic;
      cpu_rd_req_in                : in  std_logic;
      cache_to_cache_resp_in_ready: in  std_logic;
      cache_to_cache_resp_in       : in  std_logic;
      cache_to_cache_req_in        : in  std_logic;
      cache_to_cache_req_address_in: in  std_logic_vector(2 downto 0);
      cache_to_cache_resp_in_data  : in  std_logic_vector(31 downto 0);
      cpu_req_addr_in              : in  std_logic_vector(2 downto 0);
      Sdram_data_in                : in  std_logic_vector(31 downto 0);
      wantedAddress                : in  std_logic_vector(2 downto 0);
      read_en                      : out std_logic;
      write_en                     : out std_logic;
      cpu_wr_req_out               : out std_logic;
      cpu_rd_req_out               : out std_logic;
      cache_to_cache_resp_out_ready: out std_logic;
      cache_to_cache_resp_out      : out std_logic;
      cache_to_cache_req_out       : out std_logic;
      cache_to_cache_req_address_out: out std_logic_vector(2 downto 0);
      cache_to_cache_resp_out_data : out std_logic_vector(31 downto 0);
      cpu_req_addr_out             : out std_logic_vector(2 downto 0);
      Sdram_addr                   : out std_logic_vector(2 downto 0);
      Sdram_data_out               : out std_logic_vector(31 downto 0)
    );
  end component;


  -- SDRAM component
  component sdram is
    port(
      clk        : in  std_logic;
      reset      : in  std_logic;
      operation1 : in  std_logic;                     -- 0=read, 1=write on port1
      operation2 : in  std_logic;                     -- 0=read, 1=write on port2
      ready1     : in  std_logic;                     -- handshake from CPU1
      ready2     : in  std_logic;                     -- handshake from CPU2
      addr1      : in  std_logic_vector(2 downto 0);
      addr2      : in  std_logic_vector(2 downto 0);
      data_in1   : in  std_logic_vector(31 downto 0); -- CPU→SDRAM data
      data_in2   : in  std_logic_vector(31 downto 0);
      data_out1  : out std_logic_vector(31 downto 0); -- SDRAM→CPU data
      data_out2  : out std_logic_vector(31 downto 0)
    );
  end component;

  -- Internal signals for cache‐to‐cache traffic
  signal cpu0_cache_to_cache_req              : std_logic;
  signal cpu0_cache_to_cache_req_addr         : std_logic_vector(2 downto 0);
  signal cpu0_cache_to_cache_resp_data        : std_logic_vector(31 downto 0);
  signal cpu0_cache_to_cache_response         : std_logic;
  signal cpu0_cache_to_cache_response_out_ready : std_logic;
  signal cpu0_wr_req_out                      : std_logic;
  signal cpu0_rd_req_out                      : std_logic;
  signal cpu0_req_addr_out                    : std_logic_vector(2 downto 0);

  signal cpu1_cache_to_cache_req              : std_logic;
  signal cpu1_cache_to_cache_req_addr         : std_logic_vector(2 downto 0);
  signal cpu1_cache_to_cache_resp_data        : std_logic_vector(31 downto 0);
  signal cpu1_cache_to_cache_response         : std_logic;
  signal cpu1_cache_to_cache_response_out_ready : std_logic;
  signal cpu1_wr_req_out                      : std_logic;
  signal cpu1_rd_req_out                      : std_logic;
  signal cpu1_req_addr_out                    : std_logic_vector(2 downto 0);

  -- Read/Write enable flags from each CPU
  signal r_en1  : std_logic;
  signal wr_en1 : std_logic;
  signal r_en2  : std_logic;
  signal wr_en2 : std_logic;

  -- Combined “ready” lines into SDRAM
  signal ready1_sig : std_logic;
  signal ready2_sig : std_logic;

  -- Address buses from CPU → SDRAM
  signal sdram_addr1 : std_logic_vector(2 downto 0);
  signal sdram_addr2 : std_logic_vector(2 downto 0);

  -- Data buses CPU → SDRAM
  signal sdram_data_out1 : std_logic_vector(31 downto 0);
  signal sdram_data_out2 : std_logic_vector(31 downto 0);

  -- Data buses SDRAM → CPU
  signal sdram_data_in1  : std_logic_vector(31 downto 0);
  signal sdram_data_in2  : std_logic_vector(31 downto 0);

begin

  -- Generate “ready” handshake for SDRAM ports
  ready1_sig <= wr_en1 or r_en1;
  ready2_sig <= wr_en2 or r_en2;

  -- CPU Core #0 instance
  core0: CPU_Core
    port map(
      clk                            => clk,
      reset                          => rst,
      priority                       => cpu0_prio,
      cpu_wr_req_in                  => cpu1_wr_req_out,
      cpu_rd_req_in                  => cpu1_rd_req_out,
      cache_to_cache_resp_in_ready   => cpu1_cache_to_cache_response_out_ready,
      cache_to_cache_resp_in         => cpu1_cache_to_cache_response,
      cache_to_cache_req_in          => cpu1_cache_to_cache_req,
      cache_to_cache_req_address_in  => cpu1_cache_to_cache_req_addr,
      cache_to_cache_resp_in_data    => cpu1_cache_to_cache_resp_data,
      cpu_req_addr_in                => cpu1_req_addr_out,
      Sdram_data_in                  => sdram_data_in1,     -- from SDRAM
      wantedAddress                  => cpu0_wantedAddr,
      read_en                        => r_en1,
      write_en                       => wr_en1,
      cpu_wr_req_out                 => cpu0_wr_req_out,
      cpu_rd_req_out                 => cpu0_rd_req_out,
      cache_to_cache_resp_out_ready  => cpu0_cache_to_cache_response_out_ready,
      cache_to_cache_resp_out        => cpu0_cache_to_cache_response,
      cache_to_cache_req_out         => cpu0_cache_to_cache_req,
      cache_to_cache_req_address_out => cpu0_cache_to_cache_req_addr,
      cache_to_cache_resp_out_data   => cpu0_cache_to_cache_resp_data,
      cpu_req_addr_out               => cpu0_req_addr_out,
      Sdram_addr                     => sdram_addr1,         -- to SDRAM
      Sdram_data_out                 => sdram_data_out1      -- to SDRAM
    );

  -- CPU Core #1 instance
  core1: CPU_Core
    port map(
      clk                            => clk,
      reset                          => rst,
      priority                       => cpu1_prio,
      cpu_wr_req_in                  => cpu0_wr_req_out,
      cpu_rd_req_in                  => cpu0_rd_req_out,
      cache_to_cache_resp_in_ready   => cpu0_cache_to_cache_response_out_ready,
      cache_to_cache_resp_in         => cpu0_cache_to_cache_response,
      cache_to_cache_req_in          => cpu0_cache_to_cache_req,
      cache_to_cache_req_address_in  => cpu0_cache_to_cache_req_addr,
      cache_to_cache_resp_in_data    => cpu0_cache_to_cache_resp_data,
      cpu_req_addr_in                => cpu0_req_addr_out,
      Sdram_data_in                  => sdram_data_in2,     -- from SDRAM
      wantedAddress                  => cpu1_wantedAddr,
      read_en                        => r_en2,
      write_en                       => wr_en2,
      cpu_wr_req_out                 => cpu1_wr_req_out,
      cpu_rd_req_out                 => cpu1_rd_req_out,
      cache_to_cache_resp_out_ready  => cpu1_cache_to_cache_response_out_ready,
      cache_to_cache_resp_out        => cpu1_cache_to_cache_response,
      cache_to_cache_req_out         => cpu1_cache_to_cache_req,
      cache_to_cache_req_address_out => cpu1_cache_to_cache_req_addr,
      cache_to_cache_resp_out_data   => cpu1_cache_to_cache_resp_data,
      cpu_req_addr_out               => cpu1_req_addr_out,
      Sdram_addr                     => sdram_addr2,         -- to SDRAM
      Sdram_data_out                 => sdram_data_out2      -- to SDRAM
    );

  -- SDRAM instance (port‐interleaved two‐port memory)
  sdram0: sdram
    port map(
      clk        => clk,
      reset      => rst,
      operation1 => wr_en1,           -- write when wr_en1='1'
      operation2 => wr_en2,           -- write when wr_en2='1'
      ready1     => ready1_sig,
      ready2     => ready2_sig,
      addr1      => sdram_addr1,
      addr2      => sdram_addr2,
      data_in1   => sdram_data_out1,  -- CPU0 → SDRAM
      data_in2   => sdram_data_out2,  -- CPU1 → SDRAM
      data_out1  => sdram_data_in1,   -- SDRAM → CPU0
      data_out2  => sdram_data_in2    -- SDRAM → CPU1
    );

end architecture bdf_type;

// VHDL entity alu_decoder, as the project stores it:
library ieee;
use ieee.std_logic_1164.all;
use ieee.numeric_std.all;

entity alu_decoder is
  port (
    opcode  : in  std_logic_vector(6 downto 0);
    funct3  : in  std_logic_vector(2 downto 0);
    funct7  : in  std_logic_vector(6 downto 0);
    
    instr_code : out std_logic_vector(3 downto 0);
    is_imm     : out std_logic
  );
end entity alu_decoder;

architecture rtl of alu_decoder is

  -- Códigos internos para cada operación
  subtype icode_t is std_logic_vector(3 downto 0);
  constant I_ADD   : icode_t := "0000";
  constant I_SUB   : icode_t := "0001";
  constant I_ADDI  : icode_t := "0010";
  constant I_AND   : icode_t := "0011";
  constant I_OR    : icode_t := "0100";
  constant I_XOR   : icode_t := "0101";
  constant I_ANDI  : icode_t := "0110";
  constant I_ORI   : icode_t := "0111";
  constant I_XORI  : icode_t := "1000";
  constant I_SLL   : icode_t := "1001";
  constant I_SRL   : icode_t := "1010";
  constant I_SRA   : icode_t := "1011";
  constant I_NONE  : icode_t := "1111";  -- ningún match

begin

  process(opcode, funct3, funct7)
  begin
    -- Valor por defecto
    instr_code <= I_NONE;
    is_imm     <= '0';

    case opcode is

      -- R-TYPE: opcode = "0110011"
      when "0110011" =>
        is_imm <= '0';
        case funct3 is
          when "000" =>
            if funct7 = "0000000" then
                instr_code <= I_ADD;
            elsif funct7 = "0100000" then
                instr_code <= I_SUB;
            end if;
          when "111" =>
            instr_code <= I_AND;
          when "110" =>
            instr_code <= I_OR;
          when "100" =>
            instr_code <= I_XOR;
          when "001" =>
            instr_code <= I_SLL;
          when "101" =>
            if funct7 = "0000000" then
              instr_code <= I_SRL;
            elsif funct7 = "0100000" then
              instr_code <= I_SRA;
            end if;
          when others =>
            instr_code <= I_NONE;
        end case;

      -- I-TYPE aritméticas: opcode = "0010011"
      when "0010011" =>
        is_imm <= '1';
        case funct3 is
          when "000" =>
            instr_code <= I_ADDI;
          when "111" =>
            instr_code <= I_ANDI;
          when "110" =>
            instr_code <= I_ORI;
          when "100" =>
            instr_code <= I_XORI;
          -- (si deseases SLLI, SRLI, SRAI, habría que chequear funct7 también)
          when others =>
            instr_code <= I_NONE;
        end case;

      when others =>
        instr_code <= I_NONE;
        is_imm     <= '0';
    end case;
  end process;

end architecture rtl;

// VHDL entity CPU_Core, as the project stores it:
library ieee;
use ieee.std_logic_1164.all;
use ieee.numeric_std.all;

entity CPU_Core is
    port (
        clk            : in std_logic;
        reset          : in std_logic;
        priority       : in std_logic;
        
        -- CPU interface
        wantedAddress  : in std_logic_vector(2 downto 0);
        
        -- SDRAM interface
        read_en        : out std_logic;
        write_en       : out std_logic;
        Sdram_addr     : out std_logic_vector(2 downto 0);
        Sdram_data_in  : in std_logic_vector(31 downto 0);
        Sdram_data_out : out std_logic_vector(31 downto 0);
        
        -- MSI protocol - outgoing requests
        cpu_wr_req_out : out std_logic;
        cpu_rd_req_out : out std_logic;
        cpu_req_addr_out : out std_logic_vector(2 downto 0);
        
        -- MSI protocol - incoming requests (snooping)
        cpu_wr_req_in  : in std_logic;
        cpu_rd_req_in  : in std_logic;
        cpu_req_addr_in : in std_logic_vector(2 downto 0);
        
        -- Cache-to-cache communication - outgoing
        cache_to_cache_req_out : out std_logic;
        cache_to_cache_req_address_out : out std_logic_vector(2 downto 0);
        cache_to_cache_resp_out : out std_logic;
        cache_to_cache_resp_out_ready : out std_logic;
        cache_to_cache_resp_out_data : out std_logic_vector(31 downto 0);
        
        -- Cache-to-cache communication - incoming
        cache_to_cache_req_in : in std_logic;
        cache_to_cache_req_address_in : in std_logic_vector(2 downto 0);
        cache_to_cache_resp_in : in std_logic;
        cache_to_cache_resp_in_ready : in std_logic;
        cache_to_cache_resp_in_data : in std_logic_vector(31 downto 0)
    );
end CPU_Core;

architecture Behavioral of CPU_Core is
    -- Cache configuration
    constant CACHE_SIZE : integer := 4;
    
    -- MSI states
    type msi_state_type is (MSI_INVALID, MSI_SHARED, MSI_MODIFIED);
    
    -- Cache line structure
    type cache_line_type is record
        msi_state : msi_state_type;
        address   : std_logic_vector(2 downto 0);
        data      : std_logic_vector(31 downto 0);
        valid     : std_logic;
    end record;
    
    type cache_array_type is array (0 to CACHE_SIZE-1) of cache_line_type;
    
    -- CPU operation states
    type cpu_state_type is (CPU_IDLE, CPU_READ, CPU_WRITE, CPU_WAIT_CACHE, CPU_WAIT_SDRAM);
    
    -- Cache operation states  
    type cache_state_type is (CACHE_CHECK, CACHE_HIT, CACHE_MISS, CACHE_COHERENCE, CACHE_SDRAM_ACCESS);
    
    -- Signals
    signal cache_mem : cache_array_type;
    signal cpu_state : cpu_state_type;
    signal cache_state : cache_state_type;
    signal current_address : std_logic_vector(2 downto 0);
    signal current_data : std_logic_vector(31 downto 0);
    signal cache_hit_flag : std_logic;
    signal cache_hit_index : integer range 0 to CACHE_SIZE-1;
    signal evict_index : integer range 0 to CACHE_SIZE-1;
    signal operation_type : std_logic; -- 0 = read, 1 = write
    signal cycle_counter : integer range 0 to 15;
    
    -- Helper functions
    function find_cache_line(addr : std_logic_vector(2 downto 0); cache_mem : cache_array_type) 
        return integer is
    begin
        for i in 0 to CACHE_SIZE-1 loop
            if cache_mem(i).valid = '1' and cache_mem(i).address = addr then
                return i;
            end if;
        end loop;
        return -1; -- Not found
    end function;
    
    function find_empty_line(cache_mem : cache_array_type) return integer is
    begin
        for i in 0 to CACHE_SIZE-1 loop
            if cache_mem(i).valid = '0' then
                return i;
            end if;
        end loop;
        return -1; -- Cache full
    end function;

begin

    -- Main cache controller process
    main_process: process(clk, reset)
        variable hit_index : integer;
        variable empty_index : integer;
    begin
        if reset = '1' then
            -- Initialize cache
            for i in 0 to CACHE_SIZE-1 loop
                cache_mem(i).msi_state <= MSI_INVALID;
                cache_mem(i).address <= (others => '0');
                cache_mem(i).data <= (others => '0');
                cache_mem(i).valid <= '0';
            end loop;
            
            -- Reset state machines
            cpu_state <= CPU_IDLE;
            cache_state <= CACHE_CHECK;
            
            -- Reset outputs
            read_en <= '0';
            write_en <= '0';
            cpu_wr_req_out <= '0';
            cpu_rd_req_out <= '0';
            cache_to_cache_req_out <= '0';
            cache_to_cache_resp_out <= '0';
            cache_to_cache_resp_out_ready <= '0';
            
            evict_index <= 0;
            cycle_counter <= 0;
            
        elsif rising_edge(clk) then
            -- Default signal values
            read_en <= '0';
            write_en <= '0';
            cache_to_cache_req_out <= '0';
            cache_to_cache_resp_out <= '0';
            cache_to_cache_resp_out_ready <= '0';
            
            -- Handle snooping requests from other caches
            if cache_to_cache_req_in = '1' then
                hit_index := find_cache_line(cache_to_cache_req_address_in, cache_mem);
                if hit_index >= 0 then
                    if cache_mem(hit_index).msi_state = MSI_MODIFIED then
                        -- Provide data and transition to shared
                        cache_to_cache_resp_out <= '1';
                        cache_to_cache_resp_out_data <= cache_mem(hit_index).data;
                        cache_mem(hit_index).msi_state <= MSI_SHARED;
                    elsif cache_mem(hit_index).msi_state = MSI_SHARED then
                        -- Provide data, stay shared
                        cache_to_cache_resp_out <= '1';
                        cache_to_cache_resp_out_data <= cache_mem(hit_index).data;
                    end if;
                else
                    cache_to_cache_resp_out <= '0';
                end if;
                cache_to_cache_resp_out_ready <= '1';
            end if;
            
            -- Handle invalidation requests
            if cpu_wr_req_in = '1' then
                hit_index := find_cache_line(cpu_req_addr_in, cache_mem);
                if hit_index >= 0 then
                    cache_mem(hit_index).msi_state <= MSI_INVALID;
                    cache_mem(hit_index).valid <= '0';
                end if;
            end if;
            
            -- Main CPU state machine
            case cpu_state is
                when CPU_IDLE =>
                    cycle_counter <= cycle_counter + 1;
                    
                    -- Simple test pattern
                    if cycle_counter = 5 then
                        cpu_state <= CPU_WRITE;
                        current_address <= wantedAddress;
                        current_data <= x"DEADBEEF";
                        operation_type <= '1'; -- write
                        cpu_wr_req_out <= '1';
                        cpu_req_addr_out <= wantedAddress;
                        cache_state <= CACHE_CHECK;
                        cycle_counter <= 0;
                    elsif cycle_counter = 10 then
                        cpu_state <= CPU_READ;
                        current_address <= wantedAddress;
                        operation_type <= '0'; -- read
                        cpu_rd_req_out <= '1';
                        cpu_req_addr_out <= wantedAddress;
                        cache_state <= CACHE_CHECK;
                        cycle_counter <= 0;
                    end if;
                
                when CPU_READ | CPU_WRITE =>
                    case cache_state is
                        when CACHE_CHECK =>
                            hit_index := find_cache_line(current_address, cache_mem);
                            if hit_index >= 0 and cache_mem(hit_index).msi_state /= MSI_INVALID then
                                -- Cache hit
                                cache_hit_flag <= '1';
                                cache_hit_index <= hit_index;
                                cache_state <= CACHE_HIT;
                            else
                                -- Cache miss
                                cache_hit_flag <= '0';
                                cache_state <= CACHE_MISS;
                            end if;
                        
                        when CACHE_HIT =>
                            if operation_type = '0' then
                                -- Read hit - return data
                                cpu_state <= CPU_IDLE;
                                cpu_rd_req_out <= '0';
                                cache_state <= CACHE_CHECK;
                            else
                                -- Write hit - update data and set modified
                                cache_mem(cache_hit_index).data <= current_data;
                                cache_mem(cache_hit_index).msi_state <= MSI_MODIFIED;
                                cpu_state <= CPU_IDLE;
                                cpu_wr_req_out <= '0';
                                cache_state <= CACHE_CHECK;
                            end if;
                        
                        when CACHE_MISS =>
                            -- Try cache-to-cache transfer first
                            cache_to_cache_req_out <= '1';
                            cache_to_cache_req_address_out <= current_address;
                            cache_state <= CACHE_COHERENCE;
                        
                        when CACHE_COHERENCE =>
                            if cache_to_cache_resp_in_ready = '1' then
                                if cache_to_cache_resp_in = '1' then
                                    -- Cache-to-cache hit
                                    empty_index := find_empty_line(cache_mem);
                                    if empty_index >= 0 then
                                        -- Use empty line
                                        cache_mem(empty_index).valid <= '1';
                                        cache_mem(empty_index).address <= current_address;
                                        cache_mem(empty_index).data <= cache_to_cache_resp_in_data;
                                        if operation_type = '0' then
                                            cache_mem(empty_index).msi_state <= MSI_SHARED;
                                        else
                                            cache_mem(empty_index).msi_state <= MSI_MODIFIED;
                                            cache_mem(empty_index).data <= current_data;
                                        end if;
                                    else
                                        -- Evict using round-robin
                                        if cache_mem(evict_index).msi_state = MSI_MODIFIED then
                                            -- Write back to SDRAM
                                            write_en <= '1';
                                            Sdram_addr <= cache_mem(evict_index).address;
                                            Sdram_data_out <= cache_mem(evict_index).data;
                                        end if;
                                        cache_mem(evict_index).valid <= '1';
                                        cache_mem(evict_index).address <= current_address;
                                        cache_mem(evict_index).data <= cache_to_cache_resp_in_data;
                                        if operation_type = '0' then
                                            cache_mem(evict_index).msi_state <= MSI_SHARED;
                                        else
                                            cache_mem(evict_index).msi_state <= MSI_MODIFIED;
                                            cache_mem(evict_index).data <= current_data;
                                        end if;
                                        evict_index <= (evict_index + 1) mod CACHE_SIZE;
                                    end if;
                                    cpu_state <= CPU_IDLE;
                                    if operation_type = '0' then
                                        cpu_rd_req_out <= '0';
                                    else
                                        cpu_wr_req_out <= '0';
                                    end if;
                                    cache_state <= CACHE_CHECK;
                                else
                                    -- Cache-to-cache miss, go to SDRAM
                                    cache_state <= CACHE_SDRAM_ACCESS;
                                end if;
                            end if;
                        
                        when CACHE_SDRAM_ACCESS =>
                            if operation_type = '0' then
                                read_en <= '1';
                            else
                                write_en <= '1';
                                Sdram_data_out <= current_data;
                            end if;
                            Sdram_addr <= current_address;
                            
                            -- Allocate cache line
                            empty_index := find_empty_line(cache_mem);
                            if empty_index >= 0 then
                                cache_mem(empty_index).valid <= '1';
                                cache_mem(empty_index).address <= current_address;
                                if operation_type = '0' then
                                    cache_mem(empty_index).data <= Sdram_data_in;
                                    cache_mem(empty_index).msi_state <= MSI_SHARED;
                                else
                                    cache_mem(empty_index).data <= current_data;
                                    cache_mem(empty_index).msi_state <= MSI_MODIFIED;
                                end if;
                            else
                                -- Evict using round-robin
                                if cache_mem(evict_index).msi_state = MSI_MODIFIED then
                                    write_en <= '1';
                                    Sdram_addr <= cache_mem(evict_index).address;
                                    Sdram_data_out <= cache_mem(evict_index).data;
                                end if;
                                cache_mem(evict_index).valid <= '1';
                                cache_mem(evict_index).address <= current_address;
                                if operation_type = '0' then
                                    cache_mem(evict_index).data <= Sdram_data_in;
                                    cache_mem(evict_index).msi_state <= MSI_SHARED;
                                else
                                    cache_mem(evict_index).data <= current_data;
                                    cache_mem(evict_index).msi_state <= MSI_MODIFIED;
                                end if;
                                evict_index <= (evict_index + 1) mod CACHE_SIZE;
                            end if;
                            
                            cpu_state <= CPU_IDLE;
                            if operation_type = '0' then
                                cpu_rd_req_out <= '0';
                            else
                                cpu_wr_req_out <= '0';
                            end if;
                            cache_state <= CACHE_CHECK;
                    end case;
                
                when others =>
                    cpu_state <= CPU_IDLE;
            end case;
        end if;
    end process;

end Behavioral;

// VHDL entity sdram, as the project stores it:
library ieee;
use ieee.std_logic_1164.all;
use ieee.numeric_std.all;

entity sdram is
    port(
        clk        : in  std_logic;
        reset      : in  std_logic;
        operation1 : in  std_logic;                     -- 0=read, 1=write on port1
        operation2 : in  std_logic;                     -- 0=read, 1=write on port2
        ready1     : in  std_logic;                     -- handshake from CPU1
        ready2     : in  std_logic;                     -- handshake from CPU2
        addr1      : in  std_logic_vector(2 downto 0);
        addr2      : in  std_logic_vector(2 downto 0);
        data_in1   : in  std_logic_vector(31 downto 0); -- CPU→SDRAM data
        data_in2   : in  std_logic_vector(31 downto 0);
        data_out1  : out std_logic_vector(31 downto 0); -- SDRAM→CPU data
        data_out2  : out std_logic_vector(31 downto 0)
    );
end sdram;

architecture Behavioral of sdram is
    type memory_array is array (0 to 7) of std_logic_vector(31 downto 0);
    signal memory : memory_array;
begin
    process(clk, reset)
    begin
        if reset = '1' then
            -- Initialize memory with test pattern
            memory(0) <= x"00000000";
            memory(1) <= x"11111111";
            memory(2) <= x"22222222";
            memory(3) <= x"33333333";
            memory(4) <= x"44444444";
            memory(5) <= x"55555555";
            memory(6) <= x"66666666";
            memory(7) <= x"77777777";
        elsif rising_edge(clk) then
            -- Port 1 operations
            if ready1 = '1' then
                if operation1 = '1' then
                    -- Write
                    memory(to_integer(unsigned(addr1))) <= data_in1;
                else
                    -- Read
                    data_out1 <= memory(to_integer(unsigned(addr1)));
                end if;
            end if;
            
            -- Port 2 operations
            if ready2 = '1' then
                if operation2 = '1' then
                    -- Write
                    memory(to_integer(unsigned(addr2))) <= data_in2;
                else
                    -- Read
                    data_out2 <= memory(to_integer(unsigned(addr2)));
                end if;
            end if;
        end if;
    end process;
end Behavioral;

// VHDL entity ebc, as the project stores it:
-- =========================================
-- ebc.vhd  (sin genéricos, VHDL-93)
-- =========================================
library ieee;
use ieee.std_logic_1164.all;
use ieee.numeric_std.all;

entity ebc is
  port (
    clk        : in  std_logic;                      -- reloj
    reset_n    : in  std_logic;                      -- reset síncrono activo-bajo
    key_valid  : in  std_logic;                      -- pulso: key_data es válido
    enable	: in  std_logic;
    key_data   : in  std_logic_vector(6 downto 0);   -- byte de teclado
    flag_out   : out std_logic                       -- bandera de 1 ciclo
  );
end entity ebc;

architecture rtl of ebc is
  -- Tecla que dispara la bandera (0x5A = Enter, set-2)
  constant KEY_CODE_V : std_logic_vector(7 downto 0) := x"5A";

  signal flag_r : std_logic := '0';
begin
  flag_out <= flag_r;

  process (clk)
  begin
    if rising_edge(clk) and enable = '1' then
      if reset_n = '0' then
        flag_r <= '0';

      elsif key_valid = '1' and key_data = KEY_CODE_V then
        flag_r <= '1';            -- levanta la bandera exactamente un ciclo
      else
        flag_r <= '0';
      end if;
    end if;
  end process;
end architecture rtl;
